// Logisim project Projeto Processador 32 Bits Completo.circ as structural Verilog
module mux_2 (
  input  A,
  input  B,
  input  C0,
  output out_4
);

  wire and_1_out, and_2_out;

  and and_1 (and_1_out, A, ~C0);  // AND_Gate
  and and_2 (and_2_out, B, C0);
  or or_1 (out_4, and_1_out, and_2_out);
endmodule

module MUX_2____P_barrel_shift (
  input  A,
  input  B,
  input  C0,
  output out_4
);

  wire and_1_out, and_2_out;

  and and_1 (and_1_out, A, ~C0);  // AND_Gate
  and and_2 (and_2_out, B, C0);
  or or_1 (out_4, and_1_out, and_2_out);
endmodule

// MUX 4
module Mux_4 (
  input  SOMA,
  input  SUB,
  input  AND,
  input  OR,
  input  C1,
  input  C2,
  output out_7
);

  wire and_1_out, and_2_out, and_3_out, and_4_out;

  and and_1 (and_1_out, SOMA, ~C1, ~C2);  // AND_Gate
  and and_2 (and_2_out, SUB, ~C1, C2);  // AND_Gate
  and and_3 (and_3_out, AND, C1, ~C2);  // AND_Gate
  and and_4 (and_4_out, OR, C1, C2);
  or or_1 (out_7, and_1_out, and_2_out, and_3_out, and_4_out);
endmodule

// MUX 8
module Mux_8 (
  input  A,
  input  B,
  input  C,
  input  D,
  input  E,
  input  F,
  input  G,
  input  H,
  input  in_9,
  input  in_10,
  input  in_11,
  output out_12
);

  wire mux_4_1_out_7, mux_4_2_out_7;

  Mux_4 mux_4_1 (.SOMA(A), .SUB(B), .AND(C), .OR(D), .out_7(mux_4_1_out_7), .C1(in_9), .C2(in_10));
  Mux_4 mux_4_2 (.SOMA(E), .SUB(F), .AND(G), .OR(H), .out_7(mux_4_2_out_7), .C1(in_9), .C2(in_10));
  Mux_4 mux_4_3 (.SOMA(mux_4_1_out_7), .OR(mux_4_2_out_7), .out_7(out_12), .C1(in_11), .C2(in_11));  // open: SUB, AND
endmodule

// Mux 16
module Mux_16 (
  input  in_1,
  input  in_2,
  input  in_3,
  input  in_4,
  input  in_5,
  input  in_6,
  input  in_7,
  input  in_8,
  input  in_9,
  input  in_10,
  input  in_11,
  input  in_12,
  input  in_13,
  input  in_14,
  input  in_15,
  input  in_16,
  input  C1,
  input  C2,
  input  C3,
  input  C4,
  output out_21
);

  wire mux_8_1_out_12, mux_8_2_out_12;

  Mux_8 mux_8_1 (
    .A(in_1), .B(in_2), .C(in_3), .D(in_4), .E(in_5), .F(in_6), .G(in_7), .H(in_8), .in_9(C1), .in_10(C2),
    .in_11(C3), .out_12(mux_8_1_out_12));
  Mux_8 mux_8_2 (
    .A(in_9), .B(in_10), .C(in_11), .D(in_12), .E(in_13), .F(in_14), .G(in_15), .H(in_16), .in_9(C1),
    .in_10(C2), .in_11(C3), .out_12(mux_8_2_out_12));
  Mux_8 mux_8_3 (
    .A(mux_8_1_out_12), .H(mux_8_2_out_12), .in_9(C4), .in_10(C4), .in_11(C4), .out_12(out_21));  // open: B, C, D, E, F, G
endmodule

// MUX 32
module Mux_32 (
  input  _00000_00001,
  input  _01000_01001,
  input  _10000_10001,
  input  _11000_11001,
  input  _00100_00101,
  input  _01100_01101,
  input  _10100_10101,
  input  _11100,
  input  _00011_00010,
  input  _01010_01011,
  input  _10010_10011,
  input  in_12,
  input  _00110_00111,
  input  _01110,
  input  _10110_10111,
  input  in_16,
  input  _00000_00001_2,
  input  _01000_01001_2,
  input  _10000_10001_2,
  input  _11000_11001_2,
  input  _00100_00101_2,
  input  _01100_01101_2,
  input  _10100,
  input  _11100_2,
  input  _00010,
  input  _01010_01011_2,
  input  _10010_10011_2,
  input  in_28,
  input  _00110_00111_2,
  input  _01110_2,
  input  _10110_10111_2,
  input  in_32,
  input  C1,
  input  C2,
  input  C3,
  input  C4,
  input  C5,
  output out_38
);

  wire mux_16_1_out_21, mux_16_2_out_21;

  Mux_16 mux_16_1 (
    .in_1(_00000_00001), .in_2(_01000_01001), .in_3(_10000_10001), .in_4(_11000_11001), .in_5(_00100_00101),
    .in_6(_01100_01101), .in_7(_10100_10101), .in_8(_11100), .in_9(_00011_00010), .in_10(_01010_01011),
    .in_11(_10010_10011), .in_12(in_12), .in_13(_00110_00111), .in_14(_01110), .in_15(_10110_10111),
    .in_16(in_16), .out_21(mux_16_1_out_21), .C1(C1), .C2(C2), .C3(C3), .C4(C4));
  Mux_16 mux_16_2 (
    .in_1(_00000_00001_2), .in_2(_01000_01001_2), .in_3(_10000_10001_2), .in_4(_11000_11001_2),
    .in_5(_00100_00101_2), .in_6(_01100_01101_2), .in_7(_10100), .in_8(_11100_2), .in_9(_00010),
    .in_10(_01010_01011_2), .in_11(_10010_10011_2), .in_12(in_28), .in_13(_00110_00111_2), .in_14(_01110_2),
    .in_15(_10110_10111_2), .in_16(in_32), .out_21(mux_16_2_out_21), .C1(C1), .C2(C2), .C3(C3), .C4(C4));
  Mux_16 mux_16_3 (
    .in_1(mux_16_1_out_21), .in_16(mux_16_2_out_21), .out_21(out_38), .C1(C5), .C2(C5), .C3(C5), .C4(C5));  // open: in_2, in_3, in_4, in_5, in_6, in_7, in_8, in_9, in_10, in_11, in_12, in_13, in_14, in_15

  // Notes on the sheet:
  //   24
endmodule

// ULA
module ULA_32 (
  input  Cin,
  input  A,
  input  B,
  input  C1,
  input  C2,
  input  C3,
  input  C4,
  input  C5,
  output S,
  output COUT
);

  wire and_1_out, and_2_out, and_3_out, demux_4_modif_1_out_3, demux_4_modif_1_out_4, demux_4_modif_1_out_5,
       demux_4_modif_1_out_6, mux_2_1_out_4, mux_2_2_out_4, nand_1_out, not_1_out, or_1_out, or_2_out,
       somador_1_sum, xor_1_out;

  mux_2 mux_2_1 (.A(Cin), .B(1'b1), .out_4(mux_2_1_out_4), .C0(or_2_out));
  not not_1 (not_1_out, B);
  mux_2 mux_2_2 (.A(B), .B(not_1_out), .out_4(mux_2_2_out_4), .C0(or_2_out));
  or or_1 (or_1_out, A, B);
  and and_1 (and_1_out, A, B);
  nand nand_1 (nand_1_out, A, B);
  xor xor_1 (xor_1_out, A, B);
  Somador somador_1 (.A(A), .B(mux_2_2_out_4), .Cin(mux_2_1_out_4), .Sum(somador_1_sum), .Cout(COUT));
  or or_2 (or_2_out, and_2_out, and_3_out);
  and and_2 (and_2_out, ~C1, C2, C3, ~C4, ~C5);  // AND_Gate
  and and_3 (and_3_out, C1, C2, C3, ~C4, ~C5);  // AND_Gate
  Demux_4_modif demux_4_modif_1 (
    .in_1(somador_1_sum), .in_2(or_2_out), .out_3(demux_4_modif_1_out_3), .out_4(demux_4_modif_1_out_4),
    .out_5(demux_4_modif_1_out_5), .out_6(demux_4_modif_1_out_6));
  Multiplexer #(.select(5), .enable("false")) multiplexer_1 (
    .in0(or_1_out), .in1(and_1_out), .in2(nand_1_out), .in3(xor_1_out), .in4(demux_4_modif_1_out_3),
    .in5(demux_4_modif_1_out_4), .in6(demux_4_modif_1_out_5), .in7(demux_4_modif_1_out_6), .in8(1'b0),
    .in9(1'b0), .in10(1'b0), .in11(1'b0), .in12(1'b0), .in13(1'b0), .in14(1'b0), .in15(1'b0), .in16(1'b0),
    .in17(1'b0), .in18(1'b0), .in19(1'b0), .in20(1'b0), .in21(1'b0), .in22(1'b0), .in23(1'b0), .in24(1'b0),
    .in25(1'b0), .in26(1'b0), .in27(1'b0), .in28(1'b0), .in29(1'b0), .in30(1'b0), .in31(1'b0),
    .sel({C1, C2, C3, C4, C5}));  // open: out

  // Notes on the sheet:
  //   00100 = somador
  //   10100 = somador
  //   01100 = subtração
  //   11100 = subtração
endmodule

module Somador (
  input  A,
  input  B,
  input  Cin,
  output Sum,
  output Cout
);

  wire and_1_out, and_2_out, and_3_out, xor_1_out;

  xor xor_1 (xor_1_out, A, B);
  and and_1 (and_1_out, Cin, A);
  and and_2 (and_2_out, Cin, B);
  and and_3 (and_3_out, B, A);
  xor xor_2 (Sum, xor_1_out, Cin);
  or or_1 (Cout, and_1_out, and_2_out, and_3_out);
endmodule

// PROCESSADOR
module Circuito_do_Processador_32bits (
  input  [31:0] A,
  input  [4:0] Deslocamento,
  input  [31:0] B,
  input  [4:0] in_4,
  output [31:0] S,
  output out_6,
  output vai1
);

  wire _1_cout, and_1_out, or_1_out, ula_32_1_cout, ula_32_2_cout, ula_32_3_cout, ula_32_4_cout,
       ula_32_5_cout, ula_32_6_cout, ula_32_7_cout, ula_32_8_cout, ula_32_9_cout, ula_32_10_cout,
       ula_32_11_cout, ula_32_12_cout, ula_32_13_cout, ula_32_14_cout, ula_32_15_cout, ula_32_16_cout,
       ula_32_17_cout, ula_32_18_cout, ula_32_19_cout, ula_32_20_cout, ula_32_21_cout, ula_32_22_cout,
       ula_32_23_cout, ula_32_24_cout, ula_32_25_cout, ula_32_26_cout, ula_32_27_cout, ula_32_28_cout,
       ula_32_29_cout, ula_32_30_cout;
  wire [31:0] seletor_de_shifter_1_out;

  Seletor_de_Shifter seletor_de_shifter_1 (
    .IN(A), .in_2(Deslocamento), .L_R(and_1_out), .OUT(seletor_de_shifter_1_out));
  and and_1 (and_1_out, ~in_4[0], in_4[1], in_4[2], ~in_4[3], ~in_4[4]);  // AND_Gate
  ULA_32 _1 (
    .S(S[0]), .COUT(_1_cout), .A(seletor_de_shifter_1_out[0]), .B(B[0]), .C1(in_4[0]), .C2(in_4[1]),
    .C3(in_4[2]), .C4(in_4[3]), .C5(in_4[4]), .Cin(1'b0));
  ULA_32 ula_32_1 (
    .S(S[8]), .COUT(ula_32_1_cout), .A(seletor_de_shifter_1_out[8]), .B(B[8]), .C1(in_4[0]), .C2(in_4[1]),
    .C3(in_4[2]), .C4(in_4[3]), .C5(in_4[4]), .Cin(ula_32_28_cout));
  ULA_32 ula_32_2 (
    .S(S[16]), .COUT(ula_32_2_cout), .A(seletor_de_shifter_1_out[16]), .B(B[16]), .C1(in_4[0]), .C2(in_4[1]),
    .C3(in_4[2]), .C4(in_4[3]), .C5(in_4[4]), .Cin(ula_32_29_cout));
  ULA_32 ula_32_3 (
    .S(S[24]), .COUT(ula_32_3_cout), .A(seletor_de_shifter_1_out[24]), .B(B[24]), .C1(in_4[0]), .C2(in_4[1]),
    .C3(in_4[2]), .C4(in_4[3]), .C5(in_4[4]), .Cin(ula_32_30_cout));
  ULA_32 ula_32_4 (
    .S(S[1]), .COUT(ula_32_4_cout), .A(seletor_de_shifter_1_out[1]), .B(B[1]), .C1(in_4[0]), .C2(in_4[1]),
    .C3(in_4[2]), .C4(in_4[3]), .C5(in_4[4]), .Cin(_1_cout));
  ULA_32 ula_32_5 (
    .S(S[9]), .COUT(ula_32_5_cout), .A(seletor_de_shifter_1_out[9]), .B(B[9]), .C1(in_4[0]), .C2(in_4[1]),
    .C3(in_4[2]), .C4(in_4[3]), .C5(in_4[4]), .Cin(ula_32_1_cout));
  ULA_32 ula_32_6 (
    .S(S[17]), .COUT(ula_32_6_cout), .A(seletor_de_shifter_1_out[17]), .B(B[17]), .C1(in_4[0]), .C2(in_4[1]),
    .C3(in_4[2]), .C4(in_4[3]), .C5(in_4[4]), .Cin(ula_32_2_cout));
  ULA_32 ula_32_7 (
    .S(S[25]), .COUT(ula_32_7_cout), .A(seletor_de_shifter_1_out[25]), .B(B[25]), .C1(in_4[0]), .C2(in_4[1]),
    .C3(in_4[2]), .C4(in_4[3]), .C5(in_4[4]), .Cin(ula_32_3_cout));
  ULA_32 ula_32_8 (
    .S(S[2]), .COUT(ula_32_8_cout), .A(seletor_de_shifter_1_out[2]), .B(B[2]), .C1(in_4[0]), .C2(in_4[1]),
    .C3(in_4[2]), .C4(in_4[3]), .C5(in_4[4]), .Cin(ula_32_4_cout));
  ULA_32 ula_32_9 (
    .S(S[10]), .COUT(ula_32_9_cout), .A(seletor_de_shifter_1_out[10]), .B(B[10]), .C1(in_4[0]), .C2(in_4[1]),
    .C3(in_4[2]), .C4(in_4[3]), .C5(in_4[4]), .Cin(ula_32_5_cout));
  ULA_32 ula_32_10 (
    .S(S[18]), .COUT(ula_32_10_cout), .A(seletor_de_shifter_1_out[18]), .B(B[18]), .C1(in_4[0]),
    .C2(in_4[1]), .C3(in_4[2]), .C4(in_4[3]), .C5(in_4[4]), .Cin(ula_32_6_cout));
  ULA_32 ula_32_11 (
    .S(S[26]), .COUT(ula_32_11_cout), .A(seletor_de_shifter_1_out[26]), .B(B[26]), .C1(in_4[0]),
    .C2(in_4[1]), .C3(in_4[2]), .C4(in_4[3]), .C5(in_4[4]), .Cin(ula_32_7_cout));
  ULA_32 ula_32_12 (
    .S(S[3]), .COUT(ula_32_12_cout), .A(seletor_de_shifter_1_out[3]), .B(B[3]), .C1(in_4[0]), .C2(in_4[1]),
    .C3(in_4[2]), .C4(in_4[3]), .C5(in_4[4]), .Cin(ula_32_8_cout));
  ULA_32 ula_32_13 (
    .S(S[11]), .COUT(ula_32_13_cout), .A(seletor_de_shifter_1_out[11]), .B(B[11]), .C1(in_4[0]),
    .C2(in_4[1]), .C3(in_4[2]), .C4(in_4[3]), .C5(in_4[4]), .Cin(ula_32_9_cout));
  ULA_32 ula_32_14 (
    .S(S[19]), .COUT(ula_32_14_cout), .A(seletor_de_shifter_1_out[19]), .B(B[19]), .C1(in_4[0]),
    .C2(in_4[1]), .C3(in_4[2]), .C4(in_4[3]), .C5(in_4[4]), .Cin(ula_32_10_cout));
  ULA_32 ula_32_15 (
    .S(S[27]), .COUT(ula_32_15_cout), .A(seletor_de_shifter_1_out[27]), .B(B[27]), .C1(in_4[0]),
    .C2(in_4[1]), .C3(in_4[2]), .C4(in_4[3]), .C5(in_4[4]), .Cin(ula_32_11_cout));
  ULA_32 ula_32_16 (
    .S(S[4]), .COUT(ula_32_16_cout), .A(seletor_de_shifter_1_out[4]), .B(B[4]), .C1(in_4[0]), .C2(in_4[1]),
    .C3(in_4[2]), .C4(in_4[3]), .C5(in_4[4]), .Cin(ula_32_12_cout));
  ULA_32 ula_32_17 (
    .S(S[12]), .COUT(ula_32_17_cout), .A(seletor_de_shifter_1_out[12]), .B(B[12]), .C1(in_4[0]),
    .C2(in_4[1]), .C3(in_4[2]), .C4(in_4[3]), .C5(in_4[4]), .Cin(ula_32_13_cout));
  ULA_32 ula_32_18 (
    .S(S[20]), .COUT(ula_32_18_cout), .A(seletor_de_shifter_1_out[20]), .B(B[20]), .C1(in_4[0]),
    .C2(in_4[1]), .C3(in_4[2]), .C4(in_4[3]), .C5(in_4[4]), .Cin(ula_32_14_cout));
  ULA_32 ula_32_19 (
    .S(S[28]), .COUT(ula_32_19_cout), .A(seletor_de_shifter_1_out[28]), .B(B[28]), .C1(in_4[0]),
    .C2(in_4[1]), .C3(in_4[2]), .C4(in_4[3]), .C5(in_4[4]), .Cin(ula_32_15_cout));
  ULA_32 ula_32_20 (
    .S(S[21]), .COUT(ula_32_20_cout), .A(seletor_de_shifter_1_out[21]), .B(B[21]), .C1(in_4[0]),
    .C2(in_4[1]), .C3(in_4[2]), .C4(in_4[3]), .C5(in_4[4]), .Cin(ula_32_18_cout));
  ULA_32 ula_32_21 (
    .S(S[5]), .COUT(ula_32_21_cout), .A(seletor_de_shifter_1_out[5]), .B(B[5]), .C1(in_4[0]), .C2(in_4[1]),
    .C3(in_4[2]), .C4(in_4[3]), .C5(in_4[4]), .Cin(ula_32_16_cout));
  ULA_32 ula_32_22 (
    .S(S[13]), .COUT(ula_32_22_cout), .A(seletor_de_shifter_1_out[13]), .B(B[13]), .C1(in_4[0]),
    .C2(in_4[1]), .C3(in_4[2]), .C4(in_4[3]), .C5(in_4[4]), .Cin(ula_32_17_cout));
  ULA_32 ula_32_23 (
    .S(S[29]), .COUT(ula_32_23_cout), .A(seletor_de_shifter_1_out[29]), .B(B[29]), .C1(in_4[0]),
    .C2(in_4[1]), .C3(in_4[2]), .C4(in_4[3]), .C5(in_4[4]), .Cin(ula_32_19_cout));
  ULA_32 ula_32_24 (
    .S(S[6]), .COUT(ula_32_24_cout), .A(seletor_de_shifter_1_out[6]), .B(B[6]), .C1(in_4[0]), .C2(in_4[1]),
    .C3(in_4[2]), .C4(in_4[3]), .C5(in_4[4]), .Cin(ula_32_21_cout));
  ULA_32 ula_32_25 (
    .S(S[14]), .COUT(ula_32_25_cout), .A(seletor_de_shifter_1_out[14]), .B(B[15]), .C1(in_4[0]),
    .C2(in_4[1]), .C3(in_4[2]), .C4(in_4[3]), .C5(in_4[4]), .Cin(ula_32_22_cout));
  ULA_32 ula_32_26 (
    .S(S[22]), .COUT(ula_32_26_cout), .A(seletor_de_shifter_1_out[22]), .B(B[22]), .C1(in_4[0]),
    .C2(in_4[1]), .C3(in_4[2]), .C4(in_4[3]), .C5(in_4[4]), .Cin(ula_32_20_cout));
  ULA_32 ula_32_27 (
    .S(S[30]), .COUT(ula_32_27_cout), .A(seletor_de_shifter_1_out[30]), .B(B[30]), .C1(in_4[0]),
    .C2(in_4[1]), .C3(in_4[2]), .C4(in_4[3]), .C5(in_4[4]), .Cin(ula_32_23_cout));
  ULA_32 ula_32_28 (
    .S(S[7]), .COUT(ula_32_28_cout), .A(seletor_de_shifter_1_out[7]), .B(B[7]), .C1(in_4[0]), .C2(in_4[1]),
    .C3(in_4[2]), .C4(in_4[3]), .C5(in_4[4]), .Cin(ula_32_24_cout));
  ULA_32 ula_32_29 (
    .S(S[15]), .COUT(ula_32_29_cout), .A(seletor_de_shifter_1_out[15]), .B(B[14]), .C1(in_4[0]),
    .C2(in_4[1]), .C3(in_4[2]), .C4(in_4[3]), .C5(in_4[4]), .Cin(ula_32_25_cout));
  ULA_32 ula_32_30 (
    .S(S[23]), .COUT(ula_32_30_cout), .A(seletor_de_shifter_1_out[23]), .B(B[23]), .C1(in_4[0]),
    .C2(in_4[1]), .C3(in_4[2]), .C4(in_4[3]), .C5(in_4[4]), .Cin(ula_32_26_cout));
  ULA_32 _32 (
    .S(S[31]), .COUT(vai1), .A(seletor_de_shifter_1_out[31]), .B(B[31]), .C1(in_4[0]), .C2(in_4[1]),
    .C3(in_4[2]), .C4(in_4[3]), .C5(in_4[4]), .Cin(ula_32_27_cout));
  or or_1 (or_1_out, S[0], S[1], S[2], S[3], S[4], S[5], S[6], S[7], S[8], S[9], S[10], S[11], S[12], S[13], S[14], S[15], S[16], S[17], S[18], S[19], S[20], S[21], S[22], S[23], S[24], S[25], S[26], S[27], S[28], S[29], S[30], S[31]);
  not not_1 (out_6, or_1_out);
endmodule

module Barrel_left_Shifter_32 (
  input  [31:0] IN,
  input  MSB,
  input  C1,
  input  C2,
  input  C3,
  input  LSB,
  output [31:0] OUT
);

  wire mux_2_p_barrel_shift_1_out_4, mux_2_p_barrel_shift_2_out_4, mux_2_p_barrel_shift_3_out_4,
       mux_2_p_barrel_shift_4_out_4, mux_2_p_barrel_shift_6_out_4, mux_2_p_barrel_shift_7_out_4,
       mux_2_p_barrel_shift_8_out_4, mux_2_p_barrel_shift_9_out_4, mux_2_p_barrel_shift_10_out_4,
       mux_2_p_barrel_shift_11_out_4, mux_2_p_barrel_shift_12_out_4, mux_2_p_barrel_shift_14_out_4,
       mux_2_p_barrel_shift_15_out_4, mux_2_p_barrel_shift_16_out_4, mux_2_p_barrel_shift_18_out_4,
       mux_2_p_barrel_shift_19_out_4, mux_2_p_barrel_shift_20_out_4, mux_2_p_barrel_shift_22_out_4,
       mux_2_p_barrel_shift_23_out_4, mux_2_p_barrel_shift_24_out_4, mux_2_p_barrel_shift_26_out_4,
       mux_2_p_barrel_shift_27_out_4, mux_2_p_barrel_shift_28_out_4, mux_2_p_barrel_shift_29_out_4,
       mux_2_p_barrel_shift_30_out_4, mux_2_p_barrel_shift_31_out_4, mux_2_p_barrel_shift_32_out_4,
       mux_2_p_barrel_shift_34_out_4, mux_2_p_barrel_shift_35_out_4, mux_2_p_barrel_shift_36_out_4,
       mux_2_p_barrel_shift_38_out_4, mux_2_p_barrel_shift_39_out_4, mux_2_p_barrel_shift_40_out_4,
       mux_2_p_barrel_shift_42_out_4, mux_2_p_barrel_shift_43_out_4, mux_2_p_barrel_shift_44_out_4,
       mux_2_p_barrel_shift_46_out_4, mux_2_p_barrel_shift_47_out_4, mux_2_p_barrel_shift_48_out_4,
       mux_2_p_barrel_shift_49_out_4, mux_2_p_barrel_shift_50_out_4, mux_2_p_barrel_shift_51_out_4,
       mux_2_p_barrel_shift_52_out_4, mux_2_p_barrel_shift_54_out_4, mux_2_p_barrel_shift_55_out_4,
       mux_2_p_barrel_shift_56_out_4, mux_2_p_barrel_shift_58_out_4, mux_2_p_barrel_shift_59_out_4,
       mux_2_p_barrel_shift_60_out_4, mux_2_p_barrel_shift_62_out_4, mux_2_p_barrel_shift_63_out_4,
       mux_2_p_barrel_shift_64_out_4, mux_2_p_barrel_shift_66_out_4, mux_2_p_barrel_shift_67_out_4,
       mux_2_p_barrel_shift_68_out_4, mux_2_p_barrel_shift_69_out_4, mux_2_p_barrel_shift_70_out_4,
       mux_2_p_barrel_shift_71_out_4, mux_2_p_barrel_shift_72_out_4, mux_2_p_barrel_shift_74_out_4,
       mux_2_p_barrel_shift_75_out_4, mux_2_p_barrel_shift_76_out_4, mux_2_p_barrel_shift_78_out_4,
       mux_2_p_barrel_shift_79_out_4, mux_2_p_barrel_shift_80_out_4, mux_2_p_barrel_shift_82_out_4,
       mux_2_p_barrel_shift_83_out_4, mux_2_p_barrel_shift_84_out_4, mux_2_p_barrel_shift_86_out_4,
       mux_2_p_barrel_shift_87_out_4, mux_2_p_barrel_shift_88_out_4, mux_2_p_barrel_shift_89_out_4,
       mux_2_p_barrel_shift_90_out_4, mux_2_p_barrel_shift_91_out_4, mux_2_p_barrel_shift_92_out_4,
       mux_2_p_barrel_shift_94_out_4, mux_2_p_barrel_shift_95_out_4, mux_2_p_barrel_shift_96_out_4,
       mux_2_p_barrel_shift_98_out_4, mux_2_p_barrel_shift_99_out_4, mux_2_p_barrel_shift_100_out_4,
       mux_2_p_barrel_shift_102_out_4, mux_2_p_barrel_shift_103_out_4, mux_2_p_barrel_shift_104_out_4,
       mux_2_p_barrel_shift_106_out_4, mux_2_p_barrel_shift_107_out_4, mux_2_p_barrel_shift_108_out_4,
       mux_2_p_barrel_shift_109_out_4, mux_2_p_barrel_shift_110_out_4, mux_2_p_barrel_shift_111_out_4,
       mux_2_p_barrel_shift_112_out_4, mux_2_p_barrel_shift_114_out_4, mux_2_p_barrel_shift_115_out_4,
       mux_2_p_barrel_shift_116_out_4, mux_2_p_barrel_shift_118_out_4, mux_2_p_barrel_shift_119_out_4,
       mux_2_p_barrel_shift_120_out_4, mux_2_p_barrel_shift_122_out_4, mux_2_p_barrel_shift_123_out_4,
       mux_2_p_barrel_shift_124_out_4, mux_2_p_barrel_shift_126_out_4, mux_2_p_barrel_shift_127_out_4,
       mux_2_p_barrel_shift_128_out_4, mux_2_p_barrel_shift_129_out_4, mux_2_p_barrel_shift_130_out_4,
       mux_2_p_barrel_shift_131_out_4, mux_2_p_barrel_shift_132_out_4, mux_2_p_barrel_shift_134_out_4,
       mux_2_p_barrel_shift_135_out_4, mux_2_p_barrel_shift_136_out_4, mux_2_p_barrel_shift_138_out_4,
       mux_2_p_barrel_shift_139_out_4, mux_2_p_barrel_shift_140_out_4, mux_2_p_barrel_shift_142_out_4,
       mux_2_p_barrel_shift_143_out_4, mux_2_p_barrel_shift_144_out_4, mux_2_p_barrel_shift_146_out_4,
       mux_2_p_barrel_shift_147_out_4, mux_2_p_barrel_shift_148_out_4, mux_2_p_barrel_shift_149_out_4,
       mux_2_p_barrel_shift_150_out_4, mux_2_p_barrel_shift_151_out_4, mux_2_p_barrel_shift_152_out_4,
       mux_2_p_barrel_shift_154_out_4, mux_2_p_barrel_shift_155_out_4, mux_2_p_barrel_shift_156_out_4,
       mux_2_p_barrel_shift_158_out_4, mux_2_p_barrel_shift_159_out_4;

  MUX_2____P_barrel_shift mux_2_p_barrel_shift_1 (
    .A(IN[31]), .B(IN[15]), .out_4(mux_2_p_barrel_shift_1_out_4), .C0(MSB));
  MUX_2____P_barrel_shift mux_2_p_barrel_shift_2 (
    .A(mux_2_p_barrel_shift_1_out_4), .B(mux_2_p_barrel_shift_78_out_4),
    .out_4(mux_2_p_barrel_shift_2_out_4), .C0(C1));
  MUX_2____P_barrel_shift mux_2_p_barrel_shift_3 (
    .A(mux_2_p_barrel_shift_2_out_4), .B(mux_2_p_barrel_shift_22_out_4),
    .out_4(mux_2_p_barrel_shift_3_out_4), .C0(C2));
  MUX_2____P_barrel_shift mux_2_p_barrel_shift_4 (
    .A(mux_2_p_barrel_shift_3_out_4), .B(mux_2_p_barrel_shift_12_out_4),
    .out_4(mux_2_p_barrel_shift_4_out_4), .C0(C3));
  MUX_2____P_barrel_shift mux_2_p_barrel_shift_5 (
    .A(mux_2_p_barrel_shift_4_out_4), .B(mux_2_p_barrel_shift_9_out_4), .out_4(OUT[31]), .C0(LSB));
  MUX_2____P_barrel_shift mux_2_p_barrel_shift_6 (
    .A(IN[30]), .B(IN[14]), .out_4(mux_2_p_barrel_shift_6_out_4), .C0(MSB));
  MUX_2____P_barrel_shift mux_2_p_barrel_shift_7 (
    .A(mux_2_p_barrel_shift_6_out_4), .B(mux_2_p_barrel_shift_46_out_4),
    .out_4(mux_2_p_barrel_shift_7_out_4), .C0(C1));
  MUX_2____P_barrel_shift mux_2_p_barrel_shift_8 (
    .A(mux_2_p_barrel_shift_7_out_4), .B(mux_2_p_barrel_shift_27_out_4),
    .out_4(mux_2_p_barrel_shift_8_out_4), .C0(C2));
  MUX_2____P_barrel_shift mux_2_p_barrel_shift_9 (
    .A(mux_2_p_barrel_shift_8_out_4), .B(mux_2_p_barrel_shift_19_out_4),
    .out_4(mux_2_p_barrel_shift_9_out_4), .C0(C3));
  MUX_2____P_barrel_shift mux_2_p_barrel_shift_10 (
    .A(IN[29]), .B(IN[13]), .out_4(mux_2_p_barrel_shift_10_out_4), .C0(MSB));
  MUX_2____P_barrel_shift mux_2_p_barrel_shift_11 (
    .A(mux_2_p_barrel_shift_10_out_4), .B(mux_2_p_barrel_shift_50_out_4),
    .out_4(mux_2_p_barrel_shift_11_out_4), .C0(C1));
  MUX_2____P_barrel_shift mux_2_p_barrel_shift_12 (
    .A(mux_2_p_barrel_shift_11_out_4), .B(mux_2_p_barrel_shift_31_out_4),
    .out_4(mux_2_p_barrel_shift_12_out_4), .C0(C2));
  MUX_2____P_barrel_shift mux_2_p_barrel_shift_13 (
    .A(mux_2_p_barrel_shift_9_out_4), .B(mux_2_p_barrel_shift_16_out_4), .out_4(OUT[30]), .C0(LSB));
  MUX_2____P_barrel_shift mux_2_p_barrel_shift_14 (
    .A(IN[28]), .B(IN[12]), .out_4(mux_2_p_barrel_shift_14_out_4), .C0(MSB));
  MUX_2____P_barrel_shift mux_2_p_barrel_shift_15 (
    .A(mux_2_p_barrel_shift_14_out_4), .B(mux_2_p_barrel_shift_54_out_4),
    .out_4(mux_2_p_barrel_shift_15_out_4), .C0(C1));
  MUX_2____P_barrel_shift mux_2_p_barrel_shift_16 (
    .A(mux_2_p_barrel_shift_12_out_4), .B(mux_2_p_barrel_shift_23_out_4),
    .out_4(mux_2_p_barrel_shift_16_out_4), .C0(C3));
  MUX_2____P_barrel_shift mux_2_p_barrel_shift_17 (
    .A(mux_2_p_barrel_shift_16_out_4), .B(mux_2_p_barrel_shift_20_out_4), .out_4(OUT[29]), .C0(LSB));
  MUX_2____P_barrel_shift mux_2_p_barrel_shift_18 (
    .A(IN[27]), .B(IN[11]), .out_4(mux_2_p_barrel_shift_18_out_4), .C0(MSB));
  MUX_2____P_barrel_shift mux_2_p_barrel_shift_19 (
    .A(mux_2_p_barrel_shift_15_out_4), .B(mux_2_p_barrel_shift_35_out_4),
    .out_4(mux_2_p_barrel_shift_19_out_4), .C0(C2));
  MUX_2____P_barrel_shift mux_2_p_barrel_shift_20 (
    .A(mux_2_p_barrel_shift_19_out_4), .B(mux_2_p_barrel_shift_28_out_4),
    .out_4(mux_2_p_barrel_shift_20_out_4), .C0(C3));
  MUX_2____P_barrel_shift mux_2_p_barrel_shift_21 (
    .A(mux_2_p_barrel_shift_20_out_4), .B(mux_2_p_barrel_shift_24_out_4), .out_4(OUT[28]), .C0(LSB));
  MUX_2____P_barrel_shift mux_2_p_barrel_shift_22 (
    .A(mux_2_p_barrel_shift_18_out_4), .B(mux_2_p_barrel_shift_58_out_4),
    .out_4(mux_2_p_barrel_shift_22_out_4), .C0(C1));
  MUX_2____P_barrel_shift mux_2_p_barrel_shift_23 (
    .A(mux_2_p_barrel_shift_22_out_4), .B(mux_2_p_barrel_shift_42_out_4),
    .out_4(mux_2_p_barrel_shift_23_out_4), .C0(C2));
  MUX_2____P_barrel_shift mux_2_p_barrel_shift_24 (
    .A(mux_2_p_barrel_shift_23_out_4), .B(mux_2_p_barrel_shift_32_out_4),
    .out_4(mux_2_p_barrel_shift_24_out_4), .C0(C3));
  MUX_2____P_barrel_shift mux_2_p_barrel_shift_25 (
    .A(mux_2_p_barrel_shift_24_out_4), .B(mux_2_p_barrel_shift_29_out_4), .out_4(OUT[27]), .C0(LSB));
  MUX_2____P_barrel_shift mux_2_p_barrel_shift_26 (
    .A(IN[26]), .B(IN[10]), .out_4(mux_2_p_barrel_shift_26_out_4), .C0(MSB));
  MUX_2____P_barrel_shift mux_2_p_barrel_shift_27 (
    .A(mux_2_p_barrel_shift_26_out_4), .B(mux_2_p_barrel_shift_66_out_4),
    .out_4(mux_2_p_barrel_shift_27_out_4), .C0(C1));
  MUX_2____P_barrel_shift mux_2_p_barrel_shift_28 (
    .A(mux_2_p_barrel_shift_27_out_4), .B(mux_2_p_barrel_shift_47_out_4),
    .out_4(mux_2_p_barrel_shift_28_out_4), .C0(C2));
  MUX_2____P_barrel_shift mux_2_p_barrel_shift_29 (
    .A(mux_2_p_barrel_shift_28_out_4), .B(mux_2_p_barrel_shift_39_out_4),
    .out_4(mux_2_p_barrel_shift_29_out_4), .C0(C3));
  MUX_2____P_barrel_shift mux_2_p_barrel_shift_30 (
    .A(IN[25]), .B(IN[9]), .out_4(mux_2_p_barrel_shift_30_out_4), .C0(MSB));
  MUX_2____P_barrel_shift mux_2_p_barrel_shift_31 (
    .A(mux_2_p_barrel_shift_30_out_4), .B(mux_2_p_barrel_shift_70_out_4),
    .out_4(mux_2_p_barrel_shift_31_out_4), .C0(C1));
  MUX_2____P_barrel_shift mux_2_p_barrel_shift_32 (
    .A(mux_2_p_barrel_shift_31_out_4), .B(mux_2_p_barrel_shift_51_out_4),
    .out_4(mux_2_p_barrel_shift_32_out_4), .C0(C2));
  MUX_2____P_barrel_shift mux_2_p_barrel_shift_33 (
    .A(mux_2_p_barrel_shift_29_out_4), .B(mux_2_p_barrel_shift_36_out_4), .out_4(OUT[26]), .C0(LSB));
  MUX_2____P_barrel_shift mux_2_p_barrel_shift_34 (
    .A(IN[24]), .B(IN[8]), .out_4(mux_2_p_barrel_shift_34_out_4), .C0(MSB));
  MUX_2____P_barrel_shift mux_2_p_barrel_shift_35 (
    .A(mux_2_p_barrel_shift_34_out_4), .B(mux_2_p_barrel_shift_74_out_4),
    .out_4(mux_2_p_barrel_shift_35_out_4), .C0(C1));
  MUX_2____P_barrel_shift mux_2_p_barrel_shift_36 (
    .A(mux_2_p_barrel_shift_32_out_4), .B(mux_2_p_barrel_shift_43_out_4),
    .out_4(mux_2_p_barrel_shift_36_out_4), .C0(C3));
  MUX_2____P_barrel_shift mux_2_p_barrel_shift_37 (
    .A(mux_2_p_barrel_shift_36_out_4), .B(mux_2_p_barrel_shift_40_out_4), .out_4(OUT[25]), .C0(LSB));
  MUX_2____P_barrel_shift mux_2_p_barrel_shift_38 (
    .A(IN[23]), .B(IN[7]), .out_4(mux_2_p_barrel_shift_38_out_4), .C0(MSB));
  MUX_2____P_barrel_shift mux_2_p_barrel_shift_39 (
    .A(mux_2_p_barrel_shift_35_out_4), .B(mux_2_p_barrel_shift_55_out_4),
    .out_4(mux_2_p_barrel_shift_39_out_4), .C0(C2));
  MUX_2____P_barrel_shift mux_2_p_barrel_shift_40 (
    .A(mux_2_p_barrel_shift_39_out_4), .B(mux_2_p_barrel_shift_48_out_4),
    .out_4(mux_2_p_barrel_shift_40_out_4), .C0(C3));
  MUX_2____P_barrel_shift mux_2_p_barrel_shift_41 (
    .A(mux_2_p_barrel_shift_40_out_4), .B(mux_2_p_barrel_shift_44_out_4), .out_4(OUT[24]), .C0(LSB));
  MUX_2____P_barrel_shift mux_2_p_barrel_shift_42 (
    .A(mux_2_p_barrel_shift_38_out_4), .B(mux_2_p_barrel_shift_78_out_4),
    .out_4(mux_2_p_barrel_shift_42_out_4), .C0(C1));
  MUX_2____P_barrel_shift mux_2_p_barrel_shift_43 (
    .A(mux_2_p_barrel_shift_42_out_4), .B(mux_2_p_barrel_shift_62_out_4),
    .out_4(mux_2_p_barrel_shift_43_out_4), .C0(C2));
  MUX_2____P_barrel_shift mux_2_p_barrel_shift_44 (
    .A(mux_2_p_barrel_shift_43_out_4), .B(mux_2_p_barrel_shift_52_out_4),
    .out_4(mux_2_p_barrel_shift_44_out_4), .C0(C3));
  MUX_2____P_barrel_shift mux_2_p_barrel_shift_45 (
    .A(mux_2_p_barrel_shift_44_out_4), .B(mux_2_p_barrel_shift_49_out_4), .out_4(OUT[23]), .C0(LSB));
  MUX_2____P_barrel_shift mux_2_p_barrel_shift_46 (
    .A(IN[22]), .B(IN[6]), .out_4(mux_2_p_barrel_shift_46_out_4), .C0(MSB));
  MUX_2____P_barrel_shift mux_2_p_barrel_shift_47 (
    .A(mux_2_p_barrel_shift_46_out_4), .B(mux_2_p_barrel_shift_86_out_4),
    .out_4(mux_2_p_barrel_shift_47_out_4), .C0(C1));
  MUX_2____P_barrel_shift mux_2_p_barrel_shift_48 (
    .A(mux_2_p_barrel_shift_47_out_4), .B(mux_2_p_barrel_shift_67_out_4),
    .out_4(mux_2_p_barrel_shift_48_out_4), .C0(C2));
  MUX_2____P_barrel_shift mux_2_p_barrel_shift_49 (
    .A(mux_2_p_barrel_shift_48_out_4), .B(mux_2_p_barrel_shift_59_out_4),
    .out_4(mux_2_p_barrel_shift_49_out_4), .C0(C3));
  MUX_2____P_barrel_shift mux_2_p_barrel_shift_50 (
    .A(IN[21]), .B(IN[5]), .out_4(mux_2_p_barrel_shift_50_out_4), .C0(MSB));
  MUX_2____P_barrel_shift mux_2_p_barrel_shift_51 (
    .A(mux_2_p_barrel_shift_50_out_4), .B(mux_2_p_barrel_shift_90_out_4),
    .out_4(mux_2_p_barrel_shift_51_out_4), .C0(C1));
  MUX_2____P_barrel_shift mux_2_p_barrel_shift_52 (
    .A(mux_2_p_barrel_shift_51_out_4), .B(mux_2_p_barrel_shift_71_out_4),
    .out_4(mux_2_p_barrel_shift_52_out_4), .C0(C2));
  MUX_2____P_barrel_shift mux_2_p_barrel_shift_53 (
    .A(mux_2_p_barrel_shift_49_out_4), .B(mux_2_p_barrel_shift_56_out_4), .out_4(OUT[22]), .C0(LSB));
  MUX_2____P_barrel_shift mux_2_p_barrel_shift_54 (
    .A(IN[20]), .B(IN[4]), .out_4(mux_2_p_barrel_shift_54_out_4), .C0(MSB));
  MUX_2____P_barrel_shift mux_2_p_barrel_shift_55 (
    .A(mux_2_p_barrel_shift_54_out_4), .B(mux_2_p_barrel_shift_94_out_4),
    .out_4(mux_2_p_barrel_shift_55_out_4), .C0(C1));
  MUX_2____P_barrel_shift mux_2_p_barrel_shift_56 (
    .A(mux_2_p_barrel_shift_52_out_4), .B(mux_2_p_barrel_shift_63_out_4),
    .out_4(mux_2_p_barrel_shift_56_out_4), .C0(C3));
  MUX_2____P_barrel_shift mux_2_p_barrel_shift_57 (
    .A(mux_2_p_barrel_shift_56_out_4), .B(mux_2_p_barrel_shift_60_out_4), .out_4(OUT[21]), .C0(LSB));
  MUX_2____P_barrel_shift mux_2_p_barrel_shift_58 (
    .A(IN[19]), .B(IN[3]), .out_4(mux_2_p_barrel_shift_58_out_4), .C0(MSB));
  MUX_2____P_barrel_shift mux_2_p_barrel_shift_59 (
    .A(mux_2_p_barrel_shift_55_out_4), .B(mux_2_p_barrel_shift_75_out_4),
    .out_4(mux_2_p_barrel_shift_59_out_4), .C0(C2));
  MUX_2____P_barrel_shift mux_2_p_barrel_shift_60 (
    .A(mux_2_p_barrel_shift_59_out_4), .B(mux_2_p_barrel_shift_68_out_4),
    .out_4(mux_2_p_barrel_shift_60_out_4), .C0(C3));
  MUX_2____P_barrel_shift mux_2_p_barrel_shift_61 (
    .A(mux_2_p_barrel_shift_60_out_4), .B(mux_2_p_barrel_shift_64_out_4), .out_4(OUT[20]), .C0(LSB));
  MUX_2____P_barrel_shift mux_2_p_barrel_shift_62 (
    .A(mux_2_p_barrel_shift_58_out_4), .B(mux_2_p_barrel_shift_98_out_4),
    .out_4(mux_2_p_barrel_shift_62_out_4), .C0(C1));
  MUX_2____P_barrel_shift mux_2_p_barrel_shift_63 (
    .A(mux_2_p_barrel_shift_62_out_4), .B(mux_2_p_barrel_shift_82_out_4),
    .out_4(mux_2_p_barrel_shift_63_out_4), .C0(C2));
  MUX_2____P_barrel_shift mux_2_p_barrel_shift_64 (
    .A(mux_2_p_barrel_shift_63_out_4), .B(mux_2_p_barrel_shift_72_out_4),
    .out_4(mux_2_p_barrel_shift_64_out_4), .C0(C3));
  MUX_2____P_barrel_shift mux_2_p_barrel_shift_65 (
    .A(mux_2_p_barrel_shift_64_out_4), .B(mux_2_p_barrel_shift_69_out_4), .out_4(OUT[19]), .C0(LSB));
  MUX_2____P_barrel_shift mux_2_p_barrel_shift_66 (
    .A(IN[18]), .B(IN[2]), .out_4(mux_2_p_barrel_shift_66_out_4), .C0(MSB));
  MUX_2____P_barrel_shift mux_2_p_barrel_shift_67 (
    .A(mux_2_p_barrel_shift_66_out_4), .B(mux_2_p_barrel_shift_106_out_4),
    .out_4(mux_2_p_barrel_shift_67_out_4), .C0(C1));
  MUX_2____P_barrel_shift mux_2_p_barrel_shift_68 (
    .A(mux_2_p_barrel_shift_67_out_4), .B(mux_2_p_barrel_shift_87_out_4),
    .out_4(mux_2_p_barrel_shift_68_out_4), .C0(C2));
  MUX_2____P_barrel_shift mux_2_p_barrel_shift_69 (
    .A(mux_2_p_barrel_shift_68_out_4), .B(mux_2_p_barrel_shift_79_out_4),
    .out_4(mux_2_p_barrel_shift_69_out_4), .C0(C3));
  MUX_2____P_barrel_shift mux_2_p_barrel_shift_70 (
    .A(IN[17]), .B(IN[1]), .out_4(mux_2_p_barrel_shift_70_out_4), .C0(MSB));
  MUX_2____P_barrel_shift mux_2_p_barrel_shift_71 (
    .A(mux_2_p_barrel_shift_70_out_4), .B(mux_2_p_barrel_shift_110_out_4),
    .out_4(mux_2_p_barrel_shift_71_out_4), .C0(C1));
  MUX_2____P_barrel_shift mux_2_p_barrel_shift_72 (
    .A(mux_2_p_barrel_shift_71_out_4), .B(mux_2_p_barrel_shift_91_out_4),
    .out_4(mux_2_p_barrel_shift_72_out_4), .C0(C2));
  MUX_2____P_barrel_shift mux_2_p_barrel_shift_73 (
    .A(mux_2_p_barrel_shift_69_out_4), .B(mux_2_p_barrel_shift_76_out_4), .out_4(OUT[18]), .C0(LSB));
  MUX_2____P_barrel_shift mux_2_p_barrel_shift_74 (
    .A(IN[16]), .B(IN[0]), .out_4(mux_2_p_barrel_shift_74_out_4), .C0(MSB));
  MUX_2____P_barrel_shift mux_2_p_barrel_shift_75 (
    .A(mux_2_p_barrel_shift_74_out_4), .B(mux_2_p_barrel_shift_114_out_4),
    .out_4(mux_2_p_barrel_shift_75_out_4), .C0(C1));
  MUX_2____P_barrel_shift mux_2_p_barrel_shift_76 (
    .A(mux_2_p_barrel_shift_72_out_4), .B(mux_2_p_barrel_shift_83_out_4),
    .out_4(mux_2_p_barrel_shift_76_out_4), .C0(C3));
  MUX_2____P_barrel_shift mux_2_p_barrel_shift_77 (
    .A(mux_2_p_barrel_shift_76_out_4), .B(mux_2_p_barrel_shift_80_out_4), .out_4(OUT[17]), .C0(LSB));
  MUX_2____P_barrel_shift mux_2_p_barrel_shift_78 (
    .A(IN[15]), .B(1'b0), .out_4(mux_2_p_barrel_shift_78_out_4), .C0(MSB));
  MUX_2____P_barrel_shift mux_2_p_barrel_shift_79 (
    .A(mux_2_p_barrel_shift_75_out_4), .B(mux_2_p_barrel_shift_95_out_4),
    .out_4(mux_2_p_barrel_shift_79_out_4), .C0(C2));
  MUX_2____P_barrel_shift mux_2_p_barrel_shift_80 (
    .A(mux_2_p_barrel_shift_79_out_4), .B(mux_2_p_barrel_shift_88_out_4),
    .out_4(mux_2_p_barrel_shift_80_out_4), .C0(C3));
  MUX_2____P_barrel_shift mux_2_p_barrel_shift_81 (
    .A(mux_2_p_barrel_shift_80_out_4), .B(mux_2_p_barrel_shift_84_out_4), .out_4(OUT[16]), .C0(LSB));
  MUX_2____P_barrel_shift mux_2_p_barrel_shift_82 (
    .A(mux_2_p_barrel_shift_78_out_4), .B(mux_2_p_barrel_shift_118_out_4),
    .out_4(mux_2_p_barrel_shift_82_out_4), .C0(C1));
  MUX_2____P_barrel_shift mux_2_p_barrel_shift_83 (
    .A(mux_2_p_barrel_shift_82_out_4), .B(mux_2_p_barrel_shift_102_out_4),
    .out_4(mux_2_p_barrel_shift_83_out_4), .C0(C2));
  MUX_2____P_barrel_shift mux_2_p_barrel_shift_84 (
    .A(mux_2_p_barrel_shift_83_out_4), .B(mux_2_p_barrel_shift_92_out_4),
    .out_4(mux_2_p_barrel_shift_84_out_4), .C0(C3));
  MUX_2____P_barrel_shift mux_2_p_barrel_shift_85 (
    .A(mux_2_p_barrel_shift_84_out_4), .B(mux_2_p_barrel_shift_89_out_4), .out_4(OUT[15]), .C0(LSB));
  MUX_2____P_barrel_shift mux_2_p_barrel_shift_86 (
    .A(IN[14]), .B(1'b0), .out_4(mux_2_p_barrel_shift_86_out_4), .C0(MSB));
  MUX_2____P_barrel_shift mux_2_p_barrel_shift_87 (
    .A(mux_2_p_barrel_shift_86_out_4), .B(mux_2_p_barrel_shift_126_out_4),
    .out_4(mux_2_p_barrel_shift_87_out_4), .C0(C1));
  MUX_2____P_barrel_shift mux_2_p_barrel_shift_88 (
    .A(mux_2_p_barrel_shift_87_out_4), .B(mux_2_p_barrel_shift_107_out_4),
    .out_4(mux_2_p_barrel_shift_88_out_4), .C0(C2));
  MUX_2____P_barrel_shift mux_2_p_barrel_shift_89 (
    .A(mux_2_p_barrel_shift_88_out_4), .B(mux_2_p_barrel_shift_99_out_4),
    .out_4(mux_2_p_barrel_shift_89_out_4), .C0(C3));
  MUX_2____P_barrel_shift mux_2_p_barrel_shift_90 (
    .A(IN[13]), .B(1'b0), .out_4(mux_2_p_barrel_shift_90_out_4), .C0(MSB));
  MUX_2____P_barrel_shift mux_2_p_barrel_shift_91 (
    .A(mux_2_p_barrel_shift_90_out_4), .B(mux_2_p_barrel_shift_130_out_4),
    .out_4(mux_2_p_barrel_shift_91_out_4), .C0(C1));
  MUX_2____P_barrel_shift mux_2_p_barrel_shift_92 (
    .A(mux_2_p_barrel_shift_91_out_4), .B(mux_2_p_barrel_shift_111_out_4),
    .out_4(mux_2_p_barrel_shift_92_out_4), .C0(C2));
  MUX_2____P_barrel_shift mux_2_p_barrel_shift_93 (
    .A(mux_2_p_barrel_shift_89_out_4), .B(mux_2_p_barrel_shift_96_out_4), .out_4(OUT[14]), .C0(LSB));
  MUX_2____P_barrel_shift mux_2_p_barrel_shift_94 (
    .A(IN[12]), .B(1'b0), .out_4(mux_2_p_barrel_shift_94_out_4), .C0(MSB));
  MUX_2____P_barrel_shift mux_2_p_barrel_shift_95 (
    .A(mux_2_p_barrel_shift_94_out_4), .B(mux_2_p_barrel_shift_134_out_4),
    .out_4(mux_2_p_barrel_shift_95_out_4), .C0(C1));
  MUX_2____P_barrel_shift mux_2_p_barrel_shift_96 (
    .A(mux_2_p_barrel_shift_92_out_4), .B(mux_2_p_barrel_shift_103_out_4),
    .out_4(mux_2_p_barrel_shift_96_out_4), .C0(C3));
  MUX_2____P_barrel_shift mux_2_p_barrel_shift_97 (
    .A(mux_2_p_barrel_shift_96_out_4), .B(mux_2_p_barrel_shift_100_out_4), .out_4(OUT[13]), .C0(LSB));
  MUX_2____P_barrel_shift mux_2_p_barrel_shift_98 (
    .A(IN[11]), .B(1'b0), .out_4(mux_2_p_barrel_shift_98_out_4), .C0(MSB));
  MUX_2____P_barrel_shift mux_2_p_barrel_shift_99 (
    .A(mux_2_p_barrel_shift_95_out_4), .B(mux_2_p_barrel_shift_115_out_4),
    .out_4(mux_2_p_barrel_shift_99_out_4), .C0(C2));
  MUX_2____P_barrel_shift mux_2_p_barrel_shift_100 (
    .A(mux_2_p_barrel_shift_99_out_4), .B(mux_2_p_barrel_shift_108_out_4),
    .out_4(mux_2_p_barrel_shift_100_out_4), .C0(C3));
  MUX_2____P_barrel_shift mux_2_p_barrel_shift_101 (
    .A(mux_2_p_barrel_shift_100_out_4), .B(mux_2_p_barrel_shift_104_out_4), .out_4(OUT[12]), .C0(LSB));
  MUX_2____P_barrel_shift mux_2_p_barrel_shift_102 (
    .A(mux_2_p_barrel_shift_98_out_4), .B(mux_2_p_barrel_shift_138_out_4),
    .out_4(mux_2_p_barrel_shift_102_out_4), .C0(C1));
  MUX_2____P_barrel_shift mux_2_p_barrel_shift_103 (
    .A(mux_2_p_barrel_shift_102_out_4), .B(mux_2_p_barrel_shift_122_out_4),
    .out_4(mux_2_p_barrel_shift_103_out_4), .C0(C2));
  MUX_2____P_barrel_shift mux_2_p_barrel_shift_104 (
    .A(mux_2_p_barrel_shift_103_out_4), .B(mux_2_p_barrel_shift_112_out_4),
    .out_4(mux_2_p_barrel_shift_104_out_4), .C0(C3));
  MUX_2____P_barrel_shift mux_2_p_barrel_shift_105 (
    .A(mux_2_p_barrel_shift_104_out_4), .B(mux_2_p_barrel_shift_109_out_4), .out_4(OUT[11]), .C0(LSB));
  MUX_2____P_barrel_shift mux_2_p_barrel_shift_106 (
    .A(IN[10]), .B(1'b0), .out_4(mux_2_p_barrel_shift_106_out_4), .C0(MSB));
  MUX_2____P_barrel_shift mux_2_p_barrel_shift_107 (
    .A(mux_2_p_barrel_shift_106_out_4), .B(mux_2_p_barrel_shift_146_out_4),
    .out_4(mux_2_p_barrel_shift_107_out_4), .C0(C1));
  MUX_2____P_barrel_shift mux_2_p_barrel_shift_108 (
    .A(mux_2_p_barrel_shift_107_out_4), .B(mux_2_p_barrel_shift_127_out_4),
    .out_4(mux_2_p_barrel_shift_108_out_4), .C0(C2));
  MUX_2____P_barrel_shift mux_2_p_barrel_shift_109 (
    .A(mux_2_p_barrel_shift_108_out_4), .B(mux_2_p_barrel_shift_119_out_4),
    .out_4(mux_2_p_barrel_shift_109_out_4), .C0(C3));
  MUX_2____P_barrel_shift mux_2_p_barrel_shift_110 (
    .A(IN[9]), .B(1'b0), .out_4(mux_2_p_barrel_shift_110_out_4), .C0(MSB));
  MUX_2____P_barrel_shift mux_2_p_barrel_shift_111 (
    .A(mux_2_p_barrel_shift_110_out_4), .B(mux_2_p_barrel_shift_150_out_4),
    .out_4(mux_2_p_barrel_shift_111_out_4), .C0(C1));
  MUX_2____P_barrel_shift mux_2_p_barrel_shift_112 (
    .A(mux_2_p_barrel_shift_111_out_4), .B(mux_2_p_barrel_shift_131_out_4),
    .out_4(mux_2_p_barrel_shift_112_out_4), .C0(C2));
  MUX_2____P_barrel_shift mux_2_p_barrel_shift_113 (
    .A(mux_2_p_barrel_shift_109_out_4), .B(mux_2_p_barrel_shift_116_out_4), .out_4(OUT[10]), .C0(LSB));
  MUX_2____P_barrel_shift mux_2_p_barrel_shift_114 (
    .A(IN[8]), .B(1'b0), .out_4(mux_2_p_barrel_shift_114_out_4), .C0(MSB));
  MUX_2____P_barrel_shift mux_2_p_barrel_shift_115 (
    .A(mux_2_p_barrel_shift_114_out_4), .B(mux_2_p_barrel_shift_154_out_4),
    .out_4(mux_2_p_barrel_shift_115_out_4), .C0(C1));
  MUX_2____P_barrel_shift mux_2_p_barrel_shift_116 (
    .A(mux_2_p_barrel_shift_112_out_4), .B(mux_2_p_barrel_shift_123_out_4),
    .out_4(mux_2_p_barrel_shift_116_out_4), .C0(C3));
  MUX_2____P_barrel_shift mux_2_p_barrel_shift_117 (
    .A(mux_2_p_barrel_shift_116_out_4), .B(mux_2_p_barrel_shift_120_out_4), .out_4(OUT[9]), .C0(LSB));
  MUX_2____P_barrel_shift mux_2_p_barrel_shift_118 (
    .A(IN[7]), .B(1'b0), .out_4(mux_2_p_barrel_shift_118_out_4), .C0(MSB));
  MUX_2____P_barrel_shift mux_2_p_barrel_shift_119 (
    .A(mux_2_p_barrel_shift_115_out_4), .B(mux_2_p_barrel_shift_135_out_4),
    .out_4(mux_2_p_barrel_shift_119_out_4), .C0(C2));
  MUX_2____P_barrel_shift mux_2_p_barrel_shift_120 (
    .A(mux_2_p_barrel_shift_119_out_4), .B(mux_2_p_barrel_shift_128_out_4),
    .out_4(mux_2_p_barrel_shift_120_out_4), .C0(C3));
  MUX_2____P_barrel_shift mux_2_p_barrel_shift_121 (
    .A(mux_2_p_barrel_shift_120_out_4), .B(mux_2_p_barrel_shift_124_out_4), .out_4(OUT[8]), .C0(LSB));
  MUX_2____P_barrel_shift mux_2_p_barrel_shift_122 (
    .A(mux_2_p_barrel_shift_118_out_4), .B(1'b0), .out_4(mux_2_p_barrel_shift_122_out_4), .C0(C1));
  MUX_2____P_barrel_shift mux_2_p_barrel_shift_123 (
    .A(mux_2_p_barrel_shift_122_out_4), .B(mux_2_p_barrel_shift_142_out_4),
    .out_4(mux_2_p_barrel_shift_123_out_4), .C0(C2));
  MUX_2____P_barrel_shift mux_2_p_barrel_shift_124 (
    .A(mux_2_p_barrel_shift_123_out_4), .B(mux_2_p_barrel_shift_132_out_4),
    .out_4(mux_2_p_barrel_shift_124_out_4), .C0(C3));
  MUX_2____P_barrel_shift mux_2_p_barrel_shift_125 (
    .A(mux_2_p_barrel_shift_124_out_4), .B(mux_2_p_barrel_shift_129_out_4), .out_4(OUT[7]), .C0(LSB));
  MUX_2____P_barrel_shift mux_2_p_barrel_shift_126 (
    .A(IN[6]), .B(1'b0), .out_4(mux_2_p_barrel_shift_126_out_4), .C0(MSB));
  MUX_2____P_barrel_shift mux_2_p_barrel_shift_127 (
    .A(mux_2_p_barrel_shift_126_out_4), .B(1'b0), .out_4(mux_2_p_barrel_shift_127_out_4), .C0(C1));
  MUX_2____P_barrel_shift mux_2_p_barrel_shift_128 (
    .A(mux_2_p_barrel_shift_127_out_4), .B(mux_2_p_barrel_shift_147_out_4),
    .out_4(mux_2_p_barrel_shift_128_out_4), .C0(C2));
  MUX_2____P_barrel_shift mux_2_p_barrel_shift_129 (
    .A(mux_2_p_barrel_shift_128_out_4), .B(mux_2_p_barrel_shift_139_out_4),
    .out_4(mux_2_p_barrel_shift_129_out_4), .C0(C3));
  MUX_2____P_barrel_shift mux_2_p_barrel_shift_130 (
    .A(IN[5]), .B(1'b0), .out_4(mux_2_p_barrel_shift_130_out_4), .C0(MSB));
  MUX_2____P_barrel_shift mux_2_p_barrel_shift_131 (
    .A(mux_2_p_barrel_shift_130_out_4), .B(1'b0), .out_4(mux_2_p_barrel_shift_131_out_4), .C0(C1));
  MUX_2____P_barrel_shift mux_2_p_barrel_shift_132 (
    .A(mux_2_p_barrel_shift_131_out_4), .B(mux_2_p_barrel_shift_151_out_4),
    .out_4(mux_2_p_barrel_shift_132_out_4), .C0(C2));
  MUX_2____P_barrel_shift mux_2_p_barrel_shift_133 (
    .A(mux_2_p_barrel_shift_129_out_4), .B(mux_2_p_barrel_shift_136_out_4), .out_4(OUT[6]), .C0(LSB));
  MUX_2____P_barrel_shift mux_2_p_barrel_shift_134 (
    .A(IN[4]), .B(1'b0), .out_4(mux_2_p_barrel_shift_134_out_4), .C0(MSB));
  MUX_2____P_barrel_shift mux_2_p_barrel_shift_135 (
    .A(mux_2_p_barrel_shift_134_out_4), .B(1'b0), .out_4(mux_2_p_barrel_shift_135_out_4), .C0(C1));
  MUX_2____P_barrel_shift mux_2_p_barrel_shift_136 (
    .A(mux_2_p_barrel_shift_132_out_4), .B(mux_2_p_barrel_shift_143_out_4),
    .out_4(mux_2_p_barrel_shift_136_out_4), .C0(C3));
  MUX_2____P_barrel_shift mux_2_p_barrel_shift_137 (
    .A(mux_2_p_barrel_shift_136_out_4), .B(mux_2_p_barrel_shift_140_out_4), .out_4(OUT[5]), .C0(LSB));
  MUX_2____P_barrel_shift mux_2_p_barrel_shift_138 (
    .A(IN[3]), .B(1'b0), .out_4(mux_2_p_barrel_shift_138_out_4), .C0(MSB));
  MUX_2____P_barrel_shift mux_2_p_barrel_shift_139 (
    .A(mux_2_p_barrel_shift_135_out_4), .B(mux_2_p_barrel_shift_155_out_4),
    .out_4(mux_2_p_barrel_shift_139_out_4), .C0(C2));
  MUX_2____P_barrel_shift mux_2_p_barrel_shift_140 (
    .A(mux_2_p_barrel_shift_139_out_4), .B(mux_2_p_barrel_shift_148_out_4),
    .out_4(mux_2_p_barrel_shift_140_out_4), .C0(C3));
  MUX_2____P_barrel_shift mux_2_p_barrel_shift_141 (
    .A(mux_2_p_barrel_shift_140_out_4), .B(mux_2_p_barrel_shift_144_out_4), .out_4(OUT[4]), .C0(LSB));
  MUX_2____P_barrel_shift mux_2_p_barrel_shift_142 (
    .A(mux_2_p_barrel_shift_138_out_4), .B(1'b0), .out_4(mux_2_p_barrel_shift_142_out_4), .C0(C1));
  MUX_2____P_barrel_shift mux_2_p_barrel_shift_143 (
    .A(mux_2_p_barrel_shift_142_out_4), .B(1'b0), .out_4(mux_2_p_barrel_shift_143_out_4), .C0(C2));
  MUX_2____P_barrel_shift mux_2_p_barrel_shift_144 (
    .A(mux_2_p_barrel_shift_143_out_4), .B(mux_2_p_barrel_shift_152_out_4),
    .out_4(mux_2_p_barrel_shift_144_out_4), .C0(C3));
  MUX_2____P_barrel_shift mux_2_p_barrel_shift_145 (
    .A(mux_2_p_barrel_shift_144_out_4), .B(mux_2_p_barrel_shift_149_out_4), .out_4(OUT[3]), .C0(LSB));
  MUX_2____P_barrel_shift mux_2_p_barrel_shift_146 (
    .A(IN[2]), .B(1'b0), .out_4(mux_2_p_barrel_shift_146_out_4), .C0(MSB));
  MUX_2____P_barrel_shift mux_2_p_barrel_shift_147 (
    .A(mux_2_p_barrel_shift_146_out_4), .B(1'b0), .out_4(mux_2_p_barrel_shift_147_out_4), .C0(C1));
  MUX_2____P_barrel_shift mux_2_p_barrel_shift_148 (
    .A(mux_2_p_barrel_shift_147_out_4), .B(1'b0), .out_4(mux_2_p_barrel_shift_148_out_4), .C0(C2));
  MUX_2____P_barrel_shift mux_2_p_barrel_shift_149 (
    .A(mux_2_p_barrel_shift_148_out_4), .B(mux_2_p_barrel_shift_158_out_4),
    .out_4(mux_2_p_barrel_shift_149_out_4), .C0(C3));
  MUX_2____P_barrel_shift mux_2_p_barrel_shift_150 (
    .A(IN[1]), .B(1'b0), .out_4(mux_2_p_barrel_shift_150_out_4), .C0(MSB));
  MUX_2____P_barrel_shift mux_2_p_barrel_shift_151 (
    .A(mux_2_p_barrel_shift_150_out_4), .B(1'b0), .out_4(mux_2_p_barrel_shift_151_out_4), .C0(C1));
  MUX_2____P_barrel_shift mux_2_p_barrel_shift_152 (
    .A(mux_2_p_barrel_shift_151_out_4), .B(1'b0), .out_4(mux_2_p_barrel_shift_152_out_4), .C0(C2));
  MUX_2____P_barrel_shift mux_2_p_barrel_shift_153 (
    .A(mux_2_p_barrel_shift_149_out_4), .B(mux_2_p_barrel_shift_156_out_4), .out_4(OUT[2]), .C0(LSB));
  MUX_2____P_barrel_shift mux_2_p_barrel_shift_154 (
    .A(IN[0]), .B(1'b0), .out_4(mux_2_p_barrel_shift_154_out_4), .C0(MSB));
  MUX_2____P_barrel_shift mux_2_p_barrel_shift_155 (
    .A(mux_2_p_barrel_shift_154_out_4), .B(1'b0), .out_4(mux_2_p_barrel_shift_155_out_4), .C0(C1));
  MUX_2____P_barrel_shift mux_2_p_barrel_shift_156 (
    .A(mux_2_p_barrel_shift_152_out_4), .B(1'b0), .out_4(mux_2_p_barrel_shift_156_out_4), .C0(C3));
  MUX_2____P_barrel_shift mux_2_p_barrel_shift_157 (
    .A(mux_2_p_barrel_shift_156_out_4), .B(mux_2_p_barrel_shift_159_out_4), .out_4(OUT[1]), .C0(LSB));
  MUX_2____P_barrel_shift mux_2_p_barrel_shift_158 (
    .A(mux_2_p_barrel_shift_155_out_4), .B(1'b0), .out_4(mux_2_p_barrel_shift_158_out_4), .C0(C2));
  MUX_2____P_barrel_shift mux_2_p_barrel_shift_159 (
    .A(mux_2_p_barrel_shift_158_out_4), .B(1'b0), .out_4(mux_2_p_barrel_shift_159_out_4), .C0(C3));
  MUX_2____P_barrel_shift mux_2_p_barrel_shift_160 (
    .A(mux_2_p_barrel_shift_159_out_4), .B(1'b0), .out_4(OUT[0]), .C0(LSB));

  // Notes on the sheet:
  //   4
  //   2
  //   3
  //   2
  //   2
  //   2
  //   1
  //   2
  //   2
  //   0
endmodule

module Barrel_right_Shifter_32 (
  input  [31:0] IN,
  input  MSB,
  input  C1,
  input  C2,
  input  C3,
  input  LSB,
  output [31:0] OUT
);

  wire mux_2_p_barrel_shift_1_out_4, mux_2_p_barrel_shift_2_out_4, mux_2_p_barrel_shift_3_out_4,
       mux_2_p_barrel_shift_4_out_4, mux_2_p_barrel_shift_6_out_4, mux_2_p_barrel_shift_7_out_4,
       mux_2_p_barrel_shift_8_out_4, mux_2_p_barrel_shift_9_out_4, mux_2_p_barrel_shift_10_out_4,
       mux_2_p_barrel_shift_11_out_4, mux_2_p_barrel_shift_12_out_4, mux_2_p_barrel_shift_14_out_4,
       mux_2_p_barrel_shift_15_out_4, mux_2_p_barrel_shift_16_out_4, mux_2_p_barrel_shift_18_out_4,
       mux_2_p_barrel_shift_19_out_4, mux_2_p_barrel_shift_20_out_4, mux_2_p_barrel_shift_22_out_4,
       mux_2_p_barrel_shift_23_out_4, mux_2_p_barrel_shift_24_out_4, mux_2_p_barrel_shift_26_out_4,
       mux_2_p_barrel_shift_27_out_4, mux_2_p_barrel_shift_28_out_4, mux_2_p_barrel_shift_29_out_4,
       mux_2_p_barrel_shift_30_out_4, mux_2_p_barrel_shift_31_out_4, mux_2_p_barrel_shift_32_out_4,
       mux_2_p_barrel_shift_34_out_4, mux_2_p_barrel_shift_35_out_4, mux_2_p_barrel_shift_36_out_4,
       mux_2_p_barrel_shift_38_out_4, mux_2_p_barrel_shift_39_out_4, mux_2_p_barrel_shift_40_out_4,
       mux_2_p_barrel_shift_42_out_4, mux_2_p_barrel_shift_43_out_4, mux_2_p_barrel_shift_44_out_4,
       mux_2_p_barrel_shift_46_out_4, mux_2_p_barrel_shift_47_out_4, mux_2_p_barrel_shift_48_out_4,
       mux_2_p_barrel_shift_49_out_4, mux_2_p_barrel_shift_50_out_4, mux_2_p_barrel_shift_51_out_4,
       mux_2_p_barrel_shift_52_out_4, mux_2_p_barrel_shift_54_out_4, mux_2_p_barrel_shift_55_out_4,
       mux_2_p_barrel_shift_56_out_4, mux_2_p_barrel_shift_58_out_4, mux_2_p_barrel_shift_59_out_4,
       mux_2_p_barrel_shift_60_out_4, mux_2_p_barrel_shift_62_out_4, mux_2_p_barrel_shift_63_out_4,
       mux_2_p_barrel_shift_64_out_4, mux_2_p_barrel_shift_66_out_4, mux_2_p_barrel_shift_67_out_4,
       mux_2_p_barrel_shift_68_out_4, mux_2_p_barrel_shift_69_out_4, mux_2_p_barrel_shift_70_out_4,
       mux_2_p_barrel_shift_71_out_4, mux_2_p_barrel_shift_72_out_4, mux_2_p_barrel_shift_74_out_4,
       mux_2_p_barrel_shift_75_out_4, mux_2_p_barrel_shift_76_out_4, mux_2_p_barrel_shift_78_out_4,
       mux_2_p_barrel_shift_79_out_4, mux_2_p_barrel_shift_80_out_4, mux_2_p_barrel_shift_82_out_4,
       mux_2_p_barrel_shift_83_out_4, mux_2_p_barrel_shift_84_out_4, mux_2_p_barrel_shift_86_out_4,
       mux_2_p_barrel_shift_87_out_4, mux_2_p_barrel_shift_88_out_4, mux_2_p_barrel_shift_89_out_4,
       mux_2_p_barrel_shift_90_out_4, mux_2_p_barrel_shift_91_out_4, mux_2_p_barrel_shift_92_out_4,
       mux_2_p_barrel_shift_94_out_4, mux_2_p_barrel_shift_95_out_4, mux_2_p_barrel_shift_96_out_4,
       mux_2_p_barrel_shift_98_out_4, mux_2_p_barrel_shift_99_out_4, mux_2_p_barrel_shift_100_out_4,
       mux_2_p_barrel_shift_102_out_4, mux_2_p_barrel_shift_103_out_4, mux_2_p_barrel_shift_104_out_4,
       mux_2_p_barrel_shift_106_out_4, mux_2_p_barrel_shift_107_out_4, mux_2_p_barrel_shift_108_out_4,
       mux_2_p_barrel_shift_109_out_4, mux_2_p_barrel_shift_110_out_4, mux_2_p_barrel_shift_111_out_4,
       mux_2_p_barrel_shift_112_out_4, mux_2_p_barrel_shift_114_out_4, mux_2_p_barrel_shift_115_out_4,
       mux_2_p_barrel_shift_116_out_4, mux_2_p_barrel_shift_118_out_4, mux_2_p_barrel_shift_119_out_4,
       mux_2_p_barrel_shift_120_out_4, mux_2_p_barrel_shift_122_out_4, mux_2_p_barrel_shift_123_out_4,
       mux_2_p_barrel_shift_124_out_4, mux_2_p_barrel_shift_126_out_4, mux_2_p_barrel_shift_127_out_4,
       mux_2_p_barrel_shift_128_out_4, mux_2_p_barrel_shift_129_out_4, mux_2_p_barrel_shift_130_out_4,
       mux_2_p_barrel_shift_131_out_4, mux_2_p_barrel_shift_132_out_4, mux_2_p_barrel_shift_134_out_4,
       mux_2_p_barrel_shift_135_out_4, mux_2_p_barrel_shift_136_out_4, mux_2_p_barrel_shift_138_out_4,
       mux_2_p_barrel_shift_139_out_4, mux_2_p_barrel_shift_140_out_4, mux_2_p_barrel_shift_142_out_4,
       mux_2_p_barrel_shift_143_out_4, mux_2_p_barrel_shift_144_out_4, mux_2_p_barrel_shift_146_out_4,
       mux_2_p_barrel_shift_147_out_4, mux_2_p_barrel_shift_148_out_4, mux_2_p_barrel_shift_149_out_4,
       mux_2_p_barrel_shift_150_out_4, mux_2_p_barrel_shift_151_out_4, mux_2_p_barrel_shift_152_out_4,
       mux_2_p_barrel_shift_154_out_4, mux_2_p_barrel_shift_155_out_4, mux_2_p_barrel_shift_156_out_4,
       mux_2_p_barrel_shift_158_out_4, mux_2_p_barrel_shift_159_out_4;

  MUX_2____P_barrel_shift mux_2_p_barrel_shift_1 (.A(IN[31]), .B(1'b0), .out_4(mux_2_p_barrel_shift_1_out_4), .C0(MSB));
  MUX_2____P_barrel_shift mux_2_p_barrel_shift_2 (
    .A(mux_2_p_barrel_shift_1_out_4), .B(1'b0), .out_4(mux_2_p_barrel_shift_2_out_4), .C0(C1));
  MUX_2____P_barrel_shift mux_2_p_barrel_shift_3 (
    .A(mux_2_p_barrel_shift_2_out_4), .B(1'b0), .out_4(mux_2_p_barrel_shift_3_out_4), .C0(C2));
  MUX_2____P_barrel_shift mux_2_p_barrel_shift_4 (
    .A(mux_2_p_barrel_shift_3_out_4), .B(1'b0), .out_4(mux_2_p_barrel_shift_4_out_4), .C0(C3));
  MUX_2____P_barrel_shift mux_2_p_barrel_shift_5 (
    .A(mux_2_p_barrel_shift_4_out_4), .B(1'b0), .out_4(OUT[31]), .C0(LSB));
  MUX_2____P_barrel_shift mux_2_p_barrel_shift_6 (.A(IN[30]), .B(1'b0), .out_4(mux_2_p_barrel_shift_6_out_4), .C0(MSB));
  MUX_2____P_barrel_shift mux_2_p_barrel_shift_7 (
    .A(mux_2_p_barrel_shift_6_out_4), .B(1'b0), .out_4(mux_2_p_barrel_shift_7_out_4), .C0(C1));
  MUX_2____P_barrel_shift mux_2_p_barrel_shift_8 (
    .A(mux_2_p_barrel_shift_7_out_4), .B(1'b0), .out_4(mux_2_p_barrel_shift_8_out_4), .C0(C2));
  MUX_2____P_barrel_shift mux_2_p_barrel_shift_9 (
    .A(mux_2_p_barrel_shift_8_out_4), .B(1'b0), .out_4(mux_2_p_barrel_shift_9_out_4), .C0(C3));
  MUX_2____P_barrel_shift mux_2_p_barrel_shift_10 (
    .A(IN[29]), .B(1'b0), .out_4(mux_2_p_barrel_shift_10_out_4), .C0(MSB));
  MUX_2____P_barrel_shift mux_2_p_barrel_shift_11 (
    .A(mux_2_p_barrel_shift_10_out_4), .B(1'b0), .out_4(mux_2_p_barrel_shift_11_out_4), .C0(C1));
  MUX_2____P_barrel_shift mux_2_p_barrel_shift_12 (
    .A(mux_2_p_barrel_shift_11_out_4), .B(1'b0), .out_4(mux_2_p_barrel_shift_12_out_4), .C0(C2));
  MUX_2____P_barrel_shift mux_2_p_barrel_shift_13 (
    .A(mux_2_p_barrel_shift_9_out_4), .B(mux_2_p_barrel_shift_4_out_4), .out_4(OUT[30]), .C0(LSB));
  MUX_2____P_barrel_shift mux_2_p_barrel_shift_14 (
    .A(IN[28]), .B(1'b0), .out_4(mux_2_p_barrel_shift_14_out_4), .C0(MSB));
  MUX_2____P_barrel_shift mux_2_p_barrel_shift_15 (
    .A(mux_2_p_barrel_shift_14_out_4), .B(1'b0), .out_4(mux_2_p_barrel_shift_15_out_4), .C0(C1));
  MUX_2____P_barrel_shift mux_2_p_barrel_shift_16 (
    .A(mux_2_p_barrel_shift_12_out_4), .B(mux_2_p_barrel_shift_3_out_4),
    .out_4(mux_2_p_barrel_shift_16_out_4), .C0(C3));
  MUX_2____P_barrel_shift mux_2_p_barrel_shift_17 (
    .A(mux_2_p_barrel_shift_16_out_4), .B(mux_2_p_barrel_shift_9_out_4), .out_4(OUT[29]), .C0(LSB));
  MUX_2____P_barrel_shift mux_2_p_barrel_shift_18 (
    .A(IN[27]), .B(1'b0), .out_4(mux_2_p_barrel_shift_18_out_4), .C0(MSB));
  MUX_2____P_barrel_shift mux_2_p_barrel_shift_19 (
    .A(mux_2_p_barrel_shift_15_out_4), .B(1'b0), .out_4(mux_2_p_barrel_shift_19_out_4), .C0(C2));
  MUX_2____P_barrel_shift mux_2_p_barrel_shift_20 (
    .A(mux_2_p_barrel_shift_19_out_4), .B(mux_2_p_barrel_shift_8_out_4),
    .out_4(mux_2_p_barrel_shift_20_out_4), .C0(C3));
  MUX_2____P_barrel_shift mux_2_p_barrel_shift_21 (
    .A(mux_2_p_barrel_shift_20_out_4), .B(mux_2_p_barrel_shift_16_out_4), .out_4(OUT[28]), .C0(LSB));
  MUX_2____P_barrel_shift mux_2_p_barrel_shift_22 (
    .A(mux_2_p_barrel_shift_18_out_4), .B(1'b0), .out_4(mux_2_p_barrel_shift_22_out_4), .C0(C1));
  MUX_2____P_barrel_shift mux_2_p_barrel_shift_23 (
    .A(mux_2_p_barrel_shift_22_out_4), .B(mux_2_p_barrel_shift_2_out_4),
    .out_4(mux_2_p_barrel_shift_23_out_4), .C0(C2));
  MUX_2____P_barrel_shift mux_2_p_barrel_shift_24 (
    .A(mux_2_p_barrel_shift_23_out_4), .B(mux_2_p_barrel_shift_12_out_4),
    .out_4(mux_2_p_barrel_shift_24_out_4), .C0(C3));
  MUX_2____P_barrel_shift mux_2_p_barrel_shift_25 (
    .A(mux_2_p_barrel_shift_24_out_4), .B(mux_2_p_barrel_shift_20_out_4), .out_4(OUT[27]), .C0(LSB));
  MUX_2____P_barrel_shift mux_2_p_barrel_shift_26 (
    .A(IN[26]), .B(1'b0), .out_4(mux_2_p_barrel_shift_26_out_4), .C0(MSB));
  MUX_2____P_barrel_shift mux_2_p_barrel_shift_27 (
    .A(mux_2_p_barrel_shift_26_out_4), .B(1'b0), .out_4(mux_2_p_barrel_shift_27_out_4), .C0(C1));
  MUX_2____P_barrel_shift mux_2_p_barrel_shift_28 (
    .A(mux_2_p_barrel_shift_27_out_4), .B(mux_2_p_barrel_shift_7_out_4),
    .out_4(mux_2_p_barrel_shift_28_out_4), .C0(C2));
  MUX_2____P_barrel_shift mux_2_p_barrel_shift_29 (
    .A(mux_2_p_barrel_shift_28_out_4), .B(mux_2_p_barrel_shift_19_out_4),
    .out_4(mux_2_p_barrel_shift_29_out_4), .C0(C3));
  MUX_2____P_barrel_shift mux_2_p_barrel_shift_30 (
    .A(IN[25]), .B(1'b0), .out_4(mux_2_p_barrel_shift_30_out_4), .C0(MSB));
  MUX_2____P_barrel_shift mux_2_p_barrel_shift_31 (
    .A(mux_2_p_barrel_shift_30_out_4), .B(1'b0), .out_4(mux_2_p_barrel_shift_31_out_4), .C0(C1));
  MUX_2____P_barrel_shift mux_2_p_barrel_shift_32 (
    .A(mux_2_p_barrel_shift_31_out_4), .B(mux_2_p_barrel_shift_11_out_4),
    .out_4(mux_2_p_barrel_shift_32_out_4), .C0(C2));
  MUX_2____P_barrel_shift mux_2_p_barrel_shift_33 (
    .A(mux_2_p_barrel_shift_29_out_4), .B(mux_2_p_barrel_shift_24_out_4), .out_4(OUT[26]), .C0(LSB));
  MUX_2____P_barrel_shift mux_2_p_barrel_shift_34 (
    .A(IN[24]), .B(1'b0), .out_4(mux_2_p_barrel_shift_34_out_4), .C0(MSB));
  MUX_2____P_barrel_shift mux_2_p_barrel_shift_35 (
    .A(mux_2_p_barrel_shift_34_out_4), .B(1'b0), .out_4(mux_2_p_barrel_shift_35_out_4), .C0(C1));
  MUX_2____P_barrel_shift mux_2_p_barrel_shift_36 (
    .A(mux_2_p_barrel_shift_32_out_4), .B(mux_2_p_barrel_shift_23_out_4),
    .out_4(mux_2_p_barrel_shift_36_out_4), .C0(C3));
  MUX_2____P_barrel_shift mux_2_p_barrel_shift_37 (
    .A(mux_2_p_barrel_shift_36_out_4), .B(mux_2_p_barrel_shift_29_out_4), .out_4(OUT[25]), .C0(LSB));
  MUX_2____P_barrel_shift mux_2_p_barrel_shift_38 (
    .A(IN[23]), .B(1'b0), .out_4(mux_2_p_barrel_shift_38_out_4), .C0(MSB));
  MUX_2____P_barrel_shift mux_2_p_barrel_shift_39 (
    .A(mux_2_p_barrel_shift_35_out_4), .B(mux_2_p_barrel_shift_15_out_4),
    .out_4(mux_2_p_barrel_shift_39_out_4), .C0(C2));
  MUX_2____P_barrel_shift mux_2_p_barrel_shift_40 (
    .A(mux_2_p_barrel_shift_39_out_4), .B(mux_2_p_barrel_shift_28_out_4),
    .out_4(mux_2_p_barrel_shift_40_out_4), .C0(C3));
  MUX_2____P_barrel_shift mux_2_p_barrel_shift_41 (
    .A(mux_2_p_barrel_shift_40_out_4), .B(mux_2_p_barrel_shift_36_out_4), .out_4(OUT[24]), .C0(LSB));
  MUX_2____P_barrel_shift mux_2_p_barrel_shift_42 (
    .A(mux_2_p_barrel_shift_38_out_4), .B(mux_2_p_barrel_shift_1_out_4),
    .out_4(mux_2_p_barrel_shift_42_out_4), .C0(C1));
  MUX_2____P_barrel_shift mux_2_p_barrel_shift_43 (
    .A(mux_2_p_barrel_shift_42_out_4), .B(mux_2_p_barrel_shift_22_out_4),
    .out_4(mux_2_p_barrel_shift_43_out_4), .C0(C2));
  MUX_2____P_barrel_shift mux_2_p_barrel_shift_44 (
    .A(mux_2_p_barrel_shift_43_out_4), .B(mux_2_p_barrel_shift_32_out_4),
    .out_4(mux_2_p_barrel_shift_44_out_4), .C0(C3));
  MUX_2____P_barrel_shift mux_2_p_barrel_shift_45 (
    .A(mux_2_p_barrel_shift_44_out_4), .B(mux_2_p_barrel_shift_40_out_4), .out_4(OUT[23]), .C0(LSB));
  MUX_2____P_barrel_shift mux_2_p_barrel_shift_46 (
    .A(IN[22]), .B(1'b0), .out_4(mux_2_p_barrel_shift_46_out_4), .C0(MSB));
  MUX_2____P_barrel_shift mux_2_p_barrel_shift_47 (
    .A(mux_2_p_barrel_shift_46_out_4), .B(mux_2_p_barrel_shift_6_out_4),
    .out_4(mux_2_p_barrel_shift_47_out_4), .C0(C1));
  MUX_2____P_barrel_shift mux_2_p_barrel_shift_48 (
    .A(mux_2_p_barrel_shift_47_out_4), .B(mux_2_p_barrel_shift_27_out_4),
    .out_4(mux_2_p_barrel_shift_48_out_4), .C0(C2));
  MUX_2____P_barrel_shift mux_2_p_barrel_shift_49 (
    .A(mux_2_p_barrel_shift_48_out_4), .B(mux_2_p_barrel_shift_39_out_4),
    .out_4(mux_2_p_barrel_shift_49_out_4), .C0(C3));
  MUX_2____P_barrel_shift mux_2_p_barrel_shift_50 (
    .A(IN[21]), .B(1'b0), .out_4(mux_2_p_barrel_shift_50_out_4), .C0(MSB));
  MUX_2____P_barrel_shift mux_2_p_barrel_shift_51 (
    .A(mux_2_p_barrel_shift_50_out_4), .B(mux_2_p_barrel_shift_10_out_4),
    .out_4(mux_2_p_barrel_shift_51_out_4), .C0(C1));
  MUX_2____P_barrel_shift mux_2_p_barrel_shift_52 (
    .A(mux_2_p_barrel_shift_51_out_4), .B(mux_2_p_barrel_shift_31_out_4),
    .out_4(mux_2_p_barrel_shift_52_out_4), .C0(C2));
  MUX_2____P_barrel_shift mux_2_p_barrel_shift_53 (
    .A(mux_2_p_barrel_shift_49_out_4), .B(mux_2_p_barrel_shift_44_out_4), .out_4(OUT[22]), .C0(LSB));
  MUX_2____P_barrel_shift mux_2_p_barrel_shift_54 (
    .A(IN[20]), .B(1'b0), .out_4(mux_2_p_barrel_shift_54_out_4), .C0(MSB));
  MUX_2____P_barrel_shift mux_2_p_barrel_shift_55 (
    .A(mux_2_p_barrel_shift_54_out_4), .B(mux_2_p_barrel_shift_14_out_4),
    .out_4(mux_2_p_barrel_shift_55_out_4), .C0(C1));
  MUX_2____P_barrel_shift mux_2_p_barrel_shift_56 (
    .A(mux_2_p_barrel_shift_52_out_4), .B(mux_2_p_barrel_shift_43_out_4),
    .out_4(mux_2_p_barrel_shift_56_out_4), .C0(C3));
  MUX_2____P_barrel_shift mux_2_p_barrel_shift_57 (
    .A(mux_2_p_barrel_shift_56_out_4), .B(mux_2_p_barrel_shift_49_out_4), .out_4(OUT[21]), .C0(LSB));
  MUX_2____P_barrel_shift mux_2_p_barrel_shift_58 (
    .A(IN[19]), .B(1'b0), .out_4(mux_2_p_barrel_shift_58_out_4), .C0(MSB));
  MUX_2____P_barrel_shift mux_2_p_barrel_shift_59 (
    .A(mux_2_p_barrel_shift_55_out_4), .B(mux_2_p_barrel_shift_35_out_4),
    .out_4(mux_2_p_barrel_shift_59_out_4), .C0(C2));
  MUX_2____P_barrel_shift mux_2_p_barrel_shift_60 (
    .A(mux_2_p_barrel_shift_59_out_4), .B(mux_2_p_barrel_shift_48_out_4),
    .out_4(mux_2_p_barrel_shift_60_out_4), .C0(C3));
  MUX_2____P_barrel_shift mux_2_p_barrel_shift_61 (
    .A(mux_2_p_barrel_shift_60_out_4), .B(mux_2_p_barrel_shift_56_out_4), .out_4(OUT[20]), .C0(LSB));
  MUX_2____P_barrel_shift mux_2_p_barrel_shift_62 (
    .A(mux_2_p_barrel_shift_58_out_4), .B(mux_2_p_barrel_shift_18_out_4),
    .out_4(mux_2_p_barrel_shift_62_out_4), .C0(C1));
  MUX_2____P_barrel_shift mux_2_p_barrel_shift_63 (
    .A(mux_2_p_barrel_shift_62_out_4), .B(mux_2_p_barrel_shift_42_out_4),
    .out_4(mux_2_p_barrel_shift_63_out_4), .C0(C2));
  MUX_2____P_barrel_shift mux_2_p_barrel_shift_64 (
    .A(mux_2_p_barrel_shift_63_out_4), .B(mux_2_p_barrel_shift_52_out_4),
    .out_4(mux_2_p_barrel_shift_64_out_4), .C0(C3));
  MUX_2____P_barrel_shift mux_2_p_barrel_shift_65 (
    .A(mux_2_p_barrel_shift_64_out_4), .B(mux_2_p_barrel_shift_60_out_4), .out_4(OUT[19]), .C0(LSB));
  MUX_2____P_barrel_shift mux_2_p_barrel_shift_66 (
    .A(IN[18]), .B(1'b0), .out_4(mux_2_p_barrel_shift_66_out_4), .C0(MSB));
  MUX_2____P_barrel_shift mux_2_p_barrel_shift_67 (
    .A(mux_2_p_barrel_shift_66_out_4), .B(mux_2_p_barrel_shift_26_out_4),
    .out_4(mux_2_p_barrel_shift_67_out_4), .C0(C1));
  MUX_2____P_barrel_shift mux_2_p_barrel_shift_68 (
    .A(mux_2_p_barrel_shift_67_out_4), .B(mux_2_p_barrel_shift_47_out_4),
    .out_4(mux_2_p_barrel_shift_68_out_4), .C0(C2));
  MUX_2____P_barrel_shift mux_2_p_barrel_shift_69 (
    .A(mux_2_p_barrel_shift_68_out_4), .B(mux_2_p_barrel_shift_59_out_4),
    .out_4(mux_2_p_barrel_shift_69_out_4), .C0(C3));
  MUX_2____P_barrel_shift mux_2_p_barrel_shift_70 (
    .A(IN[17]), .B(1'b0), .out_4(mux_2_p_barrel_shift_70_out_4), .C0(MSB));
  MUX_2____P_barrel_shift mux_2_p_barrel_shift_71 (
    .A(mux_2_p_barrel_shift_70_out_4), .B(mux_2_p_barrel_shift_30_out_4),
    .out_4(mux_2_p_barrel_shift_71_out_4), .C0(C1));
  MUX_2____P_barrel_shift mux_2_p_barrel_shift_72 (
    .A(mux_2_p_barrel_shift_71_out_4), .B(mux_2_p_barrel_shift_51_out_4),
    .out_4(mux_2_p_barrel_shift_72_out_4), .C0(C2));
  MUX_2____P_barrel_shift mux_2_p_barrel_shift_73 (
    .A(mux_2_p_barrel_shift_69_out_4), .B(mux_2_p_barrel_shift_64_out_4), .out_4(OUT[18]), .C0(LSB));
  MUX_2____P_barrel_shift mux_2_p_barrel_shift_74 (
    .A(IN[16]), .B(1'b0), .out_4(mux_2_p_barrel_shift_74_out_4), .C0(MSB));
  MUX_2____P_barrel_shift mux_2_p_barrel_shift_75 (
    .A(mux_2_p_barrel_shift_74_out_4), .B(mux_2_p_barrel_shift_34_out_4),
    .out_4(mux_2_p_barrel_shift_75_out_4), .C0(C1));
  MUX_2____P_barrel_shift mux_2_p_barrel_shift_76 (
    .A(mux_2_p_barrel_shift_72_out_4), .B(mux_2_p_barrel_shift_63_out_4),
    .out_4(mux_2_p_barrel_shift_76_out_4), .C0(C3));
  MUX_2____P_barrel_shift mux_2_p_barrel_shift_77 (
    .A(mux_2_p_barrel_shift_76_out_4), .B(mux_2_p_barrel_shift_69_out_4), .out_4(OUT[17]), .C0(LSB));
  MUX_2____P_barrel_shift mux_2_p_barrel_shift_78 (
    .A(IN[15]), .B(IN[31]), .out_4(mux_2_p_barrel_shift_78_out_4), .C0(MSB));
  MUX_2____P_barrel_shift mux_2_p_barrel_shift_79 (
    .A(mux_2_p_barrel_shift_75_out_4), .B(mux_2_p_barrel_shift_55_out_4),
    .out_4(mux_2_p_barrel_shift_79_out_4), .C0(C2));
  MUX_2____P_barrel_shift mux_2_p_barrel_shift_80 (
    .A(mux_2_p_barrel_shift_79_out_4), .B(mux_2_p_barrel_shift_68_out_4),
    .out_4(mux_2_p_barrel_shift_80_out_4), .C0(C3));
  MUX_2____P_barrel_shift mux_2_p_barrel_shift_81 (
    .A(mux_2_p_barrel_shift_80_out_4), .B(mux_2_p_barrel_shift_76_out_4), .out_4(OUT[16]), .C0(LSB));
  MUX_2____P_barrel_shift mux_2_p_barrel_shift_82 (
    .A(mux_2_p_barrel_shift_78_out_4), .B(mux_2_p_barrel_shift_38_out_4),
    .out_4(mux_2_p_barrel_shift_82_out_4), .C0(C1));
  MUX_2____P_barrel_shift mux_2_p_barrel_shift_83 (
    .A(mux_2_p_barrel_shift_82_out_4), .B(mux_2_p_barrel_shift_62_out_4),
    .out_4(mux_2_p_barrel_shift_83_out_4), .C0(C2));
  MUX_2____P_barrel_shift mux_2_p_barrel_shift_84 (
    .A(mux_2_p_barrel_shift_83_out_4), .B(mux_2_p_barrel_shift_72_out_4),
    .out_4(mux_2_p_barrel_shift_84_out_4), .C0(C3));
  MUX_2____P_barrel_shift mux_2_p_barrel_shift_85 (
    .A(mux_2_p_barrel_shift_84_out_4), .B(mux_2_p_barrel_shift_80_out_4), .out_4(OUT[15]), .C0(LSB));
  MUX_2____P_barrel_shift mux_2_p_barrel_shift_86 (
    .A(IN[14]), .B(IN[30]), .out_4(mux_2_p_barrel_shift_86_out_4), .C0(MSB));
  MUX_2____P_barrel_shift mux_2_p_barrel_shift_87 (
    .A(mux_2_p_barrel_shift_86_out_4), .B(mux_2_p_barrel_shift_46_out_4),
    .out_4(mux_2_p_barrel_shift_87_out_4), .C0(C1));
  MUX_2____P_barrel_shift mux_2_p_barrel_shift_88 (
    .A(mux_2_p_barrel_shift_87_out_4), .B(mux_2_p_barrel_shift_67_out_4),
    .out_4(mux_2_p_barrel_shift_88_out_4), .C0(C2));
  MUX_2____P_barrel_shift mux_2_p_barrel_shift_89 (
    .A(mux_2_p_barrel_shift_88_out_4), .B(mux_2_p_barrel_shift_79_out_4),
    .out_4(mux_2_p_barrel_shift_89_out_4), .C0(C3));
  MUX_2____P_barrel_shift mux_2_p_barrel_shift_90 (
    .A(IN[13]), .B(IN[29]), .out_4(mux_2_p_barrel_shift_90_out_4), .C0(MSB));
  MUX_2____P_barrel_shift mux_2_p_barrel_shift_91 (
    .A(mux_2_p_barrel_shift_90_out_4), .B(mux_2_p_barrel_shift_50_out_4),
    .out_4(mux_2_p_barrel_shift_91_out_4), .C0(C1));
  MUX_2____P_barrel_shift mux_2_p_barrel_shift_92 (
    .A(mux_2_p_barrel_shift_91_out_4), .B(mux_2_p_barrel_shift_71_out_4),
    .out_4(mux_2_p_barrel_shift_92_out_4), .C0(C2));
  MUX_2____P_barrel_shift mux_2_p_barrel_shift_93 (
    .A(mux_2_p_barrel_shift_89_out_4), .B(mux_2_p_barrel_shift_84_out_4), .out_4(OUT[14]), .C0(LSB));
  MUX_2____P_barrel_shift mux_2_p_barrel_shift_94 (
    .A(IN[12]), .B(IN[28]), .out_4(mux_2_p_barrel_shift_94_out_4), .C0(MSB));
  MUX_2____P_barrel_shift mux_2_p_barrel_shift_95 (
    .A(mux_2_p_barrel_shift_94_out_4), .B(mux_2_p_barrel_shift_54_out_4),
    .out_4(mux_2_p_barrel_shift_95_out_4), .C0(C1));
  MUX_2____P_barrel_shift mux_2_p_barrel_shift_96 (
    .A(mux_2_p_barrel_shift_92_out_4), .B(mux_2_p_barrel_shift_83_out_4),
    .out_4(mux_2_p_barrel_shift_96_out_4), .C0(C3));
  MUX_2____P_barrel_shift mux_2_p_barrel_shift_97 (
    .A(mux_2_p_barrel_shift_96_out_4), .B(mux_2_p_barrel_shift_89_out_4), .out_4(OUT[13]), .C0(LSB));
  MUX_2____P_barrel_shift mux_2_p_barrel_shift_98 (
    .A(IN[11]), .B(IN[27]), .out_4(mux_2_p_barrel_shift_98_out_4), .C0(MSB));
  MUX_2____P_barrel_shift mux_2_p_barrel_shift_99 (
    .A(mux_2_p_barrel_shift_95_out_4), .B(mux_2_p_barrel_shift_75_out_4),
    .out_4(mux_2_p_barrel_shift_99_out_4), .C0(C2));
  MUX_2____P_barrel_shift mux_2_p_barrel_shift_100 (
    .A(mux_2_p_barrel_shift_99_out_4), .B(mux_2_p_barrel_shift_88_out_4),
    .out_4(mux_2_p_barrel_shift_100_out_4), .C0(C3));
  MUX_2____P_barrel_shift mux_2_p_barrel_shift_101 (
    .A(mux_2_p_barrel_shift_100_out_4), .B(mux_2_p_barrel_shift_96_out_4), .out_4(OUT[12]), .C0(LSB));
  MUX_2____P_barrel_shift mux_2_p_barrel_shift_102 (
    .A(mux_2_p_barrel_shift_98_out_4), .B(mux_2_p_barrel_shift_58_out_4),
    .out_4(mux_2_p_barrel_shift_102_out_4), .C0(C1));
  MUX_2____P_barrel_shift mux_2_p_barrel_shift_103 (
    .A(mux_2_p_barrel_shift_102_out_4), .B(mux_2_p_barrel_shift_82_out_4),
    .out_4(mux_2_p_barrel_shift_103_out_4), .C0(C2));
  MUX_2____P_barrel_shift mux_2_p_barrel_shift_104 (
    .A(mux_2_p_barrel_shift_103_out_4), .B(mux_2_p_barrel_shift_92_out_4),
    .out_4(mux_2_p_barrel_shift_104_out_4), .C0(C3));
  MUX_2____P_barrel_shift mux_2_p_barrel_shift_105 (
    .A(mux_2_p_barrel_shift_104_out_4), .B(mux_2_p_barrel_shift_100_out_4), .out_4(OUT[11]), .C0(LSB));
  MUX_2____P_barrel_shift mux_2_p_barrel_shift_106 (
    .A(IN[10]), .B(IN[26]), .out_4(mux_2_p_barrel_shift_106_out_4), .C0(MSB));
  MUX_2____P_barrel_shift mux_2_p_barrel_shift_107 (
    .A(mux_2_p_barrel_shift_106_out_4), .B(mux_2_p_barrel_shift_66_out_4),
    .out_4(mux_2_p_barrel_shift_107_out_4), .C0(C1));
  MUX_2____P_barrel_shift mux_2_p_barrel_shift_108 (
    .A(mux_2_p_barrel_shift_107_out_4), .B(mux_2_p_barrel_shift_87_out_4),
    .out_4(mux_2_p_barrel_shift_108_out_4), .C0(C2));
  MUX_2____P_barrel_shift mux_2_p_barrel_shift_109 (
    .A(mux_2_p_barrel_shift_108_out_4), .B(mux_2_p_barrel_shift_99_out_4),
    .out_4(mux_2_p_barrel_shift_109_out_4), .C0(C3));
  MUX_2____P_barrel_shift mux_2_p_barrel_shift_110 (
    .A(IN[9]), .B(IN[25]), .out_4(mux_2_p_barrel_shift_110_out_4), .C0(MSB));
  MUX_2____P_barrel_shift mux_2_p_barrel_shift_111 (
    .A(mux_2_p_barrel_shift_110_out_4), .B(mux_2_p_barrel_shift_70_out_4),
    .out_4(mux_2_p_barrel_shift_111_out_4), .C0(C1));
  MUX_2____P_barrel_shift mux_2_p_barrel_shift_112 (
    .A(mux_2_p_barrel_shift_111_out_4), .B(mux_2_p_barrel_shift_91_out_4),
    .out_4(mux_2_p_barrel_shift_112_out_4), .C0(C2));
  MUX_2____P_barrel_shift mux_2_p_barrel_shift_113 (
    .A(mux_2_p_barrel_shift_109_out_4), .B(mux_2_p_barrel_shift_104_out_4), .out_4(OUT[10]), .C0(LSB));
  MUX_2____P_barrel_shift mux_2_p_barrel_shift_114 (
    .A(IN[8]), .B(IN[24]), .out_4(mux_2_p_barrel_shift_114_out_4), .C0(MSB));
  MUX_2____P_barrel_shift mux_2_p_barrel_shift_115 (
    .A(mux_2_p_barrel_shift_114_out_4), .B(mux_2_p_barrel_shift_74_out_4),
    .out_4(mux_2_p_barrel_shift_115_out_4), .C0(C1));
  MUX_2____P_barrel_shift mux_2_p_barrel_shift_116 (
    .A(mux_2_p_barrel_shift_112_out_4), .B(mux_2_p_barrel_shift_103_out_4),
    .out_4(mux_2_p_barrel_shift_116_out_4), .C0(C3));
  MUX_2____P_barrel_shift mux_2_p_barrel_shift_117 (
    .A(mux_2_p_barrel_shift_116_out_4), .B(mux_2_p_barrel_shift_109_out_4), .out_4(OUT[9]), .C0(LSB));
  MUX_2____P_barrel_shift mux_2_p_barrel_shift_118 (
    .A(IN[23]), .B(IN[23]), .out_4(mux_2_p_barrel_shift_118_out_4), .C0(MSB));
  MUX_2____P_barrel_shift mux_2_p_barrel_shift_119 (
    .A(mux_2_p_barrel_shift_115_out_4), .B(mux_2_p_barrel_shift_95_out_4),
    .out_4(mux_2_p_barrel_shift_119_out_4), .C0(C2));
  MUX_2____P_barrel_shift mux_2_p_barrel_shift_120 (
    .A(mux_2_p_barrel_shift_119_out_4), .B(mux_2_p_barrel_shift_108_out_4),
    .out_4(mux_2_p_barrel_shift_120_out_4), .C0(C3));
  MUX_2____P_barrel_shift mux_2_p_barrel_shift_121 (
    .A(mux_2_p_barrel_shift_120_out_4), .B(mux_2_p_barrel_shift_116_out_4), .out_4(OUT[8]), .C0(LSB));
  MUX_2____P_barrel_shift mux_2_p_barrel_shift_122 (
    .A(mux_2_p_barrel_shift_118_out_4), .B(mux_2_p_barrel_shift_78_out_4),
    .out_4(mux_2_p_barrel_shift_122_out_4), .C0(C1));
  MUX_2____P_barrel_shift mux_2_p_barrel_shift_123 (
    .A(mux_2_p_barrel_shift_122_out_4), .B(mux_2_p_barrel_shift_102_out_4),
    .out_4(mux_2_p_barrel_shift_123_out_4), .C0(C2));
  MUX_2____P_barrel_shift mux_2_p_barrel_shift_124 (
    .A(mux_2_p_barrel_shift_123_out_4), .B(mux_2_p_barrel_shift_112_out_4),
    .out_4(mux_2_p_barrel_shift_124_out_4), .C0(C3));
  MUX_2____P_barrel_shift mux_2_p_barrel_shift_125 (
    .A(mux_2_p_barrel_shift_124_out_4), .B(mux_2_p_barrel_shift_120_out_4), .out_4(OUT[7]), .C0(LSB));
  MUX_2____P_barrel_shift mux_2_p_barrel_shift_126 (
    .A(IN[6]), .B(IN[22]), .out_4(mux_2_p_barrel_shift_126_out_4), .C0(MSB));
  MUX_2____P_barrel_shift mux_2_p_barrel_shift_127 (
    .A(mux_2_p_barrel_shift_126_out_4), .B(mux_2_p_barrel_shift_86_out_4),
    .out_4(mux_2_p_barrel_shift_127_out_4), .C0(C1));
  MUX_2____P_barrel_shift mux_2_p_barrel_shift_128 (
    .A(mux_2_p_barrel_shift_127_out_4), .B(mux_2_p_barrel_shift_107_out_4),
    .out_4(mux_2_p_barrel_shift_128_out_4), .C0(C2));
  MUX_2____P_barrel_shift mux_2_p_barrel_shift_129 (
    .A(mux_2_p_barrel_shift_128_out_4), .B(mux_2_p_barrel_shift_119_out_4),
    .out_4(mux_2_p_barrel_shift_129_out_4), .C0(C3));
  MUX_2____P_barrel_shift mux_2_p_barrel_shift_130 (
    .A(IN[5]), .B(IN[21]), .out_4(mux_2_p_barrel_shift_130_out_4), .C0(MSB));
  MUX_2____P_barrel_shift mux_2_p_barrel_shift_131 (
    .A(mux_2_p_barrel_shift_130_out_4), .B(mux_2_p_barrel_shift_90_out_4),
    .out_4(mux_2_p_barrel_shift_131_out_4), .C0(C1));
  MUX_2____P_barrel_shift mux_2_p_barrel_shift_132 (
    .A(mux_2_p_barrel_shift_131_out_4), .B(mux_2_p_barrel_shift_111_out_4),
    .out_4(mux_2_p_barrel_shift_132_out_4), .C0(C2));
  MUX_2____P_barrel_shift mux_2_p_barrel_shift_133 (
    .A(mux_2_p_barrel_shift_129_out_4), .B(mux_2_p_barrel_shift_124_out_4), .out_4(OUT[6]), .C0(LSB));
  MUX_2____P_barrel_shift mux_2_p_barrel_shift_134 (
    .A(IN[4]), .B(IN[20]), .out_4(mux_2_p_barrel_shift_134_out_4), .C0(MSB));
  MUX_2____P_barrel_shift mux_2_p_barrel_shift_135 (
    .A(mux_2_p_barrel_shift_134_out_4), .B(mux_2_p_barrel_shift_94_out_4),
    .out_4(mux_2_p_barrel_shift_135_out_4), .C0(C1));
  MUX_2____P_barrel_shift mux_2_p_barrel_shift_136 (
    .A(mux_2_p_barrel_shift_132_out_4), .B(mux_2_p_barrel_shift_123_out_4),
    .out_4(mux_2_p_barrel_shift_136_out_4), .C0(C3));
  MUX_2____P_barrel_shift mux_2_p_barrel_shift_137 (
    .A(mux_2_p_barrel_shift_136_out_4), .B(mux_2_p_barrel_shift_129_out_4), .out_4(OUT[5]), .C0(LSB));
  MUX_2____P_barrel_shift mux_2_p_barrel_shift_138 (
    .A(IN[3]), .B(IN[19]), .out_4(mux_2_p_barrel_shift_138_out_4), .C0(MSB));
  MUX_2____P_barrel_shift mux_2_p_barrel_shift_139 (
    .A(mux_2_p_barrel_shift_135_out_4), .B(mux_2_p_barrel_shift_115_out_4),
    .out_4(mux_2_p_barrel_shift_139_out_4), .C0(C2));
  MUX_2____P_barrel_shift mux_2_p_barrel_shift_140 (
    .A(mux_2_p_barrel_shift_139_out_4), .B(mux_2_p_barrel_shift_128_out_4),
    .out_4(mux_2_p_barrel_shift_140_out_4), .C0(C3));
  MUX_2____P_barrel_shift mux_2_p_barrel_shift_141 (
    .A(mux_2_p_barrel_shift_140_out_4), .B(mux_2_p_barrel_shift_136_out_4), .out_4(OUT[4]), .C0(LSB));
  MUX_2____P_barrel_shift mux_2_p_barrel_shift_142 (
    .A(mux_2_p_barrel_shift_138_out_4), .B(mux_2_p_barrel_shift_98_out_4),
    .out_4(mux_2_p_barrel_shift_142_out_4), .C0(C1));
  MUX_2____P_barrel_shift mux_2_p_barrel_shift_143 (
    .A(mux_2_p_barrel_shift_142_out_4), .B(mux_2_p_barrel_shift_122_out_4),
    .out_4(mux_2_p_barrel_shift_143_out_4), .C0(C2));
  MUX_2____P_barrel_shift mux_2_p_barrel_shift_144 (
    .A(mux_2_p_barrel_shift_143_out_4), .B(mux_2_p_barrel_shift_132_out_4),
    .out_4(mux_2_p_barrel_shift_144_out_4), .C0(C3));
  MUX_2____P_barrel_shift mux_2_p_barrel_shift_145 (
    .A(mux_2_p_barrel_shift_144_out_4), .B(mux_2_p_barrel_shift_140_out_4), .out_4(OUT[3]), .C0(LSB));
  MUX_2____P_barrel_shift mux_2_p_barrel_shift_146 (
    .A(IN[2]), .B(IN[18]), .out_4(mux_2_p_barrel_shift_146_out_4), .C0(MSB));
  MUX_2____P_barrel_shift mux_2_p_barrel_shift_147 (
    .A(mux_2_p_barrel_shift_146_out_4), .B(mux_2_p_barrel_shift_106_out_4),
    .out_4(mux_2_p_barrel_shift_147_out_4), .C0(C1));
  MUX_2____P_barrel_shift mux_2_p_barrel_shift_148 (
    .A(mux_2_p_barrel_shift_147_out_4), .B(mux_2_p_barrel_shift_127_out_4),
    .out_4(mux_2_p_barrel_shift_148_out_4), .C0(C2));
  MUX_2____P_barrel_shift mux_2_p_barrel_shift_149 (
    .A(mux_2_p_barrel_shift_148_out_4), .B(mux_2_p_barrel_shift_139_out_4),
    .out_4(mux_2_p_barrel_shift_149_out_4), .C0(C3));
  MUX_2____P_barrel_shift mux_2_p_barrel_shift_150 (
    .A(IN[1]), .B(IN[17]), .out_4(mux_2_p_barrel_shift_150_out_4), .C0(MSB));
  MUX_2____P_barrel_shift mux_2_p_barrel_shift_151 (
    .A(mux_2_p_barrel_shift_150_out_4), .B(mux_2_p_barrel_shift_110_out_4),
    .out_4(mux_2_p_barrel_shift_151_out_4), .C0(C1));
  MUX_2____P_barrel_shift mux_2_p_barrel_shift_152 (
    .A(mux_2_p_barrel_shift_151_out_4), .B(mux_2_p_barrel_shift_131_out_4),
    .out_4(mux_2_p_barrel_shift_152_out_4), .C0(C2));
  MUX_2____P_barrel_shift mux_2_p_barrel_shift_153 (
    .A(mux_2_p_barrel_shift_149_out_4), .B(mux_2_p_barrel_shift_144_out_4), .out_4(OUT[2]), .C0(LSB));
  MUX_2____P_barrel_shift mux_2_p_barrel_shift_154 (
    .A(IN[0]), .B(IN[16]), .out_4(mux_2_p_barrel_shift_154_out_4), .C0(MSB));
  MUX_2____P_barrel_shift mux_2_p_barrel_shift_155 (
    .A(mux_2_p_barrel_shift_154_out_4), .B(mux_2_p_barrel_shift_114_out_4),
    .out_4(mux_2_p_barrel_shift_155_out_4), .C0(C1));
  MUX_2____P_barrel_shift mux_2_p_barrel_shift_156 (
    .A(mux_2_p_barrel_shift_152_out_4), .B(mux_2_p_barrel_shift_143_out_4),
    .out_4(mux_2_p_barrel_shift_156_out_4), .C0(C3));
  MUX_2____P_barrel_shift mux_2_p_barrel_shift_157 (
    .A(mux_2_p_barrel_shift_156_out_4), .B(mux_2_p_barrel_shift_149_out_4), .out_4(OUT[1]), .C0(LSB));
  MUX_2____P_barrel_shift mux_2_p_barrel_shift_158 (
    .A(mux_2_p_barrel_shift_155_out_4), .B(mux_2_p_barrel_shift_135_out_4),
    .out_4(mux_2_p_barrel_shift_158_out_4), .C0(C2));
  MUX_2____P_barrel_shift mux_2_p_barrel_shift_159 (
    .A(mux_2_p_barrel_shift_158_out_4), .B(mux_2_p_barrel_shift_148_out_4),
    .out_4(mux_2_p_barrel_shift_159_out_4), .C0(C3));
  MUX_2____P_barrel_shift mux_2_p_barrel_shift_160 (
    .A(mux_2_p_barrel_shift_159_out_4), .B(mux_2_p_barrel_shift_156_out_4), .out_4(OUT[0]), .C0(LSB));

  assign IN[7] = IN[23];

  // Notes on the sheet:
  //   4
  //   2
  //   3
  //   2
  //   2
  //   2
  //   1
  //   2
  //   2
  //   0
endmodule

// Shifter
module Seletor_de_Shifter (
  input  [31:0] IN,
  input  [4:0] in_2,
  input  L_R,
  output [31:0] OUT
);

  wire [31:0] barrel_left_shifter_32_1_out, barrel_right_shifter_32_1_out;

  Barrel_right_Shifter_32 barrel_right_shifter_32_1 (
    .IN(IN), .OUT(barrel_right_shifter_32_1_out), .MSB(in_2[4]), .C1(in_2[3]), .C2(in_2[2]), .C3(in_2[1]),
    .LSB(in_2[0]));
  Barrel_left_Shifter_32 barrel_left_shifter_32_1 (
    .IN(IN), .OUT(barrel_left_shifter_32_1_out), .MSB(in_2[4]), .C1(in_2[3]), .C2(in_2[2]), .C3(in_2[1]),
    .LSB(in_2[0]));
  Multiplexer #(.width(32), .enable("false")) multiplexer_1 (
    .in0(barrel_right_shifter_32_1_out), .in1(barrel_left_shifter_32_1_out), .out(OUT), .sel(L_R));
endmodule

module Reg_32 (
  input  [31:0] DataIN,
  input  WR,
  input  Reset,
  output [31:0] RegData,
  output [31:0] out_5
);

  D_Flip_Flop _8 (.clk(WR), .D(DataIN[7]), .Q(RegData[7]), .reset(Reset));  // open: Qn, preset, en
  D_Flip_Flop _16 (.clk(WR), .D(DataIN[15]), .Q(RegData[15]), .reset(Reset));  // open: Qn, preset, en
  D_Flip_Flop _24 (.clk(WR), .D(DataIN[23]), .Q(RegData[23]), .en(Reset), .reset(Reset));  // open: Qn, preset
  D_Flip_Flop _32 (.clk(WR), .D(DataIN[31]), .Q(RegData[31]), .reset(Reset));  // open: Qn, preset, en
  D_Flip_Flop _7 (.clk(WR), .D(DataIN[6]), .Q(RegData[6]), .reset(Reset));  // open: Qn, preset, en
  D_Flip_Flop _15 (.clk(WR), .D(DataIN[14]), .Q(RegData[14]), .reset(Reset));  // open: Qn, preset, en
  D_Flip_Flop _23 (.clk(WR), .D(DataIN[22]), .Q(RegData[22]), .reset(Reset));  // open: Qn, preset, en
  D_Flip_Flop _31 (.clk(WR), .D(DataIN[30]), .Q(RegData[30]), .reset(Reset));  // open: Qn, preset, en
  D_Flip_Flop _6 (.clk(WR), .D(DataIN[5]), .Q(RegData[5]), .reset(Reset));  // open: Qn, preset, en
  D_Flip_Flop _14 (.clk(WR), .D(DataIN[13]), .Q(RegData[13]), .reset(Reset));  // open: Qn, preset, en
  D_Flip_Flop _22 (.clk(WR), .D(DataIN[21]), .Q(RegData[21]), .reset(Reset));  // open: Qn, preset, en
  D_Flip_Flop _30 (.clk(WR), .D(DataIN[29]), .Q(RegData[29]), .reset(Reset));  // open: Qn, preset, en
  D_Flip_Flop _5 (.clk(WR), .D(DataIN[4]), .Q(RegData[4]), .reset(Reset));  // open: Qn, preset, en
  D_Flip_Flop _13 (.clk(WR), .D(DataIN[12]), .Q(RegData[12]), .reset(Reset));  // open: Qn, preset, en
  D_Flip_Flop _21 (.clk(WR), .D(DataIN[20]), .Q(RegData[20]), .reset(Reset));  // open: Qn, preset, en
  D_Flip_Flop _29 (.clk(WR), .D(DataIN[28]), .Q(RegData[28]), .reset(Reset));  // open: Qn, preset, en
  D_Flip_Flop _4 (.clk(WR), .D(DataIN[3]), .Q(RegData[3]), .reset(Reset));  // open: Qn, preset, en
  D_Flip_Flop _12 (.clk(WR), .D(DataIN[11]), .Q(RegData[11]), .reset(Reset));  // open: Qn, preset, en
  D_Flip_Flop _20 (.clk(WR), .D(DataIN[19]), .Q(RegData[19]), .reset(Reset));  // open: Qn, preset, en
  D_Flip_Flop _28 (.clk(WR), .D(DataIN[27]), .Q(RegData[27]), .reset(Reset));  // open: Qn, preset, en
  D_Flip_Flop _3 (.clk(WR), .D(DataIN[2]), .Q(RegData[2]), .reset(Reset));  // open: Qn, preset, en
  D_Flip_Flop _11 (.clk(WR), .D(DataIN[10]), .Q(RegData[10]), .reset(Reset));  // open: Qn, preset, en
  D_Flip_Flop _19 (.clk(WR), .D(DataIN[18]), .Q(RegData[18]), .reset(Reset));  // open: Qn, preset, en
  D_Flip_Flop _27 (.clk(WR), .D(DataIN[26]), .Q(RegData[26]), .reset(Reset));  // open: Qn, preset, en
  D_Flip_Flop _2 (.clk(WR), .D(DataIN[1]), .Q(RegData[1]), .reset(Reset));  // open: Qn, preset, en
  D_Flip_Flop _10 (.clk(WR), .D(DataIN[9]), .Q(RegData[9]), .reset(Reset));  // open: Qn, preset, en
  D_Flip_Flop _18 (.clk(WR), .D(DataIN[17]), .Q(RegData[17]), .reset(Reset));  // open: Qn, preset, en
  D_Flip_Flop _26 (.clk(WR), .D(DataIN[25]), .Q(RegData[25]), .reset(Reset));  // open: Qn, preset, en
  D_Flip_Flop _1 (.clk(WR), .D(DataIN[0]), .Q(RegData[0]), .reset(Reset));  // open: Qn, preset, en
  D_Flip_Flop _9 (.clk(WR), .D(DataIN[8]), .Q(RegData[8]), .reset(Reset));  // open: Qn, preset, en
  D_Flip_Flop _17 (.clk(WR), .D(DataIN[16]), .Q(RegData[16]), .reset(Reset));  // open: Qn, preset, en
  D_Flip_Flop _25 (.clk(WR), .D(DataIN[24]), .Q(RegData[24]), .reset(Reset));  // open: Qn, preset, en

  assign out_5 = DataIN;
endmodule

module PROCESSADOR_32_BITS (
  input  [4:0] RegWR,
  input  [31:0] A,
  input  [4:0] DESLOCAMENTO,
  input  [4:0] RegWR_2,
  input  [31:0] B,
  input  in_6,
  input  [4:0] CONTROLADOR,
  output out_8,
  output [31:0] S,
  output out_10
);

  wire [31:0] regbank_1_a, regbank_2_a;

  RegBank regbank_1 (
    .WR(in_6), .RegWR(RegWR), .RegIN(A), .A(regbank_1_a), .DataRegXb(RegWR));  // open: DataRegXa, B, zero, zero_2, reset
  RegBank regbank_2 (
    .WR(in_6), .RegWR(RegWR_2), .RegIN(B), .A(regbank_2_a), .DataRegXb(RegWR_2));  // open: DataRegXa, B, zero, zero_2, reset
  Circuito_do_Processador_32bits circuito_do_processador_32bits_1 (
    .in_4(CONTROLADOR), .A(regbank_1_a), .B(regbank_2_a), .S(S), .out_6(out_8), .Deslocamento(DESLOCAMENTO),
    .vai1(out_10));

  // Notes on the sheet:
  //   00000 = or
  //   00001 == nand
  //   00010 == and
  //   00011 == xor
  //   00110 == SLL
  //   00100 == SLR
  //   00100 = somador
  //   10100 = somador
  //   01100 = subtração
  //   11100 = subtração
endmodule

module Demux_4_modif (
  input  in_1,
  input  in_2,
  output out_3,
  output out_4,
  output out_5,
  output out_6
);

  Demultiplexer #(.enable("false")) demultiplexer_1 (.out0(out_3), .out1(out_4), .in(in_1), .sel(in_2));
  Demultiplexer #(.enable("false")) demultiplexer_2 (.out0(out_5), .out1(out_6), .in(in_1), .sel(in_2));
endmodule

module RegBank (
  input  WR,
  input  [31:0] RegIN,
  input  [4:0] RegWR,
  input  reset,
  input  [4:0] DataRegXa,
  input  [4:0] DataRegXb,
  output zero,
  output [31:0] A,
  output [31:0] B,
  output zero_2
);

  wire demultiplexer_1_out0, demultiplexer_1_out1, demultiplexer_1_out2, demultiplexer_1_out3,
       demultiplexer_1_out4, demultiplexer_1_out5, demultiplexer_1_out6, demultiplexer_1_out7,
       demultiplexer_1_out8, demultiplexer_1_out9, demultiplexer_1_out10, demultiplexer_1_out11,
       demultiplexer_1_out12, demultiplexer_1_out13, demultiplexer_1_out14, demultiplexer_1_out15,
       demultiplexer_1_out16, demultiplexer_1_out17, demultiplexer_1_out18, demultiplexer_1_out19,
       demultiplexer_1_out20, demultiplexer_1_out21, demultiplexer_1_out22, demultiplexer_1_out23,
       demultiplexer_1_out24, demultiplexer_1_out25, demultiplexer_1_out26, demultiplexer_1_out27,
       demultiplexer_1_out28, demultiplexer_1_out29, demultiplexer_1_out30, demultiplexer_1_out31, or_1_out,
       or_2_out;
  wire [31:0] reg_32_1_out_5, reg_32_1_regdata, reg_32_2_out_5, reg_32_2_regdata, reg_32_3_out_5,
       reg_32_3_regdata, reg_32_4_out_5, reg_32_4_regdata, reg_32_5_out_5, reg_32_5_regdata, reg_32_6_out_5,
       reg_32_6_regdata, reg_32_7_out_5, reg_32_7_regdata, reg_32_8_out_5, reg_32_8_regdata, reg_32_9_out_5,
       reg_32_9_regdata, reg_32_10_out_5, reg_32_10_regdata, reg_32_11_out_5, reg_32_11_regdata,
       reg_32_12_out_5, reg_32_12_regdata, reg_32_13_out_5, reg_32_13_regdata, reg_32_14_out_5,
       reg_32_14_regdata, reg_32_15_out_5, reg_32_15_regdata, reg_32_16_out_5, reg_32_16_regdata,
       reg_32_17_out_5, reg_32_17_regdata, reg_32_18_out_5, reg_32_18_regdata, reg_32_19_out_5,
       reg_32_19_regdata, reg_32_20_out_5, reg_32_20_regdata, reg_32_21_out_5, reg_32_21_regdata,
       reg_32_22_out_5, reg_32_22_regdata, reg_32_23_out_5, reg_32_23_regdata, reg_32_24_out_5,
       reg_32_24_regdata, reg_32_25_out_5, reg_32_25_regdata, reg_32_26_out_5, reg_32_26_regdata,
       reg_32_27_out_5, reg_32_27_regdata, reg_32_28_out_5, reg_32_28_regdata, reg_32_29_out_5,
       reg_32_29_regdata, reg_32_30_out_5, reg_32_30_regdata, reg_32_31_out_5, reg_32_31_regdata,
       reg_32_32_regdata;

  Demultiplexer #(.select(5), .enable("false")) demultiplexer_1 (
    .out0(demultiplexer_1_out0), .out1(demultiplexer_1_out1), .out2(demultiplexer_1_out2),
    .out3(demultiplexer_1_out3), .out4(demultiplexer_1_out4), .out5(demultiplexer_1_out5),
    .out6(demultiplexer_1_out6), .out7(demultiplexer_1_out7), .out8(demultiplexer_1_out8),
    .out9(demultiplexer_1_out9), .out10(demultiplexer_1_out10), .out11(demultiplexer_1_out11),
    .out12(demultiplexer_1_out12), .out13(demultiplexer_1_out13), .out14(demultiplexer_1_out14),
    .out15(demultiplexer_1_out15), .out16(demultiplexer_1_out16), .out17(demultiplexer_1_out17),
    .out18(demultiplexer_1_out18), .out19(demultiplexer_1_out19), .out20(demultiplexer_1_out20),
    .out21(demultiplexer_1_out21), .out22(demultiplexer_1_out22), .out23(demultiplexer_1_out23),
    .out24(demultiplexer_1_out24), .out25(demultiplexer_1_out25), .out26(demultiplexer_1_out26),
    .out27(demultiplexer_1_out27), .out28(demultiplexer_1_out28), .out29(demultiplexer_1_out29),
    .out30(demultiplexer_1_out30), .out31(demultiplexer_1_out31), .in(WR), .sel(RegWR));
  Reg_32 reg_32_1 (
    .DataIN(RegIN), .WR(demultiplexer_1_out7), .out_5(reg_32_1_out_5), .RegData(reg_32_1_regdata),
    .Reset(reset));
  Reg_32 reg_32_2 (
    .DataIN(reg_32_29_out_5), .WR(demultiplexer_1_out15), .out_5(reg_32_2_out_5), .RegData(reg_32_2_regdata),
    .Reset(reset));
  Reg_32 reg_32_3 (
    .DataIN(reg_32_30_out_5), .WR(demultiplexer_1_out23), .out_5(reg_32_3_out_5), .RegData(reg_32_3_regdata),
    .Reset(reset));
  Reg_32 reg_32_4 (
    .DataIN(reg_32_31_out_5), .WR(demultiplexer_1_out31), .out_5(reg_32_4_out_5), .RegData(reg_32_4_regdata),
    .Reset(reset));
  Reg_32 reg_32_5 (
    .DataIN(reg_32_1_out_5), .WR(demultiplexer_1_out6), .out_5(reg_32_5_out_5), .RegData(reg_32_5_regdata),
    .Reset(reset));
  Reg_32 reg_32_6 (
    .DataIN(reg_32_2_out_5), .WR(demultiplexer_1_out14), .out_5(reg_32_6_out_5), .RegData(reg_32_6_regdata),
    .Reset(reset));
  Reg_32 reg_32_7 (
    .DataIN(reg_32_3_out_5), .WR(demultiplexer_1_out22), .out_5(reg_32_7_out_5), .RegData(reg_32_7_regdata),
    .Reset(reset));
  Reg_32 reg_32_8 (
    .DataIN(reg_32_4_out_5), .WR(demultiplexer_1_out30), .out_5(reg_32_8_out_5), .RegData(reg_32_8_regdata),
    .Reset(reset));
  Reg_32 reg_32_9 (
    .DataIN(reg_32_5_out_5), .WR(demultiplexer_1_out5), .out_5(reg_32_9_out_5), .RegData(reg_32_9_regdata),
    .Reset(reset));
  Reg_32 reg_32_10 (
    .DataIN(reg_32_6_out_5), .WR(demultiplexer_1_out13), .out_5(reg_32_10_out_5),
    .RegData(reg_32_10_regdata), .Reset(reset));
  Reg_32 reg_32_11 (
    .DataIN(reg_32_7_out_5), .WR(demultiplexer_1_out21), .out_5(reg_32_11_out_5),
    .RegData(reg_32_11_regdata), .Reset(reset));
  Reg_32 reg_32_12 (
    .DataIN(reg_32_8_out_5), .WR(demultiplexer_1_out29), .out_5(reg_32_12_out_5),
    .RegData(reg_32_12_regdata), .Reset(reset));
  Reg_32 reg_32_13 (
    .DataIN(reg_32_9_out_5), .WR(demultiplexer_1_out4), .out_5(reg_32_13_out_5), .RegData(reg_32_13_regdata),
    .Reset(reset));
  Reg_32 reg_32_14 (
    .DataIN(reg_32_10_out_5), .WR(demultiplexer_1_out12), .out_5(reg_32_14_out_5),
    .RegData(reg_32_14_regdata), .Reset(reset));
  Reg_32 reg_32_15 (
    .DataIN(reg_32_11_out_5), .WR(demultiplexer_1_out20), .out_5(reg_32_15_out_5),
    .RegData(reg_32_15_regdata), .Reset(reset));
  Reg_32 reg_32_16 (
    .DataIN(reg_32_12_out_5), .WR(demultiplexer_1_out28), .out_5(reg_32_16_out_5),
    .RegData(reg_32_16_regdata), .Reset(reset));
  Reg_32 reg_32_17 (
    .DataIN(reg_32_13_out_5), .WR(demultiplexer_1_out3), .out_5(reg_32_17_out_5),
    .RegData(reg_32_17_regdata), .Reset(reset));
  Reg_32 reg_32_18 (
    .DataIN(reg_32_14_out_5), .WR(demultiplexer_1_out11), .out_5(reg_32_18_out_5),
    .RegData(reg_32_18_regdata), .Reset(reset));
  Reg_32 reg_32_19 (
    .DataIN(reg_32_15_out_5), .WR(demultiplexer_1_out19), .out_5(reg_32_19_out_5),
    .RegData(reg_32_19_regdata), .Reset(reset));
  Reg_32 reg_32_20 (
    .DataIN(reg_32_16_out_5), .WR(demultiplexer_1_out27), .out_5(reg_32_20_out_5),
    .RegData(reg_32_20_regdata), .Reset(reset));
  Reg_32 reg_32_21 (
    .DataIN(reg_32_17_out_5), .WR(demultiplexer_1_out2), .out_5(reg_32_21_out_5),
    .RegData(reg_32_21_regdata), .Reset(reset));
  Reg_32 reg_32_22 (
    .DataIN(reg_32_18_out_5), .WR(demultiplexer_1_out10), .out_5(reg_32_22_out_5),
    .RegData(reg_32_22_regdata), .Reset(reset));
  Reg_32 reg_32_23 (
    .DataIN(reg_32_19_out_5), .WR(demultiplexer_1_out18), .out_5(reg_32_23_out_5),
    .RegData(reg_32_23_regdata), .Reset(reset));
  Reg_32 reg_32_24 (
    .DataIN(reg_32_20_out_5), .WR(demultiplexer_1_out26), .out_5(reg_32_24_out_5),
    .RegData(reg_32_24_regdata), .Reset(reset));
  or or_1 (or_1_out, A[0], A[1], A[2], A[3], A[4], A[5], A[6], A[7], A[8], A[9], A[10], A[11], A[12], A[13], A[14], A[15], A[17], A[18], A[19], A[20], A[21], A[22], A[23], A[24], A[25], A[26], A[27], A[28], A[29], A[30], A[31], A[16]);
  Reg_32 reg_32_25 (
    .DataIN(reg_32_21_out_5), .WR(demultiplexer_1_out1), .out_5(reg_32_25_out_5),
    .RegData(reg_32_25_regdata), .Reset(reset));
  Reg_32 reg_32_26 (
    .DataIN(reg_32_22_out_5), .WR(demultiplexer_1_out9), .out_5(reg_32_26_out_5),
    .RegData(reg_32_26_regdata), .Reset(reset));
  Reg_32 reg_32_27 (
    .DataIN(reg_32_23_out_5), .WR(demultiplexer_1_out17), .out_5(reg_32_27_out_5),
    .RegData(reg_32_27_regdata), .Reset(reset));
  Reg_32 reg_32_28 (
    .DataIN(reg_32_24_out_5), .WR(demultiplexer_1_out25), .out_5(reg_32_28_out_5),
    .RegData(reg_32_28_regdata), .Reset(reset));
  not not_1 (zero, or_1_out);
  Reg_32 reg_32_29 (
    .DataIN(reg_32_25_out_5), .WR(demultiplexer_1_out0), .out_5(reg_32_29_out_5),
    .RegData(reg_32_29_regdata), .Reset(reset));
  Reg_32 reg_32_30 (
    .DataIN(reg_32_26_out_5), .WR(demultiplexer_1_out8), .out_5(reg_32_30_out_5),
    .RegData(reg_32_30_regdata), .Reset(reset));
  Reg_32 reg_32_31 (
    .DataIN(reg_32_27_out_5), .WR(demultiplexer_1_out16), .out_5(reg_32_31_out_5),
    .RegData(reg_32_31_regdata), .Reset(reset));
  Reg_32 reg_32_32 (
    .DataIN(reg_32_28_out_5), .WR(demultiplexer_1_out24), .RegData(reg_32_32_regdata), .Reset(reset));  // open: out_5
  Multiplexer #(.select(5), .width(32), .enable("false")) multiplexer_1 (
    .in0(reg_32_4_regdata), .in1(reg_32_8_regdata), .in2(reg_32_12_regdata), .in3(reg_32_16_regdata),
    .in4(reg_32_20_regdata), .in5(reg_32_24_regdata), .in6(reg_32_28_regdata), .in7(reg_32_32_regdata),
    .in8(reg_32_3_regdata), .in9(reg_32_7_regdata), .in10(reg_32_11_regdata), .in11(reg_32_15_regdata),
    .in12(reg_32_19_regdata), .in13(reg_32_23_regdata), .in14(reg_32_27_regdata), .in15(reg_32_31_regdata),
    .in16(reg_32_2_regdata), .in17(reg_32_6_regdata), .in18(reg_32_10_regdata), .in19(reg_32_14_regdata),
    .in20(reg_32_18_regdata), .in21(reg_32_22_regdata), .in22(reg_32_26_regdata), .in23(reg_32_30_regdata),
    .in24(reg_32_1_regdata), .in25(reg_32_5_regdata), .in26(reg_32_9_regdata), .in27(reg_32_13_regdata),
    .in28(reg_32_17_regdata), .in29(reg_32_21_regdata), .in30(reg_32_25_regdata), .in31(reg_32_29_regdata),
    .out(A), .sel(DataRegXa));
  Multiplexer #(.select(5), .width(32), .enable("false")) multiplexer_2 (
    .in0(reg_32_4_regdata), .in1(reg_32_8_regdata), .in2(reg_32_12_regdata), .in3(reg_32_16_regdata),
    .in4(reg_32_20_regdata), .in5(reg_32_24_regdata), .in6(reg_32_28_regdata), .in7(reg_32_32_regdata),
    .in8(reg_32_3_regdata), .in9(reg_32_7_regdata), .in10(reg_32_11_regdata), .in11(reg_32_15_regdata),
    .in12(reg_32_19_regdata), .in13(reg_32_23_regdata), .in14(reg_32_27_regdata), .in15(reg_32_31_regdata),
    .in16(reg_32_2_regdata), .in17(reg_32_6_regdata), .in18(reg_32_10_regdata), .in19(reg_32_14_regdata),
    .in20(reg_32_18_regdata), .in21(reg_32_22_regdata), .in22(reg_32_26_regdata), .in23(reg_32_30_regdata),
    .in24(reg_32_1_regdata), .in25(reg_32_5_regdata), .in26(reg_32_9_regdata), .in27(reg_32_13_regdata),
    .in28(reg_32_17_regdata), .in29(reg_32_21_regdata), .in30(reg_32_25_regdata), .in31(reg_32_29_regdata),
    .out(B), .sel(DataRegXb));
  not not_2 (zero_2, or_2_out);
  or or_2 (or_2_out, B[0], B[1], B[2], B[3], B[4], B[5], B[6], B[7], B[8], B[9], B[10], B[11], B[12], B[13], B[14], B[15], B[17], B[18], B[19], B[20], B[21], B[22], B[23], B[24], B[25], B[26], B[27], B[28], B[29], B[30], B[31], B[16]);
endmodule

// PROCESSADOR
module Ula_simples (
  input  [31:0] A,
  input  [31:0] B,
  input  [4:0] Controlador,
  output out_4,
  output [31:0] S,
  output OVERFLOW_N
);

  wire or_2_out;
  wire [31:0] adder_1_out, and_1_out, nand_1_out, not_1_out, or_1_out;

  assign and_1_out = A & B;  // AND_Gate and_1, 32 bits wide
  assign or_1_out = A | B;  // OR_Gate or_1, 32 bits wide
  assign not_1_out = ~A;  // NOT_Gate not_1, 32 bits wide
  Adder #(.width(32)) adder_1 (.a(A), .b(B), .out(adder_1_out), .cout(OVERFLOW_N));  // open: cin
  assign nand_1_out = ~(~A & B);  // NAND_Gate nand_1, 32 bits wide
  Multiplexer #(.select(5), .width(32), .enable("false")) multiplexer_1 (
    .in0(and_1_out), .in1(or_1_out), .in2(not_1_out), .in3(adder_1_out), .in31(nand_1_out), .out(S),
    .sel(Controlador));  // open: in4, in5, in6, in7, in8, in9, in10, in11, in12, in13, in14, in15, in16, in17, in18, in19, in20, in21, in22, in23, in24, in25, in26, in27, in28, in29, in30
  or or_2 (or_2_out, S[0], S[1], S[2], S[3], S[4], S[5], S[6], S[7], S[8], S[9], S[10], S[11], S[12], S[13], S[14], S[15], S[17], S[18], S[19], S[20], S[21], S[22], S[23], S[24], S[25], S[26], S[27], S[28], S[29], S[30], S[31], S[16]);
  not not_2 (out_4, or_2_out);
endmodule

module Processador_Simples (
  input  [31:0] A,
  input  [31:0] B,
  input  [4:0] CONTROLADOR,
  output ZERO,
  output [31:0] S,
  output OVERFLOW_N
);

  Ula_simples ula_simples_1 (.S(S), .A(B), .B(A), .Controlador(CONTROLADOR), .OVERFLOW_N(OVERFLOW_N), .out_4(ZERO));

  // Notes on the sheet:
  //   OPCODES:
  //   AND > 00000
  //   OR > 00001 
  //   NOT A > 00010
  //   SUM A + B > 00011
endmodule

module ViaDeDados (
  input  CLock,
  input  reset,
  output [31:0] out_3
);

  wire not_1_out;
  wire [7:0] adder_1_out, register_1_q;
  wire [31:0] circuito_do_processador_32bits_1_s, exit_1_s, multiplexer_1_out, regbank_1_a, regbank_1_b;

  Adder adder_1 (.a(register_1_q), .b(8'h1), .out(adder_1_out), .cin(1'b0));  // open: cout
  Register register_1 (.D(adder_1_out), .Q(register_1_q), .clk(not_1_out), .clr(reset));  // open: en
  RAM #(.dataWidth(32)) ram_1 (.addr(register_1_q), .data(out_3));  // open: sel, clk, ld, clr
  Circuito_do_Processador_32bits circuito_do_processador_32bits_1 (
    .in_4(out_3[31:27]), .A(regbank_1_a), .B(multiplexer_1_out), .S(circuito_do_processador_32bits_1_s));  // open: out_6, Deslocamento, vai1
  not not_1 (not_1_out, CLock);
  Multiplexer #(.width(32), .enable("false")) multiplexer_1 (
    .in0(regbank_1_b), .in1(exit_1_s), .out(multiplexer_1_out), .sel(out_3[0]));
  exit exit_1 (.I(out_3[11:1]), .S(exit_1_s));
  RegBank regbank_1 (
    .WR(CLock), .RegWR(out_3[26:22]), .DataRegXa(out_3[21:17]), .RegIN(circuito_do_processador_32bits_1_s),
    .A(regbank_1_a), .DataRegXb(out_3[16:12]), .B(regbank_1_b), .reset(reset));  // open: zero, zero_2
endmodule

module exit (
  input  [10:0] I,
  output [31:0] S
);


  assign S = {{22{I[10]}}, I[9:0]};
endmodule
