// Logisim project Projeto Processador 32bits.circ as structural Verilog: 11 circuits, main circuit mux2
module mux2 (
  input  I0,
  input  I1,
  input  sel0,
  output out_4
);

  wire and_1_out, and_2_out;

  and and_1 (and_1_out, I0, ~sel0);  // AND_Gate
  and and_2 (and_2_out, I1, sel0);
  or or_1 (out_4, and_1_out, and_2_out);
endmodule

module mux_2_P_barrel_shift (
  input  [31:0] I0,
  input  [31:0] I1,
  input  in_3,
  output [31:0] out_4
);

  wire [31:0] and_1_out, and_2_out;

  assign and_1_out = I0 & ~{32{in_3}};  // AND_Gate and_1, 32 bits wide
  assign and_2_out = I1 & {32{in_3}};  // AND_Gate and_2, 32 bits wide
  assign out_4 = and_1_out | and_2_out;  // OR_Gate or_1, 32 bits wide
endmodule

module mux4 (
  input  I0,
  input  I1,
  input  I2,
  input  I3,
  input  sel1,
  input  sel0,
  output out_7
);

  wire mux2_1_out_4, mux2_2_out_4;

  mux2 mux2_1 (.I0(I0), .I1(I1), .sel0(sel0), .out_4(mux2_1_out_4));
  mux2 mux2_2 (.I0(I2), .I1(I3), .sel0(sel0), .out_4(mux2_2_out_4));
  mux2 mux2_3 (.I0(mux2_1_out_4), .I1(mux2_2_out_4), .sel0(sel1), .out_4(out_7));
endmodule

module mux8 (
  input  I0,
  input  I1,
  input  I2,
  input  I3,
  input  I4,
  input  I5,
  input  I6,
  input  I7,
  input  sel2,
  input  sel1,
  input  sel0,
  output out_12
);

  wire mux4_1_out_7, mux4_2_out_7;

  mux4 mux4_1 (.I0(I0), .I1(I1), .I2(I2), .I3(I3), .sel1(sel1), .sel0(sel0), .out_7(mux4_1_out_7));
  mux4 mux4_2 (.I0(I4), .I1(I5), .I2(I6), .I3(I7), .sel1(sel1), .sel0(sel0), .out_7(mux4_2_out_7));
  mux2 mux2_1 (.I0(mux4_1_out_7), .I1(mux4_2_out_7), .sel0(sel2), .out_4(out_12));
endmodule

module mux16 (
  input  I0,
  input  I1,
  input  I2,
  input  I3,
  input  I4,
  input  I5,
  input  I6,
  input  I7,
  input  I8,
  input  I9,
  input  I10,
  input  I11,
  input  I12,
  input  I13,
  input  I14,
  input  I15,
  input  sel3,
  input  sel2,
  input  sel1,
  input  sel0,
  output out_21
);

  wire mux8_1_out_12, mux8_2_out_12;

  mux8 mux8_1 (
    .I0(I0), .I1(I1), .I2(I2), .I3(I3), .I4(I4), .I5(I5), .I6(I6), .I7(I7), .sel2(sel2), .sel1(sel1),
    .sel0(sel0), .out_12(mux8_1_out_12));
  mux8 mux8_2 (
    .I0(I8), .I1(I9), .I2(I10), .I3(I11), .I4(I12), .I5(I13), .I6(I14), .I7(I15), .sel2(sel2), .sel1(sel1),
    .sel0(sel0), .out_12(mux8_2_out_12));
  mux2 mux2_1 (.I0(mux8_1_out_12), .I1(mux8_2_out_12), .sel0(sel3), .out_4(out_21));
endmodule

// MUX 32
module MUX32 (
  input  I0,
  input  I1,
  input  I2,
  input  I3,
  input  I4,
  input  I5,
  input  I6,
  input  I7,
  input  I8,
  input  I9,
  input  I10,
  input  I11,
  input  I12,
  input  I13,
  input  I14,
  input  I15,
  input  I16,
  input  I17,
  input  I18,
  input  I19,
  input  I20,
  input  I21,
  input  I22,
  input  I23,
  input  I24,
  input  I25,
  input  I26,
  input  I27,
  input  I28,
  input  I29,
  input  I30,
  input  I31,
  input  sel4,
  input  sel3,
  input  sel2,
  input  sel1,
  input  sel0,
  output out_38
);

  wire mux16_1_out_21, mux16_2_out_21;

  mux16 mux16_1 (
    .I0(I0), .I1(I1), .I2(I2), .I3(I3), .I4(I4), .I5(I5), .I6(I6), .I7(I7), .I8(I8), .I9(I9), .I10(I10),
    .I11(I11), .I12(I12), .I13(I13), .I14(I14), .I15(I15), .sel3(sel3), .sel2(sel2), .sel1(sel1),
    .sel0(sel0), .out_21(mux16_1_out_21));
  mux16 mux16_2 (
    .I0(I16), .I1(I17), .I2(I18), .I3(I19), .I4(I20), .I5(I21), .I6(I22), .I7(I23), .I8(I24), .I9(I25),
    .I10(I26), .I11(I27), .I12(I28), .I13(I29), .I14(I30), .I15(I31), .sel3(sel3), .sel2(sel2), .sel1(sel1),
    .sel0(sel0), .out_21(mux16_2_out_21));
  mux2 mux2_1 (.I0(mux16_1_out_21), .I1(mux16_2_out_21), .sel0(sel4), .out_4(out_38));
endmodule

// MUX 32
module mux_32_P_barrel_shift (
  input  I0,
  input  I1,
  input  I2,
  input  I3,
  input  I4,
  input  I5,
  input  I6,
  input  I7,
  input  I8,
  input  I9,
  input  I10,
  input  I11,
  input  I12,
  input  I13,
  input  I14,
  input  I15,
  input  I16,
  input  I17,
  input  I18,
  input  I19,
  input  I20,
  input  I21,
  input  I22,
  input  I23,
  input  I24,
  input  I25,
  input  I26,
  input  I27,
  input  I28,
  input  I29,
  input  I30,
  input  I31,
  input  [4:0] in_33,
  output out_34
);

  wire mux16_1_out_21, mux16_2_out_21;

  mux16 mux16_1 (
    .I0(I0), .I1(I1), .I2(I2), .I3(I3), .I4(I4), .I5(I5), .I6(I6), .I7(I7), .I8(I8), .I9(I9), .I10(I10),
    .I11(I11), .I12(I12), .I13(I13), .I14(I14), .I15(I15), .sel3(in_33[3]), .sel2(in_33[2]), .sel1(in_33[1]),
    .sel0(in_33[0]), .out_21(mux16_1_out_21));
  mux16 mux16_2 (
    .I0(I16), .I1(I17), .I2(I18), .I3(I19), .I4(I20), .I5(I21), .I6(I22), .I7(I23), .I8(I24), .I9(I25),
    .I10(I26), .I11(I27), .I12(I28), .I13(I29), .I14(I30), .I15(I31), .sel3(in_33[3]), .sel2(in_33[2]),
    .sel1(in_33[1]), .sel0(in_33[0]), .out_21(mux16_2_out_21));
  mux2 mux2_1 (.I0(mux16_1_out_21), .I1(mux16_2_out_21), .sel0(in_33[4]), .out_4(out_34));
endmodule

module mux64 (
  input  in_1,
  input  in_2,
  input  in_3,
  input  in_4,
  input  in_5,
  input  in_6,
  input  in_7,
  input  in_8,
  input  in_9,
  input  in_10,
  input  in_11,
  input  in_12,
  input  in_13,
  input  in_14,
  input  in_15,
  input  in_16,
  input  in_17,
  input  in_18,
  input  in_19,
  input  in_20,
  input  in_21,
  input  in_22,
  input  in_23,
  input  in_24,
  input  in_25,
  input  in_26,
  input  in_27,
  input  in_28,
  input  in_29,
  input  in_30,
  input  in_31,
  input  in_32,
  input  in_33,
  input  in_34,
  input  in_35,
  input  in_36,
  input  in_37,
  input  in_38,
  input  in_39,
  input  in_40,
  input  in_41,
  input  in_42,
  input  in_43,
  input  in_44,
  input  in_45,
  input  in_46,
  input  in_47,
  input  in_48,
  input  in_49,
  input  in_50,
  input  in_51,
  input  in_52,
  input  in_53,
  input  in_54,
  input  in_55,
  input  in_56,
  input  in_57,
  input  in_58,
  input  in_59,
  input  in_60,
  input  in_61,
  input  in_62,
  input  in_63,
  input  in_64,
  input  in_65,
  input  in_66,
  input  in_67,
  input  in_68,
  input  in_69,
  input  in_70,
  output out_71
);

  wire mux32_1_out_38, mux32_2_out_38;

  MUX32 mux32_1 (
    .I0(in_1), .I1(in_2), .I2(in_3), .I3(in_4), .I4(in_5), .I5(in_6), .I6(in_7), .I7(in_8), .I8(in_9),
    .I9(in_10), .I10(in_11), .I11(in_12), .I12(in_13), .I13(in_14), .I14(in_15), .I15(in_16), .I16(in_17),
    .I17(in_18), .I18(in_19), .I19(in_20), .I20(in_21), .I21(in_22), .I22(in_23), .I23(in_24), .I24(in_25),
    .I25(in_26), .I26(in_27), .I27(in_28), .I28(in_29), .I29(in_30), .I30(in_31), .I31(in_32), .sel4(in_66),
    .sel3(in_67), .sel2(in_68), .sel1(in_69), .sel0(in_70), .out_38(mux32_1_out_38));
  MUX32 mux32_2 (
    .I0(in_33), .I1(in_34), .I2(in_35), .I3(in_36), .I4(in_37), .I5(in_38), .I6(in_39), .I7(in_40),
    .I8(in_41), .I9(in_42), .I10(in_43), .I11(in_44), .I12(in_45), .I13(in_46), .I14(in_47), .I15(in_48),
    .I16(in_49), .I17(in_50), .I18(in_51), .I19(in_52), .I20(in_53), .I21(in_54), .I22(in_55), .I23(in_56),
    .I24(in_57), .I25(in_58), .I26(in_59), .I27(in_60), .I28(in_61), .I29(in_62), .I30(in_63), .I31(in_64),
    .sel4(in_66), .sel3(in_67), .sel2(in_68), .sel1(in_69), .sel0(in_70), .out_38(mux32_2_out_38));
  mux2 mux2_1 (.I0(mux32_1_out_38), .I1(mux32_2_out_38), .sel0(in_65), .out_4(out_71));
endmodule

// SUM
module SOMADOR (
  input  A,
  input  B,
  input  Cin,
  output S,
  output Cout
);

  wire and_1_out, and_2_out, xor_1_out;

  xor xor_1 (xor_1_out, A, B);
  xor xor_2 (S, xor_1_out, Cin);
  and and_1 (and_1_out, Cin, xor_1_out);
  and and_2 (and_2_out, A, B);
  or or_1 (Cout, and_1_out, and_2_out);
endmodule

module ALUcell (
  input  B,
  input  A,
  input  Cin,
  input  [4:0] in_4,
  output S,
  output Cout
);

  wire and_1_out, or_1_out, somador_1_s, xor_1_out;

  and and_1 (and_1_out, A, B);
  or or_1 (or_1_out, A, B);
  SOMADOR somador_1 (.A(A), .B(B), .Cin(Cin), .S(somador_1_s), .Cout(Cout));
  xor xor_1 (xor_1_out, A, B);
  mux_32_P_barrel_shift mux_32_p_barrel_shift_1 (
    .I0(and_1_out), .I1(or_1_out), .I2(somador_1_s), .I3(xor_1_out), .I4(B), .I5(B), .I6(B), .in_33(in_4),
    .out_34(S));  // open: I7, I8, I9, I10, I11, I12, I13, I14, I15, I16, I17, I18, I19, I20, I21, I22, I23, I24, I25, I26, I27, I28, I29, I30, I31
endmodule

module ALU (
  input  [31:0] in_1,
  input  [4:0] in_2
);

  wire alucell_2_cout, alucell_3_cout, alucell_4_cout, alucell_5_cout, alucell_6_cout, alucell_7_cout,
       alucell_8_cout, alucell_9_cout, alucell_10_cout, alucell_11_cout, alucell_12_cout, alucell_13_cout,
       alucell_14_cout, alucell_15_cout, alucell_16_cout, alucell_17_cout, alucell_18_cout, alucell_19_cout,
       alucell_20_cout, alucell_21_cout, alucell_22_cout, alucell_23_cout, alucell_24_cout, alucell_25_cout,
       alucell_26_cout, alucell_27_cout, alucell_28_cout, alucell_29_cout, alucell_30_cout, alucell_31_cout,
       alucell_32_cout;

  ALUcell alucell_1 (.Cin(alucell_2_cout), .in_4(in_2));  // open: S, B, A, Cout
  ALUcell alucell_2 (.Cin(alucell_3_cout), .Cout(alucell_2_cout), .in_4(in_2));  // open: S, B, A
  ALUcell alucell_3 (.Cin(alucell_4_cout), .Cout(alucell_3_cout), .in_4(in_2));  // open: S, B, A
  ALUcell alucell_4 (.Cin(alucell_5_cout), .Cout(alucell_4_cout), .in_4(in_2));  // open: S, B, A
  ALUcell alucell_5 (.Cin(alucell_6_cout), .Cout(alucell_5_cout), .in_4(in_2));  // open: S, B, A
  ALUcell alucell_6 (.Cin(alucell_7_cout), .Cout(alucell_6_cout), .in_4(in_2));  // open: S, B, A
  ALUcell alucell_7 (.Cin(alucell_8_cout), .Cout(alucell_7_cout), .in_4(in_2));  // open: S, B, A
  ALUcell alucell_8 (.Cin(alucell_9_cout), .Cout(alucell_8_cout), .in_4(in_2));  // open: S, B, A
  ALUcell alucell_9 (.Cin(alucell_10_cout), .Cout(alucell_9_cout), .in_4(in_2));  // open: S, B, A
  ALUcell alucell_10 (.Cin(alucell_11_cout), .Cout(alucell_10_cout), .in_4(in_2));  // open: S, B, A
  ALUcell alucell_11 (.Cin(alucell_12_cout), .Cout(alucell_11_cout), .in_4(in_2));  // open: S, B, A
  ALUcell alucell_12 (.Cin(alucell_13_cout), .Cout(alucell_12_cout), .in_4(in_2));  // open: S, B, A
  ALUcell alucell_13 (.Cin(alucell_14_cout), .Cout(alucell_13_cout), .in_4(in_2));  // open: S, B, A
  ALUcell alucell_14 (.Cin(alucell_15_cout), .Cout(alucell_14_cout), .in_4(in_2));  // open: S, B, A
  ALUcell alucell_15 (.Cin(alucell_16_cout), .Cout(alucell_15_cout), .in_4(in_2));  // open: S, B, A
  ALUcell alucell_16 (.Cin(alucell_17_cout), .Cout(alucell_16_cout), .in_4(in_2));  // open: S, B, A
  ALUcell alucell_17 (.Cin(alucell_18_cout), .Cout(alucell_17_cout), .in_4(in_2));  // open: S, B, A
  ALUcell alucell_18 (.Cin(alucell_19_cout), .Cout(alucell_18_cout), .in_4(in_2));  // open: S, B, A
  ALUcell alucell_19 (.Cin(alucell_20_cout), .Cout(alucell_19_cout), .in_4(in_2));  // open: S, B, A
  ALUcell alucell_20 (.Cin(alucell_21_cout), .Cout(alucell_20_cout), .in_4(in_2));  // open: S, B, A
  ALUcell alucell_21 (.Cin(alucell_22_cout), .Cout(alucell_21_cout), .in_4(in_2));  // open: S, B, A
  ALUcell alucell_22 (.Cin(alucell_23_cout), .Cout(alucell_22_cout), .in_4(in_2));  // open: S, B, A
  ALUcell alucell_23 (.Cin(alucell_24_cout), .Cout(alucell_23_cout), .in_4(in_2));  // open: S, B, A
  ALUcell alucell_24 (.S(in_1[8]), .Cin(alucell_25_cout), .Cout(alucell_24_cout), .in_4(in_2));  // open: B, A
  ALUcell alucell_25 (.S(in_1[7]), .Cin(alucell_26_cout), .Cout(alucell_25_cout), .in_4(in_2));  // open: B, A
  ALUcell alucell_26 (.S(in_1[6]), .Cin(alucell_27_cout), .Cout(alucell_26_cout), .in_4(in_2));  // open: B, A
  ALUcell alucell_27 (.S(in_1[5]), .Cin(alucell_28_cout), .Cout(alucell_27_cout), .in_4(in_2));  // open: B, A
  ALUcell alucell_28 (.S(in_1[4]), .Cin(alucell_29_cout), .Cout(alucell_28_cout), .in_4(in_2));  // open: B, A
  ALUcell alucell_29 (.S(in_1[3]), .Cin(alucell_30_cout), .Cout(alucell_29_cout), .in_4(in_2));  // open: B, A
  ALUcell alucell_30 (.S(in_1[2]), .Cin(alucell_31_cout), .Cout(alucell_30_cout), .in_4(in_2));  // open: B, A
  ALUcell alucell_31 (.S(in_1[1]), .Cin(alucell_32_cout), .Cout(alucell_31_cout), .in_4(in_2));  // open: B, A
  ALUcell alucell_32 (.S(in_1[0]), .Cin(1'b0), .Cout(alucell_32_cout), .in_4(in_2));  // open: B, A
endmodule
