// Logisim project Sistemas_Digitais(ULA).circ as structural Verilog: 29 circuits, main circuit mux2-4bit
module mux2_4bit (
  input  [3:0] in_1,
  input  [3:0] in_2,
  input  in_3,
  output [3:0] out_4
);

  wire [3:0] and_1_out, and_2_out;

  assign and_1_out = in_1 & ~{4{in_3}};  // AND_Gate and_1, 4 bits wide
  assign and_2_out = in_2 & {4{in_3}};  // AND_Gate and_2, 4 bits wide
  assign out_4 = and_1_out | and_2_out;  // OR_Gate or_1, 4 bits wide
endmodule

module mux8_ula (
  input  in_1,
  input  in_2,
  input  in_3,
  input  in_4,
  input  in_5,
  input  in_6,
  input  in_7,
  input  in_8,
  input  [2:0] in_9,
  output out_10
);

  wire mux4_1_out_7, mux4_2_out_7;

  mux4 mux4_1 (
    .in_1(in_1), .in_2(in_2), .in_3(in_3), .in_4(in_4), .in_5(in_9[1]), .in_6(in_9[0]), .out_7(mux4_1_out_7));
  mux4 mux4_2 (
    .in_1(in_5), .in_2(in_6), .in_3(in_7), .in_4(in_8), .in_5(in_9[1]), .in_6(in_9[0]), .out_7(mux4_2_out_7));
  mux4 mux4_3 (
    .in_1(mux4_1_out_7), .in_4(mux4_2_out_7), .in_5(in_9[2]), .in_6(in_9[2]), .out_7(out_10));  // open: in_2, in_3
endmodule

module mux32_ula (
  input  in_1,
  input  in_2,
  input  in_3,
  input  in_4,
  input  in_5,
  input  in_6,
  input  in_7,
  input  in_8,
  input  in_9,
  input  in_10,
  input  in_11,
  input  in_12,
  input  in_13,
  input  in_14,
  input  in_15,
  input  in_16,
  input  in_17,
  input  in_18,
  input  in_19,
  input  in_20,
  input  in_21,
  input  in_22,
  input  in_23,
  input  in_24,
  input  in_25,
  input  in_26,
  input  in_27,
  input  in_28,
  input  in_29,
  input  in_30,
  input  in_31,
  input  in_32,
  input  [4:0] in_33,
  output out_34
);

  wire mux16_1_out_21, mux16_2_out_21;

  mux16 mux16_1 (
    .in_1(in_1), .in_2(in_2), .in_3(in_3), .in_4(in_4), .in_5(in_5), .in_6(in_6), .in_7(in_7), .in_8(in_8),
    .in_9(in_9), .in_10(in_10), .in_11(in_11), .in_12(in_12), .in_13(in_13), .in_14(in_14), .in_15(in_15),
    .in_16(in_16), .in_17(in_33[3]), .in_18(in_33[2]), .in_19(in_33[1]), .in_20(in_33[0]),
    .out_21(mux16_1_out_21));
  mux16 mux16_2 (
    .in_1(in_17), .in_2(in_18), .in_3(in_19), .in_4(in_20), .in_5(in_21), .in_6(in_22), .in_7(in_23),
    .in_8(in_24), .in_9(in_25), .in_10(in_26), .in_11(in_27), .in_12(in_28), .in_13(in_29), .in_14(in_30),
    .in_15(in_31), .in_16(in_32), .in_17(in_33[3]), .in_18(in_33[2]), .in_19(in_33[1]), .in_20(in_33[0]),
    .out_21(mux16_2_out_21));
  mux16 mux16_3 (
    .in_1(mux16_1_out_21), .in_16(mux16_2_out_21), .in_17(in_33[4]), .in_18(in_33[4]), .in_19(in_33[4]),
    .in_20(in_33[4]), .out_21(out_34));  // open: in_2, in_3, in_4, in_5, in_6, in_7, in_8, in_9, in_10, in_11, in_12, in_13, in_14, in_15
endmodule

module shiftleftlogical1bit (
  input  [3:0] in_1,
  input  in_2,
  output [3:0] out_3
);

  mux2_4bit mux2_4bit_1 (.in_1(in_1), .in_2({in_1[2:0], 1'b0}), .in_3(in_2), .out_4(out_3));
endmodule

module slldetect (
  input  [2:0] in_1,
  output out_2
);

  and and_1 (out_2, ~in_1[0], ~in_1[1], in_1[2]);  // AND_Gate
endmodule

module shiftrightlogical (
  input  [3:0] in_1,
  input  in_2,
  output [3:0] out_3
);

  mux2_4bit mux2_4bit_1 (.in_1(in_1), .in_2({1'b0, in_1[3:1]}), .in_3(in_2), .out_4(out_3));
endmodule

module shiftrightarhitimetical (
  input  [3:0] in_1,
  input  in_2,
  output [3:0] out_3
);

  mux2_4bit mux2_4bit_1 (.in_1(in_1), .in_2({{2{in_1[3]}}, in_1[2:1]}), .in_3(in_2), .out_4(out_3));
endmodule

module ulacelltester (
  input  B,
  input  A,
  input  Vem_1,
  input  [2:0] Up_code,
  output \Saída ,
  output Vai_1
);

  wire and_1_out, or_1_out, \somador_1_saída , xor_1_out;

  somador somador_1 (.out_4(Vai_1), .B(B), .A(A), .\Saída (\somador_1_saída ), .Vem_1(Vem_1));
  and and_1 (and_1_out, A, B);
  or or_1 (or_1_out, A, B);
  xor xor_1 (xor_1_out, A, B);
  mux8_ula mux8_ula_1 (
    .in_1(and_1_out), .in_2(or_1_out), .in_3(\somador_1_saída ), .in_4(xor_1_out), .in_5(B), .in_6(B),
    .in_7(B), .in_9(Up_code), .out_10(\Saída ));  // open: in_8
endmodule

module ulatester (
  input  [3:0] in_1,
  input  [3:0] in_2,
  input  in_3,
  input  in_4,
  input  [2:0] in_5,
  output [3:0] out_6
);

  wire slldetect_1_out_2, ulacelltester_2_vai_1, ulacelltester_3_vai_1, ulacelltester_4_vai_1;
  wire [3:0] shiftleftlogical1bit_1_out_3, shiftrightarhitimetical_1_out_3, shiftrightlogical_1_out_3;

  shiftleftlogical1bit shiftleftlogical1bit_1 (
    .in_1(in_2), .in_2(slldetect_1_out_2), .out_3(shiftleftlogical1bit_1_out_3));
  slldetect slldetect_1 (.in_1(in_5), .out_2(slldetect_1_out_2));
  shiftrightlogical shiftrightlogical_1 (
    .in_1(shiftleftlogical1bit_1_out_3), .in_2(in_3), .out_3(shiftrightlogical_1_out_3));
  shiftrightarhitimetical shiftrightarhitimetical_1 (
    .in_1(shiftrightlogical_1_out_3), .in_2(in_4), .out_3(shiftrightarhitimetical_1_out_3));
  ulacelltester ulacelltester_1 (
    .B(shiftrightarhitimetical_1_out_3[3]), .A(in_1[3]), .Up_code(in_5), .\Saída (out_6[3]),
    .Vem_1(ulacelltester_2_vai_1));  // open: Vai_1
  ulacelltester ulacelltester_2 (
    .Vai_1(ulacelltester_2_vai_1), .B(shiftrightarhitimetical_1_out_3[2]), .A(in_1[2]), .Up_code(in_5),
    .\Saída (out_6[2]), .Vem_1(ulacelltester_3_vai_1));
  ulacelltester ulacelltester_3 (
    .Vai_1(ulacelltester_3_vai_1), .B(shiftrightarhitimetical_1_out_3[1]), .A(in_1[1]), .Up_code(in_5),
    .\Saída (out_6[1]), .Vem_1(ulacelltester_4_vai_1));
  ulacelltester ulacelltester_4 (
    .Vai_1(ulacelltester_4_vai_1), .B(shiftrightarhitimetical_1_out_3[0]), .A(in_1[0]), .Up_code(in_5),
    .\Saída (out_6[0]), .Vem_1(1'b0));
endmodule

module mux2 (
  input  in_1,
  input  in_2,
  input  in_3,
  output out_4
);

  wire and_1_out, and_2_out;

  and and_1 (and_1_out, in_1, ~in_3);  // AND_Gate
  and and_2 (and_2_out, in_2, in_3);
  or or_1 (out_4, and_1_out, and_2_out);
endmodule

module mux4 (
  input  in_1,
  input  in_2,
  input  in_3,
  input  in_4,
  input  in_5,
  input  in_6,
  output out_7
);

  wire mux2_1_out_4, mux2_2_out_4;

  mux2 mux2_1 (.in_1(in_1), .in_2(in_2), .in_3(in_6), .out_4(mux2_1_out_4));
  mux2 mux2_2 (.in_1(in_3), .in_2(in_4), .in_3(in_6), .out_4(mux2_2_out_4));
  mux2 mux2_3 (.in_1(mux2_1_out_4), .in_2(mux2_2_out_4), .in_3(in_5), .out_4(out_7));
endmodule

module mux8 (
  input  in_1,
  input  in_2,
  input  in_3,
  input  in_4,
  input  in_5,
  input  in_6,
  input  in_7,
  input  in_8,
  input  in_9,
  input  in_10,
  input  in_11,
  output out_12
);

  wire mux4_1_out_7, mux4_2_out_7;

  mux4 mux4_1 (.in_1(in_1), .in_2(in_2), .in_3(in_3), .in_4(in_4), .in_5(in_10), .in_6(in_11), .out_7(mux4_1_out_7));
  mux4 mux4_2 (.in_1(in_5), .in_2(in_6), .in_3(in_7), .in_4(in_8), .in_5(in_10), .in_6(in_11), .out_7(mux4_2_out_7));
  mux4 mux4_3 (.in_1(mux4_1_out_7), .in_4(mux4_2_out_7), .in_5(in_9), .in_6(in_9), .out_7(out_12));  // open: in_2, in_3
endmodule

module mux16 (
  input  in_1,
  input  in_2,
  input  in_3,
  input  in_4,
  input  in_5,
  input  in_6,
  input  in_7,
  input  in_8,
  input  in_9,
  input  in_10,
  input  in_11,
  input  in_12,
  input  in_13,
  input  in_14,
  input  in_15,
  input  in_16,
  input  in_17,
  input  in_18,
  input  in_19,
  input  in_20,
  output out_21
);

  wire mux8_1_out_12, mux8_2_out_12;

  mux8 mux8_1 (
    .in_1(in_1), .in_2(in_2), .in_3(in_3), .in_4(in_4), .in_5(in_5), .in_6(in_6), .in_7(in_7), .in_8(in_8),
    .in_9(in_18), .in_10(in_19), .in_11(in_20), .out_12(mux8_1_out_12));
  mux8 mux8_2 (
    .in_1(in_9), .in_2(in_10), .in_3(in_11), .in_4(in_12), .in_5(in_13), .in_6(in_14), .in_7(in_15),
    .in_8(in_16), .in_9(in_18), .in_10(in_19), .in_11(in_20), .out_12(mux8_2_out_12));
  mux8 mux8_3 (
    .in_1(mux8_1_out_12), .in_8(mux8_2_out_12), .in_9(in_17), .in_10(in_17), .in_11(in_17), .out_12(out_21));  // open: in_2, in_3, in_4, in_5, in_6, in_7
endmodule

module mux32 (
  input  in_1,
  input  in_2,
  input  in_3,
  input  in_4,
  input  in_5,
  input  in_6,
  input  in_7,
  input  in_8,
  input  in_9,
  input  in_10,
  input  in_11,
  input  in_12,
  input  in_13,
  input  in_14,
  input  in_15,
  input  in_16,
  input  in_17,
  input  in_18,
  input  in_19,
  input  in_20,
  input  in_21,
  input  in_22,
  input  in_23,
  input  in_24,
  input  in_25,
  input  in_26,
  input  in_27,
  input  in_28,
  input  in_29,
  input  in_30,
  input  in_31,
  input  in_32,
  input  in_33,
  input  in_34,
  input  in_35,
  input  in_36,
  input  in_37,
  output out_38
);

  wire mux16_1_out_21, mux16_2_out_21;

  mux16 mux16_1 (
    .in_1(in_1), .in_2(in_2), .in_3(in_3), .in_4(in_4), .in_5(in_5), .in_6(in_6), .in_7(in_7), .in_8(in_8),
    .in_9(in_9), .in_10(in_10), .in_11(in_11), .in_12(in_12), .in_13(in_13), .in_14(in_14), .in_15(in_15),
    .in_16(in_16), .in_17(in_34), .in_18(in_35), .in_19(in_36), .in_20(in_37), .out_21(mux16_1_out_21));
  mux16 mux16_2 (
    .in_1(in_17), .in_2(in_18), .in_3(in_19), .in_4(in_20), .in_5(in_21), .in_6(in_22), .in_7(in_23),
    .in_8(in_24), .in_9(in_25), .in_10(in_26), .in_11(in_27), .in_12(in_28), .in_13(in_29), .in_14(in_30),
    .in_15(in_31), .in_16(in_32), .in_17(in_34), .in_18(in_35), .in_19(in_36), .in_20(in_37),
    .out_21(mux16_2_out_21));
  mux16 mux16_3 (
    .in_1(mux16_1_out_21), .in_16(mux16_2_out_21), .in_17(in_33), .in_18(in_33), .in_19(in_33),
    .in_20(in_33), .out_21(out_38));  // open: in_2, in_3, in_4, in_5, in_6, in_7, in_8, in_9, in_10, in_11, in_12, in_13, in_14, in_15
endmodule

module mux64 (
);

  mux32 mux32_1 ();  // open: in_1, in_2, in_3, in_4, in_5, in_6, in_7, in_8, in_9, in_10, in_11, in_12, in_13, in_14, in_15, in_16, in_17, in_18, in_19, in_20, in_21, in_22, in_23, in_24, in_25, in_26, in_27, in_28, in_29, in_30, in_31, in_32, in_33, in_34, in_35, in_36, in_37, out_38
endmodule

module somador (
  input  B,
  input  A,
  input  Vem_1,
  output out_4,
  output \Saída 
);

  wire and_1_out, and_2_out, xor_1_out;

  and and_1 (and_1_out, B, A);
  or or_1 (out_4, and_1_out, and_2_out);
  xor xor_1 (xor_1_out, B, A);
  and and_2 (and_2_out, xor_1_out, Vem_1);
  xor xor_2 (\Saída , xor_1_out, Vem_1);
endmodule

module mux2_32bit (
  input  [31:0] in_1,
  input  [31:0] in_2,
  input  in_3,
  output [31:0] out_4
);

  wire [31:0] and_1_out, and_2_out;

  assign and_1_out = in_1 & ~{32{in_3}};  // AND_Gate and_1, 32 bits wide
  assign and_2_out = in_2 & {32{in_3}};  // AND_Gate and_2, 32 bits wide
  assign out_4 = and_1_out | and_2_out;  // OR_Gate or_1, 32 bits wide
endmodule

module SLL (
  input  [31:0] in_1,
  input  in_2,
  output [31:0] out_3
);

  mux2_32bit mux2_32bit_1 (.in_1(in_1), .in_2({in_1[30:0], 1'b0}), .in_3(in_2), .out_4(out_3));
endmodule

module SLLD (
  input  [4:0] in_1,
  output out_2
);

  and and_1 (out_2, ~in_1[0], ~in_1[1], in_1[2], ~in_1[3], ~in_1[4]);  // AND_Gate
endmodule

module SLR (
  input  [31:0] in_1,
  input  in_2,
  output [31:0] out_3
);

  mux2_32bit mux2_32bit_1 (.in_1(in_1), .in_2({1'b0, in_1[31:1]}), .in_3(in_2), .out_4(out_3));
endmodule

module SLRD (
  input  [4:0] in_1,
  output out_2
);

  and and_1 (out_2, in_1[0], ~in_1[1], in_1[2], ~in_1[3], ~in_1[4]);  // AND_Gate
endmodule

module SAR (
  input  [31:0] in_1,
  input  in_2,
  output [31:0] out_3
);

  mux2_32bit mux2_32bit_1 (.in_1(in_1), .in_2({{2{in_1[31]}}, in_1[30:1]}), .in_3(in_2), .out_4(out_3));
endmodule

module SARD (
  input  [4:0] in_1,
  output out_2
);

  and and_1 (out_2, ~in_1[0], in_1[1], in_1[2], ~in_1[3], ~in_1[4]);  // AND_Gate
endmodule

module ULACELL (
  input  B,
  input  A,
  input  in_3,
  input  [4:0] in_4,
  output out_5,
  output out_6
);

  wire and_1_out, nand_1_out, or_1_out, \somador_1_saída , xor_1_out;

  somador somador_1 (.out_4(out_6), .B(B), .A(A), .\Saída (\somador_1_saída ), .Vem_1(in_3));
  and and_1 (and_1_out, A, B);
  or or_1 (or_1_out, A, B);
  xor xor_1 (xor_1_out, A, B);
  nand nand_1 (nand_1_out, ~A, B);  // NAND_Gate
  mux32_ula mux32_ula_1 (
    .in_1(and_1_out), .in_2(or_1_out), .in_3(\somador_1_saída ), .in_4(xor_1_out), .in_5(B), .in_6(B),
    .in_7(B), .in_32(nand_1_out), .in_33(in_4), .out_34(out_5));  // open: in_8, in_9, in_10, in_11, in_12, in_13, in_14, in_15, in_16, in_17, in_18, in_19, in_20, in_21, in_22, in_23, in_24, in_25, in_26, in_27, in_28, in_29, in_30, in_31
endmodule

module ULA (
  input  [31:0] A,
  input  [31:0] B,
  input  [4:0] OPCODE,
  output out_4,
  output [31:0] \Saída 
);

  wire or_1_out, sard_1_out_2, slld_1_out_2, slrd_1_out_2, ulacell_2_out_6, ulacell_3_out_6, ulacell_4_out_6,
       ulacell_5_out_6, ulacell_6_out_6, ulacell_7_out_6, ulacell_8_out_6, ulacell_9_out_6, ulacell_10_out_6,
       ulacell_11_out_6, ulacell_12_out_6, ulacell_13_out_6, ulacell_14_out_6, ulacell_15_out_6,
       ulacell_16_out_6, ulacell_17_out_6, ulacell_18_out_6, ulacell_19_out_6, ulacell_20_out_6,
       ulacell_21_out_6, ulacell_22_out_6, ulacell_23_out_6, ulacell_24_out_6, ulacell_25_out_6,
       ulacell_26_out_6, ulacell_27_out_6, ulacell_28_out_6, ulacell_29_out_6, ulacell_30_out_6,
       ulacell_31_out_6, ulacell_32_out_6;
  wire [31:0] sar_1_out_3, sll_1_out_3, slr_1_out_3;

  SLLD slld_1 (.in_1(OPCODE), .out_2(slld_1_out_2));
  SLL sll_1 (.in_1(B), .in_2(slld_1_out_2), .out_3(sll_1_out_3));
  SLR slr_1 (.in_1(sll_1_out_3), .in_2(slrd_1_out_2), .out_3(slr_1_out_3));
  SLRD slrd_1 (.in_1(OPCODE), .out_2(slrd_1_out_2));
  SAR sar_1 (.in_1(slr_1_out_3), .in_2(sard_1_out_2), .out_3(sar_1_out_3));
  SARD sard_1 (.in_1(OPCODE), .out_2(sard_1_out_2));
  ULACELL ulacell_1 (
    .B(sar_1_out_3[31]), .A(A[31]), .in_4(OPCODE), .out_5(\Saída [31]), .in_3(ulacell_2_out_6));  // open: out_6
  ULACELL ulacell_2 (
    .out_6(ulacell_2_out_6), .B(sar_1_out_3[30]), .A(A[30]), .in_4(OPCODE), .out_5(\Saída [30]),
    .in_3(ulacell_3_out_6));
  ULACELL ulacell_3 (
    .out_6(ulacell_3_out_6), .B(sar_1_out_3[29]), .A(A[29]), .in_4(OPCODE), .out_5(\Saída [29]),
    .in_3(ulacell_4_out_6));
  ULACELL ulacell_4 (
    .out_6(ulacell_4_out_6), .B(sar_1_out_3[28]), .A(A[28]), .in_4(OPCODE), .out_5(\Saída [28]),
    .in_3(ulacell_5_out_6));
  ULACELL ulacell_5 (
    .out_6(ulacell_5_out_6), .B(sar_1_out_3[27]), .A(A[27]), .in_4(OPCODE), .out_5(\Saída [27]),
    .in_3(ulacell_6_out_6));
  ULACELL ulacell_6 (
    .out_6(ulacell_6_out_6), .B(sar_1_out_3[26]), .A(A[26]), .in_4(OPCODE), .out_5(\Saída [26]),
    .in_3(ulacell_7_out_6));
  ULACELL ulacell_7 (
    .out_6(ulacell_7_out_6), .B(sar_1_out_3[25]), .A(A[25]), .in_4(OPCODE), .out_5(\Saída [25]),
    .in_3(ulacell_8_out_6));
  ULACELL ulacell_8 (
    .out_6(ulacell_8_out_6), .B(sar_1_out_3[24]), .A(A[24]), .in_4(OPCODE), .out_5(\Saída [24]),
    .in_3(ulacell_9_out_6));
  ULACELL ulacell_9 (
    .out_6(ulacell_9_out_6), .B(sar_1_out_3[23]), .A(A[23]), .in_4(OPCODE), .out_5(\Saída [23]),
    .in_3(ulacell_10_out_6));
  ULACELL ulacell_10 (
    .out_6(ulacell_10_out_6), .B(sar_1_out_3[22]), .A(A[22]), .in_4(OPCODE), .out_5(\Saída [22]),
    .in_3(ulacell_11_out_6));
  ULACELL ulacell_11 (
    .out_6(ulacell_11_out_6), .B(sar_1_out_3[21]), .A(A[21]), .in_4(OPCODE), .out_5(\Saída [21]),
    .in_3(ulacell_12_out_6));
  ULACELL ulacell_12 (
    .out_6(ulacell_12_out_6), .B(sar_1_out_3[20]), .A(A[20]), .in_4(OPCODE), .out_5(\Saída [20]),
    .in_3(ulacell_13_out_6));
  ULACELL ulacell_13 (
    .out_6(ulacell_13_out_6), .B(sar_1_out_3[19]), .A(A[19]), .in_4(OPCODE), .out_5(\Saída [19]),
    .in_3(ulacell_14_out_6));
  ULACELL ulacell_14 (
    .out_6(ulacell_14_out_6), .B(sar_1_out_3[18]), .A(A[18]), .in_4(OPCODE), .out_5(\Saída [18]),
    .in_3(ulacell_15_out_6));
  ULACELL ulacell_15 (
    .out_6(ulacell_15_out_6), .B(sar_1_out_3[17]), .A(A[17]), .in_4(OPCODE), .out_5(\Saída [17]),
    .in_3(ulacell_16_out_6));
  ULACELL ulacell_16 (
    .out_6(ulacell_16_out_6), .B(sar_1_out_3[16]), .A(A[16]), .in_4(OPCODE), .out_5(\Saída [16]),
    .in_3(ulacell_17_out_6));
  ULACELL ulacell_17 (
    .out_6(ulacell_17_out_6), .B(sar_1_out_3[15]), .A(A[15]), .in_4(OPCODE), .out_5(\Saída [15]),
    .in_3(ulacell_18_out_6));
  ULACELL ulacell_18 (
    .out_6(ulacell_18_out_6), .B(sar_1_out_3[14]), .A(A[14]), .in_4(OPCODE), .out_5(\Saída [14]),
    .in_3(ulacell_19_out_6));
  ULACELL ulacell_19 (
    .out_6(ulacell_19_out_6), .B(sar_1_out_3[13]), .A(A[13]), .in_4(OPCODE), .out_5(\Saída [13]),
    .in_3(ulacell_20_out_6));
  ULACELL ulacell_20 (
    .out_6(ulacell_20_out_6), .B(sar_1_out_3[12]), .A(A[12]), .in_4(OPCODE), .out_5(\Saída [12]),
    .in_3(ulacell_21_out_6));
  ULACELL ulacell_21 (
    .out_6(ulacell_21_out_6), .B(sar_1_out_3[11]), .A(A[11]), .in_4(OPCODE), .out_5(\Saída [11]),
    .in_3(ulacell_22_out_6));
  ULACELL ulacell_22 (
    .out_6(ulacell_22_out_6), .B(sar_1_out_3[10]), .A(A[10]), .in_4(OPCODE), .out_5(\Saída [10]),
    .in_3(ulacell_23_out_6));
  ULACELL ulacell_23 (
    .out_6(ulacell_23_out_6), .B(sar_1_out_3[9]), .A(A[9]), .in_4(OPCODE), .out_5(\Saída [9]),
    .in_3(ulacell_24_out_6));
  ULACELL ulacell_24 (
    .out_6(ulacell_24_out_6), .B(sar_1_out_3[8]), .A(A[8]), .in_4(OPCODE), .out_5(\Saída [8]),
    .in_3(ulacell_25_out_6));
  ULACELL ulacell_25 (
    .out_6(ulacell_25_out_6), .B(sar_1_out_3[7]), .A(A[7]), .in_4(OPCODE), .out_5(\Saída [7]),
    .in_3(ulacell_26_out_6));
  ULACELL ulacell_26 (
    .out_6(ulacell_26_out_6), .B(sar_1_out_3[6]), .A(A[6]), .in_4(OPCODE), .out_5(\Saída [6]),
    .in_3(ulacell_27_out_6));
  ULACELL ulacell_27 (
    .out_6(ulacell_27_out_6), .B(sar_1_out_3[5]), .A(A[5]), .in_4(OPCODE), .out_5(\Saída [5]),
    .in_3(ulacell_28_out_6));
  ULACELL ulacell_28 (
    .out_6(ulacell_28_out_6), .B(sar_1_out_3[4]), .A(A[4]), .in_4(OPCODE), .out_5(\Saída [4]),
    .in_3(ulacell_29_out_6));
  ULACELL ulacell_29 (
    .out_6(ulacell_29_out_6), .B(sar_1_out_3[3]), .A(A[3]), .in_4(OPCODE), .out_5(\Saída [3]),
    .in_3(ulacell_30_out_6));
  ULACELL ulacell_30 (
    .out_6(ulacell_30_out_6), .B(sar_1_out_3[2]), .A(A[2]), .in_4(OPCODE), .out_5(\Saída [2]),
    .in_3(ulacell_31_out_6));
  ULACELL ulacell_31 (
    .out_6(ulacell_31_out_6), .B(sar_1_out_3[1]), .A(A[1]), .in_4(OPCODE), .out_5(\Saída [1]),
    .in_3(ulacell_32_out_6));
  ULACELL ulacell_32 (
    .out_6(ulacell_32_out_6), .B(sar_1_out_3[0]), .A(A[0]), .in_4(OPCODE), .out_5(\Saída [0]), .in_3(1'b0));
  or or_1 (or_1_out, \Saída [0], \Saída [1], \Saída [2], \Saída [3], \Saída [4], \Saída [5], \Saída [6], \Saída [7], \Saída [8], \Saída [9], \Saída [10], \Saída [11], \Saída [12], \Saída [13], \Saída [14], \Saída [15], \Saída [17], \Saída [18], \Saída [19], \Saída [20], \Saída [21], \Saída [22], \Saída [23], \Saída [24], \Saída [25], \Saída [26], \Saída [27], \Saída [28], \Saída [29], \Saída [30], \Saída [31], \Saída [16]);
  not not_1 (out_4, or_1_out);
endmodule

module caixaULA (
);

  ULA ula_1 ();  // open: A, B, Saída, OPCODE, out_4
endmodule

module detectright_logical (
  input  [2:0] in_1,
  output out_2
);

  and and_1 (out_2, in_1[0], ~in_1[1], in_1[2]);  // AND_Gate
endmodule

module selectrightaritimetico (
  input  [2:0] in_1,
  output out_2
);

  and and_1 (out_2, in_1[0], in_1[1], ~in_1[2]);  // AND_Gate
endmodule

module slrdetector (
  input  [2:0] in_1
);

  // AND_Gate and_1: pin names not known; wires that end beside it: in_1[0], in_1[1]
endmodule
