// Logisim project ULA.circ as structural Verilog
module mux2 (
  input  A,
  input  B,
  input  Sel,
  output S
);

  wire and_1_out, and_2_out;

  and and_1 (and_1_out, A, ~Sel);  // AND_Gate
  and and_2 (and_2_out, B, Sel);
  or or_1 (S, and_1_out, and_2_out);
endmodule

module mux4 (
  input  A,
  input  B,
  input  C,
  input  D,
  input  Sel1,
  input  Sel0,
  output out_7
);

  wire mux2_1_s, mux2_2_s;

  mux2 mux2_1 (.A(A), .B(B), .Sel(Sel0), .S(mux2_1_s));
  mux2 mux2_2 (.A(C), .B(D), .Sel(Sel0), .S(mux2_2_s));
  mux2 mux2_3 (.A(mux2_1_s), .B(mux2_2_s), .Sel(Sel1), .S(out_7));
endmodule

module mux4b (
  input  in_1,
  input  in_2,
  input  in_3,
  input  in_4,
  input  [1:0] in_5,
  output out_6
);

  wire and_1_out, and_2_out, and_3_out, and_4_out;

  and and_1 (and_1_out, in_1, ~in_5[1], ~in_5[0]);  // AND_Gate
  and and_2 (and_2_out, in_2, ~in_5[1], in_5[0]);  // AND_Gate
  and and_3 (and_3_out, in_3, in_5[1], ~in_5[0]);  // AND_Gate
  and and_4 (and_4_out, in_4, in_5[1], in_5[0]);
  or or_1 (out_6, and_1_out, and_2_out, and_3_out, and_4_out);
endmodule

module somador (
  input  Cin,
  input  A,
  input  B,
  output S,
  output Cout
);

  wire and_1_out, and_2_out, and_3_out, xor_1_out;

  xor xor_1 (xor_1_out, A, B);
  and and_1 (and_1_out, Cin, A);
  and and_2 (and_2_out, Cin, B);
  and and_3 (and_3_out, B, A);
  xor xor_2 (S, xor_1_out, Cin);
  or or_1 (Cout, and_1_out, and_2_out, and_3_out);
endmodule

module ULACell (
  input  b,
  input  a,
  input  Vem1,
  input  [2:0] OpCode,
  output saida,
  output Vai1
);

  wire and_1_out, or_1_out, somador_1_s, xor_1_out;

  and and_1 (and_1_out, a, b);
  or or_1 (or_1_out, a, b);
  somador somador_1 (.A(a), .B(b), .Cin(Vem1), .Cout(Vai1), .S(somador_1_s));
  xor xor_1 (xor_1_out, a, b);
  Multiplexer #(.select(3), .enable("false")) multiplexer_1 (
    .in0(and_1_out), .in1(or_1_out), .in2(somador_1_s), .in3(xor_1_out), .in4(b), .in5(b), .in6(b),
    .out(saida), .sel(OpCode));  // open: in7
endmodule

module ULA (
  input  [3:0] A,
  input  [3:0] B,
  input  in_3,
  input  in_4,
  input  [2:0] ULAOpCode,
  output [3:0] Result
);

  wire slldetect_1_sll, ulacell_2_vai1, ulacell_3_vai1, ulacell_4_vai1;
  wire [3:0] shiftleftlogical1bit_1_out_3, shiftrightarith1bit_1_out_3, shiftrightlogical1bit_1_out_3;

  SLLDetect slldetect_1 (.ALUOpCode(ULAOpCode), .sll(slldetect_1_sll));
  ShiftRightLogical1bit shiftrightlogical1bit_1 (
    .in_1(shiftleftlogical1bit_1_out_3), .Shift(in_3), .out_3(shiftrightlogical1bit_1_out_3));
  ShiftLeftLogical1bit shiftleftlogical1bit_1 (.in_1(B), .Shift(slldetect_1_sll), .out_3(shiftleftlogical1bit_1_out_3));
  ShiftRightArith1bit shiftrightarith1bit_1 (
    .in_1(shiftrightlogical1bit_1_out_3), .Shift(in_4), .out_3(shiftrightarith1bit_1_out_3));
  ULACell ulacell_1 (
    .b(shiftrightarith1bit_1_out_3[3]), .a(A[3]), .OpCode(ULAOpCode), .saida(Result[3]), .Vem1(ulacell_2_vai1));  // open: Vai1
  ULACell ulacell_2 (
    .Vai1(ulacell_2_vai1), .b(shiftrightarith1bit_1_out_3[2]), .a(A[2]), .OpCode(ULAOpCode),
    .saida(Result[2]), .Vem1(ulacell_3_vai1));
  ULACell ulacell_3 (
    .Vai1(ulacell_3_vai1), .b(shiftrightarith1bit_1_out_3[1]), .a(A[1]), .OpCode(ULAOpCode),
    .saida(Result[1]), .Vem1(ulacell_4_vai1));
  ULACell ulacell_4 (
    .Vai1(ulacell_4_vai1), .b(shiftrightarith1bit_1_out_3[0]), .a(A[0]), .OpCode(ULAOpCode),
    .saida(Result[0]), .Vem1(1'b0));

  // Notes on the sheet:
  //   000 = and
  //   001 = or
  //   010 = soma
  //   011 = xor
  //   100 = sll
endmodule

module ShiftLeftLogical1bit (
  input  [3:0] in_1,
  input  Shift,
  output [3:0] out_3
);

  Multiplexer #(.width(4), .enable("false")) multiplexer_1 (
    .in0(in_1), .in1({in_1[2:0], 1'b0}), .out(out_3), .sel(Shift));
endmodule

module ShiftRightLogical1bit (
  input  [3:0] in_1,
  input  Shift,
  output [3:0] out_3
);

  Multiplexer #(.width(4), .enable("false")) multiplexer_1 (
    .in0(in_1), .in1({1'b0, in_1[3:1]}), .out(out_3), .sel(Shift));
endmodule

module ShiftRightArith1bit (
  input  [3:0] in_1,
  input  Shift,
  output [3:0] out_3
);

  Multiplexer #(.width(4), .enable("false")) multiplexer_1 (
    .in0(in_1), .in1({{2{in_1[3]}}, in_1[2:1]}), .out(out_3), .sel(Shift));
endmodule

module SLLDetect (
  input  [2:0] ALUOpCode,
  output sll
);

  and and_1 (sll, ~ALUOpCode[0], ~ALUOpCode[1], ALUOpCode[2]);  // AND_Gate
endmodule
