// Logisim project circuitos.circ as structural Verilog: 3 circuits, main circuit main
module main (
  input  in_1,
  input  in_2,
  output out_3,
  output out_4
);

  and and_1 (out_3, in_1, in_2);
  or or_1 (out_4, in_1, in_2);
endmodule

module mux2 (
  input  A,
  input  B,
  input  in_3,
  output out_4
);

  wire and_1_out, and_2_out;

  and and_1 (and_1_out, A, ~in_3);  // AND_Gate
  and and_2 (and_2_out, B, in_3);
  or or_1 (out_4, and_1_out, and_2_out);
endmodule

module mux4 (
  input  A,
  input  B,
  input  C,
  input  D,
  input  sel1,
  input  sel0,
  output out_7
);

  wire mux2_1_out_4, mux2_2_out_4;

  mux2 mux2_1 (.A(A), .B(B), .in_3(sel0), .out_4(mux2_1_out_4));
  mux2 mux2_2 (.A(C), .B(D), .in_3(sel0), .out_4(mux2_2_out_4));
  mux2 mux2_3 (.A(mux2_1_out_4), .B(mux2_2_out_4), .in_3(sel1), .out_4(out_7));
endmodule
