// Logisim project aula02-introducao-ULA.circ as structural Verilog: 4 circuits, main circuit main
module main (
  input  Cin,
  input  a,
  input  b,
  output S,
  output Cout
);

  wire and_1_out, and_2_out, xor_1_out;

  xor xor_1 (xor_1_out, a, b);
  xor xor_2 (S, xor_1_out, Cin);
  and and_1 (and_1_out, Cin, xor_1_out);
  and and_2 (and_2_out, a, b);
  or or_1 (Cout, and_1_out, and_2_out);
endmodule

module ULAcell (
  input  a,
  input  b,
  input  in_3,
  input  sel1,
  input  sel0,
  output out_6
);

  wire and_1_out, main_1_s, or_1_out, xor_1_out;

  and and_1 (and_1_out, a, b);
  or or_1 (or_1_out, a, b);
  main main_1 (.a(a), .b(b), .Cin(in_3), .Cout(out_6), .S(main_1_s));
  xor xor_1 (xor_1_out, a, b);
  mux4 mux4_1 (.a(and_1_out), .b(or_1_out), .c(main_1_s), .d(xor_1_out), .sel1(sel1), .sel0(sel0));  // open: S
endmodule

module mux2 (
  input  a,
  input  b,
  input  sel0,
  output S
);

  wire and_1_out, and_2_out;

  and and_1 (and_1_out, a, ~sel0);  // AND_Gate
  and and_2 (and_2_out, b, sel0);
  or or_1 (S, and_1_out, and_2_out);
endmodule

module mux4 (
  input  a,
  input  b,
  input  c,
  input  d,
  input  sel1,
  input  sel0,
  output S
);

  wire mux2_1_s, mux2_2_s;

  mux2 mux2_1 (.a(a), .b(b), .sel0(sel0), .S(mux2_1_s));
  mux2 mux2_2 (.a(c), .b(d), .sel0(sel0), .S(mux2_2_s));
  mux2 mux2_3 (.a(mux2_1_s), .b(mux2_2_s), .sel0(sel1), .S(S));
endmodule
