// Logisim project projeto_geral.circ as structural Verilog
module mux2 (
  input  I0,
  input  I1,
  input  sel0,
  output out_4
);

  wire and_1_out, and_2_out;

  and and_1 (and_1_out, I0, ~sel0);  // AND_Gate
  and and_2 (and_2_out, I1, sel0);
  or or_1 (out_4, and_1_out, and_2_out);
endmodule

module mux4 (
  input  I0,
  input  I1,
  input  I2,
  input  I3,
  input  sel1,
  input  sel0,
  output out_7
);

  wire mux2_1_out_4, mux2_2_out_4;

  mux2 mux2_1 (.I0(I0), .I1(I1), .sel0(sel0), .out_4(mux2_1_out_4));
  mux2 mux2_2 (.I0(I2), .I1(I3), .sel0(sel0), .out_4(mux2_2_out_4));
  mux2 mux2_3 (.I0(mux2_1_out_4), .I1(mux2_2_out_4), .sel0(sel1), .out_4(out_7));
endmodule

module mux8 (
  input  I0,
  input  I1,
  input  I2,
  input  I3,
  input  I4,
  input  I5,
  input  I6,
  input  I7,
  input  sel2,
  input  sel1,
  input  sel0,
  output out_12
);

  wire mux4_1_out_7, mux4_2_out_7;

  mux4 mux4_1 (.I0(I0), .I1(I1), .I2(I2), .I3(I3), .sel1(sel1), .sel0(sel0), .out_7(mux4_1_out_7));
  mux4 mux4_2 (.I0(I4), .I1(I5), .I2(I6), .I3(I7), .sel1(sel1), .sel0(sel0), .out_7(mux4_2_out_7));
  mux2 mux2_1 (.I0(mux4_1_out_7), .I1(mux4_2_out_7), .sel0(sel2), .out_4(out_12));
endmodule

module mux16 (
  input  I0,
  input  I1,
  input  I2,
  input  I3,
  input  I4,
  input  I5,
  input  I6,
  input  I7,
  input  I8,
  input  I9,
  input  I10,
  input  I11,
  input  I12,
  input  I13,
  input  I14,
  input  I15,
  input  sel3,
  input  sel2,
  input  sel1,
  input  sel0,
  output out_21
);

  wire mux8_1_out_12, mux8_2_out_12;

  mux8 mux8_1 (
    .I0(I0), .I1(I1), .I2(I2), .I3(I3), .I4(I4), .I5(I5), .I6(I6), .I7(I7), .sel2(sel2), .sel1(sel1),
    .sel0(sel0), .out_12(mux8_1_out_12));
  mux8 mux8_2 (
    .I0(I8), .I1(I9), .I2(I10), .I3(I11), .I4(I12), .I5(I13), .I6(I14), .I7(I15), .sel2(sel2), .sel1(sel1),
    .sel0(sel0), .out_12(mux8_2_out_12));
  mux2 mux2_1 (.I0(mux8_1_out_12), .I1(mux8_2_out_12), .sel0(sel3), .out_4(out_21));
endmodule

module mux32 (
  input  I0,
  input  I1,
  input  I2,
  input  I3,
  input  I4,
  input  I5,
  input  I6,
  input  I7,
  input  I8,
  input  I9,
  input  I10,
  input  I11,
  input  I12,
  input  I13,
  input  I14,
  input  I15,
  input  I16,
  input  I17,
  input  I18,
  input  I19,
  input  I20,
  input  I21,
  input  I22,
  input  I23,
  input  I24,
  input  I25,
  input  I26,
  input  I27,
  input  I28,
  input  I29,
  input  I30,
  input  I31,
  input  sel4,
  input  sel3,
  input  sel2,
  input  sel1,
  input  sel0,
  output out_38
);

  wire mux16_1_out_21, mux16_2_out_21;

  mux16 mux16_1 (
    .I0(I0), .I1(I1), .I2(I2), .I3(I3), .I4(I4), .I5(I5), .I6(I6), .I7(I7), .I8(I8), .I9(I9), .I10(I10),
    .I11(I11), .I12(I12), .I13(I13), .I14(I14), .I15(I15), .sel3(sel3), .sel2(sel2), .sel1(sel1),
    .sel0(sel0), .out_21(mux16_1_out_21));
  mux16 mux16_2 (
    .I0(I16), .I1(I17), .I2(I18), .I3(I19), .I4(I20), .I5(I21), .I6(I22), .I7(I23), .I8(I24), .I9(I25),
    .I10(I26), .I11(I27), .I12(I28), .I13(I29), .I14(I30), .I15(I31), .sel3(sel3), .sel2(sel2), .sel1(sel1),
    .sel0(sel0), .out_21(mux16_2_out_21));
  mux2 mux2_1 (.I0(mux16_1_out_21), .I1(mux16_2_out_21), .sel0(sel4), .out_4(out_38));
endmodule

module mux64 (
  input  in_1,
  input  in_2,
  input  in_3,
  input  in_4,
  input  in_5,
  input  in_6,
  input  in_7,
  input  in_8,
  input  in_9,
  input  in_10,
  input  in_11,
  input  in_12,
  input  in_13,
  input  in_14,
  input  in_15,
  input  in_16,
  input  in_17,
  input  in_18,
  input  in_19,
  input  in_20,
  input  in_21,
  input  in_22,
  input  in_23,
  input  in_24,
  input  in_25,
  input  in_26,
  input  in_27,
  input  in_28,
  input  in_29,
  input  in_30,
  input  in_31,
  input  in_32,
  input  in_33,
  input  in_34,
  input  in_35,
  input  in_36,
  input  in_37,
  input  in_38,
  input  in_39,
  input  in_40,
  input  in_41,
  input  in_42,
  input  in_43,
  input  in_44,
  input  in_45,
  input  in_46,
  input  in_47,
  input  in_48,
  input  in_49,
  input  in_50,
  input  in_51,
  input  in_52,
  input  in_53,
  input  in_54,
  input  in_55,
  input  in_56,
  input  in_57,
  input  in_58,
  input  in_59,
  input  in_60,
  input  in_61,
  input  in_62,
  input  in_63,
  input  in_64,
  input  in_65,
  input  in_66,
  input  in_67,
  input  in_68,
  input  in_69,
  input  in_70,
  output out_71
);

  wire mux32_1_out_38, mux32_2_out_38;

  mux32 mux32_1 (
    .I0(in_1), .I1(in_2), .I2(in_3), .I3(in_4), .I4(in_5), .I5(in_6), .I6(in_7), .I7(in_8), .I8(in_9),
    .I9(in_10), .I10(in_11), .I11(in_12), .I12(in_13), .I13(in_14), .I14(in_15), .I15(in_16), .I16(in_17),
    .I17(in_18), .I18(in_19), .I19(in_20), .I20(in_21), .I21(in_22), .I22(in_23), .I23(in_24), .I24(in_25),
    .I25(in_26), .I26(in_27), .I27(in_28), .I28(in_29), .I29(in_30), .I30(in_31), .I31(in_32), .sel4(in_66),
    .sel3(in_67), .sel2(in_68), .sel1(in_69), .sel0(in_70), .out_38(mux32_1_out_38));
  mux32 mux32_2 (
    .I0(in_33), .I1(in_34), .I2(in_35), .I3(in_36), .I4(in_37), .I5(in_38), .I6(in_39), .I7(in_40),
    .I8(in_41), .I9(in_42), .I10(in_43), .I11(in_44), .I12(in_45), .I13(in_46), .I14(in_47), .I15(in_48),
    .I16(in_49), .I17(in_50), .I18(in_51), .I19(in_52), .I20(in_53), .I21(in_54), .I22(in_55), .I23(in_56),
    .I24(in_57), .I25(in_58), .I26(in_59), .I27(in_60), .I28(in_61), .I29(in_62), .I30(in_63), .I31(in_64),
    .sel4(in_66), .sel3(in_67), .sel2(in_68), .sel1(in_69), .sel0(in_70), .out_38(mux32_2_out_38));
  mux2 mux2_1 (.I0(mux32_1_out_38), .I1(mux32_2_out_38), .sel0(in_65), .out_4(out_71));
endmodule
